// Logisim project wiersz_p4.circ as structural Verilog: 1 circuit, main circuit main
module main (
  input  RESET,
  input  [1:0] DATA_IN,
  input  CLK,
  output [1:0] DATA_OUT,
  output RAM_CLK,
  output ZD_OUT
);

  wire and_1_out, comparator_1_eq, comparator_1_gt, comparator_1_lt, or_1_out;
  wire [1:0] logiczno_ustawiacz_norm_1_p22, logiczno_ustawiacz_norm_1_p23, logiczno_ustawiacz_norm_1_p24,
       logiczno_ustawiacz_norm_1_p25, logiczno_ustawiacz_norm_1_p26, logiczno_ustawiacz_norm_1_p27,
       logiczno_ustawiacz_norm_1_p28, logiczno_ustawiacz_norm_1_p29, logiczno_ustawiacz_norm_1_p30,
       logiczno_ustawiacz_norm_1_p31, logiczno_ustawiacz_norm_1_p32, logiczno_ustawiacz_norm_1_p33,
       logiczno_ustawiacz_norm_1_p34, logiczno_ustawiacz_norm_1_p35, logiczno_ustawiacz_norm_1_p36,
       logiczno_ustawiacz_norm_1_p37, logiczno_ustawiacz_norm_1_p38, logiczno_ustawiacz_norm_1_p39,
       logiczno_ustawiacz_norm_1_p40, logiczno_ustawiacz_norm_1_p41, main_1_data_out_0, main_1_data_out_1,
       main_1_data_out_2, main_1_data_out_3, main_1_data_out_4, main_1_data_out_5, main_1_data_out_6,
       main_1_data_out_7, main_1_data_out_8, main_1_data_out_9, main_1_data_out_10, main_1_data_out_11,
       main_1_data_out_12, main_1_data_out_13, main_1_data_out_14, main_1_data_out_15, main_1_data_out_16,
       main_1_data_out_17, main_1_data_out_18, main_1_data_out_19;
  wire [4:0] counter_2_q, undriven;
  wire [5:0] counter_1_q;

  Counter #(.width(6), .max('h1f)) counter_1 (.Q(counter_1_q), .clk(CLK), .clr(RESET));  // open: load, D, count, carry
  and and_1 (and_1_out, CLK, comparator_1_lt);
  Comparator #(.width(6), .mode("unsigned")) comparator_1 (
    .a(counter_1_q), .b(6'b010001), .gt(comparator_1_gt), .eq(comparator_1_eq), .lt(comparator_1_lt));
  or or_1 (or_1_out, comparator_1_gt, comparator_1_eq);
  Counter #(.width(5), .max('hf)) counter_2 (
    .Q(counter_2_q), .clk(RAM_CLK), .clr(RESET));  // open: load, D, count, carry
  MEGA_register_p4_main main_1 (
    .DATA_IN(DATA_IN), .CLK(and_1_out), .DATA_OUT_0(main_1_data_out_0), .DATA_OUT_1(main_1_data_out_1),
    .DATA_OUT_2(main_1_data_out_2), .DATA_OUT_3(main_1_data_out_3), .DATA_OUT_4(main_1_data_out_4),
    .DATA_OUT_5(main_1_data_out_5), .DATA_OUT_6(main_1_data_out_6), .DATA_OUT_7(main_1_data_out_7),
    .DATA_OUT_8(main_1_data_out_8), .DATA_OUT_9(main_1_data_out_9), .DATA_OUT_10(main_1_data_out_10),
    .DATA_OUT_11(main_1_data_out_11), .DATA_OUT_12(main_1_data_out_12), .DATA_OUT_13(main_1_data_out_13),
    .DATA_OUT_14(main_1_data_out_14), .DATA_OUT_15(main_1_data_out_15), .DATA_OUT_16(main_1_data_out_16),
    .DATA_OUT_17(main_1_data_out_17), .DATA_OUT_18(main_1_data_out_18), .DATA_OUT_19(main_1_data_out_19),
    .R(RESET));
  // logiczno_ustawiacz_norm logiczno_ustawiacz_norm_1: pin names not known; wires that end beside it: main_1_data_out_0, main_1_data_out_1, main_1_data_out_2, main_1_data_out_3, main_1_data_out_4, main_1_data_out_5, main_1_data_out_6, main_1_data_out_7, main_1_data_out_8, main_1_data_out_9, main_1_data_out_10, main_1_data_out_11, main_1_data_out_12, main_1_data_out_13, main_1_data_out_14, main_1_data_out_15, main_1_data_out_16, main_1_data_out_17, main_1_data_out_18, main_1_data_out_19, ZD_OUT, logiczno_ustawiacz_norm_1_p22, logiczno_ustawiacz_norm_1_p23, logiczno_ustawiacz_norm_1_p24, logiczno_ustawiacz_norm_1_p25, logiczno_ustawiacz_norm_1_p26, logiczno_ustawiacz_norm_1_p27, logiczno_ustawiacz_norm_1_p28, logiczno_ustawiacz_norm_1_p29, logiczno_ustawiacz_norm_1_p30, logiczno_ustawiacz_norm_1_p31, logiczno_ustawiacz_norm_1_p32, logiczno_ustawiacz_norm_1_p33, logiczno_ustawiacz_norm_1_p34, logiczno_ustawiacz_norm_1_p35, logiczno_ustawiacz_norm_1_p36, logiczno_ustawiacz_norm_1_p37, logiczno_ustawiacz_norm_1_p38, logiczno_ustawiacz_norm_1_p39, logiczno_ustawiacz_norm_1_p40, logiczno_ustawiacz_norm_1_p41
  and and_2 (RAM_CLK, or_1_out, CLK);
  Adder #(.width(5)) adder_1 (.a(undriven), .b(5'b00100));  // open: out, cin, cout
  Multiplexer #(.select(5), .width(2)) multiplexer_1 (
    .in0(logiczno_ustawiacz_norm_1_p22), .in1(logiczno_ustawiacz_norm_1_p23),
    .in2(logiczno_ustawiacz_norm_1_p24), .in3(logiczno_ustawiacz_norm_1_p25),
    .in4(logiczno_ustawiacz_norm_1_p26), .in5(logiczno_ustawiacz_norm_1_p27),
    .in6(logiczno_ustawiacz_norm_1_p28), .in7(logiczno_ustawiacz_norm_1_p29),
    .in8(logiczno_ustawiacz_norm_1_p30), .in9(logiczno_ustawiacz_norm_1_p31),
    .in10(logiczno_ustawiacz_norm_1_p32), .in11(logiczno_ustawiacz_norm_1_p33),
    .in12(logiczno_ustawiacz_norm_1_p34), .in13(logiczno_ustawiacz_norm_1_p35),
    .in14(logiczno_ustawiacz_norm_1_p36), .in15(logiczno_ustawiacz_norm_1_p37),
    .in16(logiczno_ustawiacz_norm_1_p38), .in17(logiczno_ustawiacz_norm_1_p39),
    .in18(logiczno_ustawiacz_norm_1_p40), .in19(logiczno_ustawiacz_norm_1_p41), .out(DATA_OUT),
    .sel(counter_2_q));  // open: in20, in21, in22, in23, in24, in25, in26, in27, in28, in29, in30, in31, en
  Demultiplexer #(.select(5)) demultiplexer_1 (
    .in(1'b1), .sel(counter_2_q));  // open: out0, out1, out2, out3, out4, out5, out6, out7, out8, out9, out10, out11, out12, out13, out14, out15, out16, out17, out18, out19, out20, out21, out22, out23, out24, out25, out26, out27, out28, out29, out30, out31, en

  // Other names for the same wires on the sheet: ZD = ZD_OUT

  // Notes on the sheet:
  //   23
endmodule
