// Logisim project ustawiacz_rotacja_prawo.circ as structural Verilog: 1 circuit, main circuit logiczno-ustawiacz_norm
module logiczno_ustawiacz_norm (
  input  [1:0] REG_0,
  input  [1:0] REG_1,
  input  [1:0] REG_2,
  input  [1:0] REG_3,
  input  [1:0] REG_0_2,
  input  [1:0] REG_1_2,
  input  [1:0] REG_2_2,
  input  [1:0] REG_3_2,
  input  [1:0] REG_0_3,
  input  [1:0] REG_1_3,
  input  [1:0] REG_2_3,
  input  [1:0] REG_3_3,
  input  [1:0] REG_0_4,
  input  [1:0] REG_1_4,
  input  [1:0] REG_2_4,
  input  [1:0] REG_3_4,
  output [1:0] OUT_0,
  output [1:0] OUT_1,
  output [1:0] OUT_2,
  output [1:0] OUT_3,
  output [1:0] OUT_0_2,
  output [1:0] OUT_1_2,
  output [1:0] OUT_2_2,
  output [1:0] OUT_3_2,
  output [1:0] OUT_0_3,
  output [1:0] OUT_1_3,
  output [1:0] OUT_2_3,
  output [1:0] OUT_3_3,
  output [1:0] OUT_0_4,
  output [1:0] OUT_1_4,
  output [1:0] OUT_2_4,
  output [1:0] OUT_3_4,
  output ZD_OUT
);

  wire czy_zderzenie_1_out, czy_zderzenie_2_out, czy_zderzenie_3_out, czy_zderzenie_4_out,
       czy_zderzenie_5_out, czy_zderzenie_6_out, czy_zderzenie_7_out, czy_zderzenie_8_out,
       czy_zderzenie_9_out, czy_zderzenie_10_out, czy_zderzenie_11_out, czy_zderzenie_12_out,
       czy_zderzenie_13_out, czy_zderzenie_14_out, czy_zderzenie_15_out, czy_zderzenie_16_out, or_1_out,
       or_2_out, or_3_out, or_4_out;
  wire [1:0] zamieniacz_1_a_2, zamieniacz_2_a_2, zamieniacz_3_a_2, zamieniacz_4_a_2, zamieniacz_5_a_2,
       zamieniacz_6_a_2, zamieniacz_7_a_2, zamieniacz_8_a_2;

  czy_zderzenie czy_zderzenie_1 (.W(REG_0), .L(REG_3), .OUT(czy_zderzenie_1_out));
  czy_zderzenie czy_zderzenie_2 (.W(REG_1), .L(REG_3_2), .OUT(czy_zderzenie_2_out));
  czy_zderzenie czy_zderzenie_3 (.W(REG_2), .L(REG_3_3), .OUT(czy_zderzenie_3_out));
  czy_zderzenie czy_zderzenie_4 (.W(REG_3), .L(REG_3_4), .OUT(czy_zderzenie_4_out));
  zamieniacz zamieniacz_1 (.A(REG_0), .B(REG_3), .A_2(zamieniacz_1_a_2), .B_2(OUT_3), .WYSTAPILO_ZDERZENIE(ZD_OUT));
  zamieniacz zamieniacz_2 (.A(REG_1), .B(REG_3_2), .A_2(zamieniacz_2_a_2), .B_2(OUT_3_2), .WYSTAPILO_ZDERZENIE(ZD_OUT));
  zamieniacz zamieniacz_3 (.A(REG_2), .B(REG_3_3), .A_2(zamieniacz_3_a_2), .B_2(OUT_3_3), .WYSTAPILO_ZDERZENIE(ZD_OUT));
  zamieniacz zamieniacz_4 (
    .A(REG_1_2), .B(REG_2_2), .A_2(zamieniacz_4_a_2), .B_2(OUT_2_2), .WYSTAPILO_ZDERZENIE(ZD_OUT));
  or or_1 (or_1_out, czy_zderzenie_1_out, czy_zderzenie_2_out, czy_zderzenie_3_out, czy_zderzenie_4_out);
  czy_zderzenie czy_zderzenie_5 (.W(REG_0_2), .L(REG_2), .OUT(czy_zderzenie_5_out));
  czy_zderzenie czy_zderzenie_6 (.W(REG_1_2), .L(REG_2_2), .OUT(czy_zderzenie_6_out));
  czy_zderzenie czy_zderzenie_7 (.W(REG_2_2), .L(REG_2_3), .OUT(czy_zderzenie_7_out));
  czy_zderzenie czy_zderzenie_8 (.W(REG_3_2), .L(REG_2_4), .OUT(czy_zderzenie_8_out));
  or or_2 (or_2_out, czy_zderzenie_5_out, czy_zderzenie_6_out, czy_zderzenie_7_out, czy_zderzenie_8_out);
  zamieniacz zamieniacz_5 (
    .A(zamieniacz_1_a_2), .B(REG_3_4), .A_2(zamieniacz_5_a_2), .B_2(OUT_3_4), .WYSTAPILO_ZDERZENIE(ZD_OUT));
  zamieniacz zamieniacz_6 (
    .A(zamieniacz_2_a_2), .B(REG_2_4), .A_2(zamieniacz_6_a_2), .B_2(OUT_2_4), .WYSTAPILO_ZDERZENIE(ZD_OUT));
  zamieniacz zamieniacz_7 (
    .A(zamieniacz_3_a_2), .B(REG_1_4), .A_2(zamieniacz_7_a_2), .B_2(OUT_1_4), .WYSTAPILO_ZDERZENIE(ZD_OUT));
  zamieniacz zamieniacz_8 (
    .A(zamieniacz_4_a_2), .B(REG_2_3), .A_2(zamieniacz_8_a_2), .B_2(OUT_2_3), .WYSTAPILO_ZDERZENIE(ZD_OUT));
  czy_zderzenie czy_zderzenie_9 (.W(REG_0_3), .L(REG_1), .OUT(czy_zderzenie_9_out));
  czy_zderzenie czy_zderzenie_10 (.W(REG_1_3), .L(REG_1_2), .OUT(czy_zderzenie_10_out));
  czy_zderzenie czy_zderzenie_11 (.W(REG_2_3), .L(REG_1_3), .OUT(czy_zderzenie_11_out));
  czy_zderzenie czy_zderzenie_12 (.W(REG_3_3), .L(REG_1_4), .OUT(czy_zderzenie_12_out));
  zamieniacz zamieniacz_9 (.A(zamieniacz_5_a_2), .B(REG_0_4), .A_2(OUT_0), .B_2(OUT_0_4), .WYSTAPILO_ZDERZENIE(ZD_OUT));
  zamieniacz zamieniacz_10 (
    .A(zamieniacz_6_a_2), .B(REG_0_3), .A_2(OUT_1), .B_2(OUT_0_3), .WYSTAPILO_ZDERZENIE(ZD_OUT));
  zamieniacz zamieniacz_11 (
    .A(zamieniacz_7_a_2), .B(REG_0_2), .A_2(OUT_2), .B_2(OUT_0_2), .WYSTAPILO_ZDERZENIE(ZD_OUT));
  zamieniacz zamieniacz_12 (
    .A(zamieniacz_8_a_2), .B(REG_1_3), .A_2(OUT_1_2), .B_2(OUT_1_3), .WYSTAPILO_ZDERZENIE(ZD_OUT));
  or or_3 (or_3_out, czy_zderzenie_9_out, czy_zderzenie_10_out, czy_zderzenie_11_out, czy_zderzenie_12_out);
  czy_zderzenie czy_zderzenie_13 (.W(REG_0_4), .L(REG_0), .OUT(czy_zderzenie_13_out));
  czy_zderzenie czy_zderzenie_14 (.W(REG_1_4), .L(REG_0_2), .OUT(czy_zderzenie_14_out));
  czy_zderzenie czy_zderzenie_15 (.W(REG_2_4), .L(REG_0_3), .OUT(czy_zderzenie_15_out));
  czy_zderzenie czy_zderzenie_16 (.W(REG_3_4), .L(REG_0_4), .OUT(czy_zderzenie_16_out));
  or or_4 (or_4_out, czy_zderzenie_13_out, czy_zderzenie_14_out, czy_zderzenie_15_out, czy_zderzenie_16_out);
  or or_5 (ZD_OUT, or_4_out, or_3_out, or_2_out, or_1_out);

  // Other names for the same wires on the sheet: _0[1:0] = REG_0; _1[1:0] = REG_1; _2[1:0] = REG_2; _3[1:0] = REG_3;
  //   _4[1:0] = REG_0_2; _5[1:0] = REG_1_2; _6[1:0] = REG_2_2; _7[1:0] = REG_3_2; _8[1:0] = REG_0_3;
  //   _9[1:0] = REG_1_3; _10[1:0] = REG_2_3; _11[1:0] = REG_3_3; _12[1:0] = REG_0_4; _13[1:0] = REG_1_4;
  //   _14[1:0] = REG_2_4; _15[1:0] = REG_3_4; OUT_4[1:0] = OUT_0_2; OUT_5[1:0] = OUT_1_2; OUT_6[1:0] = OUT_2_2;
  //   OUT_7[1:0] = OUT_3_2; OUT_8[1:0] = OUT_0_3; OUT_9[1:0] = OUT_1_3; OUT_10[1:0] = OUT_2_3; OUT_11[1:0] = OUT_3_3;
  //   OUT_12[1:0] = OUT_0_4; OUT_13[1:0] = OUT_1_4; OUT_14[1:0] = OUT_2_4; OUT_15[1:0] = OUT_3_4; ZD = ZD_OUT

  // Notes on the sheet:
  //   ZDERZENIE
endmodule
