// Logisim project ustawiacz_prawo_sciana.circ as structural Verilog: 1 circuit, main circuit logiczno-ustawiacz_norm
module logiczno_ustawiacz_norm (
  input  [1:0] REG_0,
  input  [1:0] REG_1,
  input  [1:0] REG_2,
  input  [1:0] REG_3,
  input  [1:0] REG_0_2,
  input  [1:0] REG_1_2,
  input  [1:0] REG_2_2,
  input  [1:0] REG_3_2,
  input  [1:0] REG_0_3,
  input  [1:0] REG_1_3,
  input  [1:0] REG_2_3,
  input  [1:0] REG_3_3,
  input  [1:0] REG_0_4,
  input  [1:0] REG_1_4,
  input  [1:0] REG_2_4,
  input  [1:0] REG_3_4,
  input  [1:0] REG_0_5,
  input  [1:0] REG_1_5,
  input  [1:0] REG_2_5,
  input  [1:0] REG_3_5,
  output [1:0] OUT_0,
  output [1:0] OUT_1,
  output [1:0] OUT_2,
  output [1:0] OUT_3,
  output [1:0] OUT_0_2,
  output [1:0] OUT_1_2,
  output [1:0] OUT_2_2,
  output [1:0] OUT_3_2,
  output [1:0] OUT_0_3,
  output [1:0] OUT_1_3,
  output [1:0] OUT_2_3,
  output [1:0] OUT_3_3,
  output [1:0] OUT_0_4,
  output [1:0] OUT_1_4,
  output [1:0] OUT_2_4,
  output [1:0] OUT_3_4,
  output ZD_OUT
);

  wire czy_zderzenie_1_p3, czy_zderzenie_2_p3, czy_zderzenie_3_p3, czy_zderzenie_4_p3, czy_zderzenie_5_p3,
       czy_zderzenie_6_p3, czy_zderzenie_7_p3, czy_zderzenie_8_p3, czy_zderzenie_9_p3, czy_zderzenie_10_p3,
       czy_zderzenie_11_p3, czy_zderzenie_12_p3, czy_zderzenie_13_p3, czy_zderzenie_14_p3,
       czy_zderzenie_15_p3, czy_zderzenie_16_p3, or_1_out, or_2_out, or_3_out, or_4_out, zamieniacz_1_p4,
       zamieniacz_2_p4, zamieniacz_3_p4, zamieniacz_4_p4, zamieniacz_5_p4, zamieniacz_6_p4, zamieniacz_7_p4,
       zamieniacz_8_p4, zamieniacz_9_p4, zamieniacz_10_p4, zamieniacz_11_p4, zamieniacz_12_p4;

  // czy_zderzenie czy_zderzenie_1: pin names not known; wires that end beside it: REG_0_2, REG_1_2, czy_zderzenie_1_p3
  // czy_zderzenie czy_zderzenie_2: pin names not known; wires that end beside it: REG_1_2, REG_2_2, czy_zderzenie_2_p3
  // czy_zderzenie czy_zderzenie_3: pin names not known; wires that end beside it: REG_2_2, REG_3_2, czy_zderzenie_3_p3
  // czy_zderzenie czy_zderzenie_4: pin names not known; wires that end beside it: REG_3_2, REG_0, czy_zderzenie_4_p3
  or or_1 (or_1_out, czy_zderzenie_1_p3, czy_zderzenie_2_p3, czy_zderzenie_3_p3, czy_zderzenie_4_p3);
  // zamieniacz zamieniacz_1: pin names not known; wires that end beside it: REG_3_2, REG_0, ZD_OUT, zamieniacz_1_p4
  // zamieniacz zamieniacz_2: pin names not known; wires that end beside it: REG_3_3, REG_1, ZD_OUT, zamieniacz_2_p4
  // zamieniacz zamieniacz_3: pin names not known; wires that end beside it: REG_3_4, REG_2, ZD_OUT, zamieniacz_3_p4
  // zamieniacz zamieniacz_4: pin names not known; wires that end beside it: REG_3_5, REG_3, ZD_OUT, zamieniacz_4_p4
  // czy_zderzenie czy_zderzenie_5: pin names not known; wires that end beside it: REG_0_3, REG_1_3, czy_zderzenie_5_p3
  // czy_zderzenie czy_zderzenie_6: pin names not known; wires that end beside it: REG_1_3, REG_2_3, czy_zderzenie_6_p3
  // czy_zderzenie czy_zderzenie_7: pin names not known; wires that end beside it: REG_2_3, REG_3_3, czy_zderzenie_7_p3
  // czy_zderzenie czy_zderzenie_8: pin names not known; wires that end beside it: REG_3_3, REG_1, czy_zderzenie_8_p3
  or or_2 (or_2_out, czy_zderzenie_5_p3, czy_zderzenie_6_p3, czy_zderzenie_7_p3, czy_zderzenie_8_p3);
  // zamieniacz zamieniacz_5: pin names not known; wires that end beside it: REG_2_2, zamieniacz_1_p4, ZD_OUT, zamieniacz_5_p4, OUT_3
  // zamieniacz zamieniacz_6: pin names not known; wires that end beside it: REG_2_3, zamieniacz_2_p4, ZD_OUT, zamieniacz_6_p4, OUT_3_2
  // zamieniacz zamieniacz_7: pin names not known; wires that end beside it: REG_2_4, zamieniacz_3_p4, ZD_OUT, zamieniacz_7_p4, OUT_3_3
  // zamieniacz zamieniacz_8: pin names not known; wires that end beside it: REG_2_5, zamieniacz_4_p4, ZD_OUT, zamieniacz_8_p4, OUT_3_4
  // czy_zderzenie czy_zderzenie_9: pin names not known; wires that end beside it: REG_0_4, REG_1_4, czy_zderzenie_9_p3
  // czy_zderzenie czy_zderzenie_10: pin names not known; wires that end beside it: REG_1_4, REG_2_4, czy_zderzenie_10_p3
  // czy_zderzenie czy_zderzenie_11: pin names not known; wires that end beside it: REG_2_4, REG_3_4, czy_zderzenie_11_p3
  // czy_zderzenie czy_zderzenie_12: pin names not known; wires that end beside it: REG_3_4, REG_2, czy_zderzenie_12_p3
  // zamieniacz zamieniacz_9: pin names not known; wires that end beside it: REG_1_2, zamieniacz_5_p4, ZD_OUT, zamieniacz_9_p4, OUT_2
  // zamieniacz zamieniacz_10: pin names not known; wires that end beside it: REG_1_3, zamieniacz_6_p4, ZD_OUT, zamieniacz_10_p4, OUT_2_2
  // zamieniacz zamieniacz_11: pin names not known; wires that end beside it: REG_1_4, zamieniacz_7_p4, ZD_OUT, zamieniacz_11_p4, OUT_2_3
  // zamieniacz zamieniacz_12: pin names not known; wires that end beside it: REG_1_5, zamieniacz_8_p4, ZD_OUT, zamieniacz_12_p4, OUT_2_4
  or or_3 (or_3_out, czy_zderzenie_9_p3, czy_zderzenie_10_p3, czy_zderzenie_11_p3, czy_zderzenie_12_p3);
  // czy_zderzenie czy_zderzenie_13: pin names not known; wires that end beside it: REG_0_5, REG_1_5, czy_zderzenie_13_p3
  // czy_zderzenie czy_zderzenie_14: pin names not known; wires that end beside it: REG_1_5, REG_2_5, czy_zderzenie_14_p3
  // czy_zderzenie czy_zderzenie_15: pin names not known; wires that end beside it: REG_2_5, REG_3_5, czy_zderzenie_15_p3
  // czy_zderzenie czy_zderzenie_16: pin names not known; wires that end beside it: REG_3_5, REG_3, czy_zderzenie_16_p3
  // zamieniacz zamieniacz_13: pin names not known; wires that end beside it: REG_0_2, zamieniacz_9_p4, ZD_OUT, OUT_0, OUT_1
  // zamieniacz zamieniacz_14: pin names not known; wires that end beside it: REG_0_3, zamieniacz_10_p4, ZD_OUT, OUT_0_2, OUT_1_2
  // zamieniacz zamieniacz_15: pin names not known; wires that end beside it: REG_0_4, zamieniacz_11_p4, ZD_OUT, OUT_0_3, OUT_1_3
  // zamieniacz zamieniacz_16: pin names not known; wires that end beside it: REG_0_5, zamieniacz_12_p4, ZD_OUT, OUT_0_4, OUT_1_4
  or or_4 (or_4_out, czy_zderzenie_13_p3, czy_zderzenie_14_p3, czy_zderzenie_15_p3, czy_zderzenie_16_p3);
  or or_5 (ZD_OUT, or_4_out, or_3_out, or_2_out, or_1_out);

  // Other names for the same wires on the sheet: _0[1:0] = REG_0; _1[1:0] = REG_1; _2[1:0] = REG_2; _3[1:0] = REG_3;
  //   _4[1:0] = REG_0_2; _5[1:0] = REG_1_2; _6[1:0] = REG_2_2; _7[1:0] = REG_3_2; _8[1:0] = REG_0_3;
  //   _9[1:0] = REG_1_3; _10[1:0] = REG_2_3; _11[1:0] = REG_3_3; _12[1:0] = REG_0_4; _13[1:0] = REG_1_4;
  //   _14[1:0] = REG_2_4; _15[1:0] = REG_3_4; _16[1:0] = REG_0_5; _17[1:0] = REG_1_5; _18[1:0] = REG_2_5;
  //   _19[1:0] = REG_3_5; OUT_4[1:0] = OUT_0; OUT_5[1:0] = OUT_1; OUT_6[1:0] = OUT_2; OUT_7[1:0] = OUT_3;
  //   OUT_8[1:0] = OUT_0_2; OUT_9[1:0] = OUT_1_2; OUT_10[1:0] = OUT_2_2; OUT_11[1:0] = OUT_3_2; OUT_12[1:0] = OUT_0_3;
  //   OUT_13[1:0] = OUT_1_3; OUT_14[1:0] = OUT_2_3; OUT_15[1:0] = OUT_3_3; OUT_16[1:0] = OUT_0_4;
  //   OUT_17[1:0] = OUT_1_4; OUT_18[1:0] = OUT_2_4; OUT_19[1:0] = OUT_3_4; ZD = ZD_OUT

  // Notes on the sheet:
  //   wiersz 1
  //   wiersz 2
  //   wiersz 3
  //   wiersz 4
  //   wiersz 5
  //   ZDERZENIE
endmodule
