// Logisim project przesuwanie.circ as structural Verilog: 1 circuit, main circuit main
module main (
  input  RESET,
  input  [6:0] A1,
  input  CLK,
  input  ENABLE,
  input  [1:0] DATA_IN,
  input  FLAGA,
  output [6:0] NOWE_A1,
  output [1:0] DATA_OUT,
  output RAM_CLK,
  output ZD,
  output [6:0] A,
  output FINISH
);

  wire and_1_out, demultiplexer_2_out0, demultiplexer_2_out1, demultiplexer_2_out2, demultiplexer_2_out3,
       main_2_finish, main_2_ram_clk, main_2_zd_out, main_3_finish, main_3_ram_clk, main_3_zd_out,
       main_4_finish, main_4_ram_clk, main_4_zd_out, main_5_finish, main_5_ram_clk, main_5_zd_out,
       multiplexer_3_out;
  wire [1:0] demultiplexer_3_out0, demultiplexer_3_out1, demultiplexer_3_out2, demultiplexer_3_out3,
       main_2_data_out, main_3_data_out, main_4_data_out, main_5_data_out, TRYB;
  wire [6:0] demultiplexer_1_out0, demultiplexer_1_out1, demultiplexer_1_out2, demultiplexer_1_out3,
       main_2_a, main_3_a, main_4_a, main_5_a;

  and and_1 (and_1_out, CLK, ENABLE);
  trybo_selektor_main main_1 (.A1(A1), .FLAGA(FLAGA), .NOWE_A1(NOWE_A1), .TRYB(TRYB));
  Demultiplexer #(.select(2), .width(7)) demultiplexer_1 (
    .out0(demultiplexer_1_out0), .out1(demultiplexer_1_out1), .out2(demultiplexer_1_out2),
    .out3(demultiplexer_1_out3), .in(A1), .sel(TRYB));  // open: en
  Demultiplexer #(.select(2)) demultiplexer_2 (
    .out0(demultiplexer_2_out0), .out1(demultiplexer_2_out1), .out2(demultiplexer_2_out2),
    .out3(demultiplexer_2_out3), .in(and_1_out), .sel(TRYB));  // open: en
  Demultiplexer #(.select(2), .width(2)) demultiplexer_3 (
    .out0(demultiplexer_3_out0), .out1(demultiplexer_3_out1), .out2(demultiplexer_3_out2),
    .out3(demultiplexer_3_out3), .in(DATA_IN), .sel(TRYB));  // open: en
  przesuwanie_prawo_bezsciany_main main_2 (
    .A1(demultiplexer_1_out1), .DATA_IN(demultiplexer_3_out1), .CLK(demultiplexer_2_out1),
    .ZD_OUT(main_2_zd_out), .A(main_2_a), .FINISH(main_2_finish), .RAM_CLK(main_2_ram_clk),
    .DATA_OUT(main_2_data_out), .R(RESET));
  przesuwanie_lewo_bezsciany_main main_3 (
    .A1(demultiplexer_1_out3), .DATA_IN(demultiplexer_3_out3), .CLK(demultiplexer_2_out3),
    .ZD_OUT(main_3_zd_out), .A(main_3_a), .FINISH(main_3_finish), .RAM_CLK(main_3_ram_clk),
    .DATA_OUT(main_3_data_out), .RESET(RESET));
  przesuwanie_prawo_sciana_main main_4 (
    .A1(demultiplexer_1_out0), .DATA_IN(demultiplexer_3_out0), .CLK(demultiplexer_2_out0),
    .ZD_OUT(main_4_zd_out), .A(main_4_a), .FINISH(main_4_finish), .RAM_CLK(main_4_ram_clk),
    .DATA_OUT(main_4_data_out), .Reset(RESET));
  przesuwanie_lewo_sciana_main main_5 (
    .A1(demultiplexer_1_out2), .DATA_IN(demultiplexer_3_out2), .CLK(demultiplexer_2_out2),
    .ZD_OUT(main_5_zd_out), .A(main_5_a), .FINISH(main_5_finish), .RAM_CLK(main_5_ram_clk),
    .DATA_OUT(main_5_data_out), .RESET(RESET));
  Multiplexer #(.select(2), .width(2)) multiplexer_1 (
    .in0(main_4_data_out), .in1(main_2_data_out), .in2(main_5_data_out), .in3(main_3_data_out),
    .out(DATA_OUT), .sel(TRYB));  // open: en
  Multiplexer #(.select(2)) multiplexer_2 (
    .in0(main_4_ram_clk), .in1(main_2_ram_clk), .in2(main_5_ram_clk), .in3(main_3_ram_clk), .out(RAM_CLK),
    .sel(TRYB));  // open: en
  Multiplexer #(.select(2)) multiplexer_3 (
    .in0(main_4_zd_out), .in1(main_2_zd_out), .in2(main_5_zd_out), .in3(main_3_zd_out),
    .out(multiplexer_3_out), .sel(TRYB));  // open: en
  Multiplexer #(.select(2), .width(7)) multiplexer_4 (
    .in0(main_4_a), .in1(main_2_a), .in2(main_5_a), .in3(main_3_a), .out(A), .sel(TRYB));  // open: en
  Multiplexer #(.select(2)) multiplexer_5 (
    .in0(main_4_finish), .in1(main_2_finish), .in2(main_5_finish), .in3(main_3_finish), .out(FINISH),
    .sel(TRYB));  // open: en
  and and_2 (ZD, multiplexer_3_out, FINISH);

  // Other names for the same wires on the sheet: R = RESET
endmodule
