// Logisim project trybo_selektor.circ as structural Verilog: 1 circuit, main circuit main
module main (
  input  [6:0] A1,
  input  FLAGA,
  output [6:0] NOWE_A1,
  output [1:0] TRYB
);

  wire comparator_1_eq, comparator_1_gt, comparator_2_eq, comparator_2_gt, comparator_2_lt, or_1_out;
  wire [3:0] SELECT;
  wire [6:0] adder_1_out, divider_1_rem, subtractor_1_out;

  Comparator #(.width(7), .mode("unsigned")) comparator_1 (
    .a(divider_1_rem), .b({7{1'b0}}), .gt(comparator_1_gt), .eq(comparator_1_eq));  // open: lt
  Divider #(.width(7)) divider_1 (.a(A1), .b(7'b0001000), .rem(divider_1_rem));  // open: out, upper
  Comparator #(.width(7), .mode("unsigned")) comparator_2 (
    .a(divider_1_rem), .b(7'b0000011), .gt(comparator_2_gt), .eq(comparator_2_eq), .lt(comparator_2_lt));
  or or_1 (or_1_out, comparator_2_lt, comparator_2_eq);
  and and_1 (SELECT[1], or_1_out, FLAGA);
  and and_2 (SELECT[2], comparator_1_eq, ~FLAGA);  // AND_Gate
  and and_3 (SELECT[3], comparator_1_gt, ~FLAGA);  // AND_Gate
  and and_4 (SELECT[0], comparator_2_gt, FLAGA);
  Subtractor #(.width(7)) subtractor_1 (.a(A1), .b(7'b0000001), .out(subtractor_1_out));  // open: bin, bout
  Adder #(.width(7)) adder_1 (.a(A1), .b(7'b0000001), .out(adder_1_out));  // open: cin, cout
  Multiplexer #(.select(4), .width(7)) multiplexer_1 (
    .in1(A1), .in2(adder_1_out), .in4(A1), .in8(subtractor_1_out), .out(NOWE_A1), .sel(SELECT));  // open: in0, in3, in5, in6, in7, in9, in10, in11, in12, in13, in14, in15, en
  Multiplexer #(.select(4), .width(2)) multiplexer_2 (
    .in1(2'b00), .in2(2'b01), .in4(2'b10), .in8(2'b11), .out(TRYB), .sel(SELECT));  // open: in0, in3, in5, in6, in7, in9, in10, in11, in12, in13, in14, in15, en

  // Notes on the sheet:
  //   1 to prawo
  //   nie trzeba przesuwac w srodku lewo
  //   nie trzeba przesuwac w srodku
  //   trzeba przesunac w srodku lewo
  //   na zewnatrz musi byc wykrycie gdy cos nacisnie na klawiature i w zalezności od tego ustawia flagę na 0 (lewo) lub 1(prawo) i ustawia enable
  //   trzeba przesunac w srodku prawo
  //   prawo
  //   0 - prawo pozostaje A1
  //   2-lewo pozostaje A1
  //   3-lewo przesuwanie A1
  //   1- prawo przesuwanie A1
endmodule
