// Logisim project obnizanie.circ as structural Verilog: 1 circuit, main circuit main
module main (
  input  [1:0] DATA_IN,
  input  [6:0] A1,
  input  RAM_CLK,
  input  ENABLE,
  output [1:0] DATA_OUT,
  output [6:0] A,
  output [6:0] out_7,
  output [3:0] poprzednie__W,
  output \ZAMROŹ ,
  output FINISH
);

  wire and_1_out, and_2_out, and_3_out, clock_1_out, comparator_1_lt, comparator_2_eq, main_1__0_4,
       main_1__0_5, main_1__0_6, main_1__0_7, main_1__0_8, or_2_out, or_3_out;
  wire [1:0] register_3_q;
  wire [2:0] counter_1_q;
  wire [3:0] multiplexer_2_out;
  wire [6:0] adder_2_out, counter_2_q, register_1_q, subtractor_1_out;

  Adder #(.width(7)) adder_1 (.a(A1), .b(7'b0100111), .out(out_7));  // open: cin, cout
  Counter #(.width(3), .max('h7)) counter_1 (.Q(counter_1_q), .clk(and_2_out));  // open: load, D, count, carry, clr
  or or_1 (RAM_CLK, main_1__0_4, main_1__0_5);
  Clock clock_1 (.out(clock_1_out));
  switch8bit_main main_1 (
    .INPUT(counter_1_q), ._0_4(main_1__0_4), ._0_5(main_1__0_5), ._0_6(main_1__0_6), ._0_7(main_1__0_7),
    ._0_8(main_1__0_8));  // open: _0, _0_2, _0_3
  Counter #(.width(7), .max('h7f)) counter_2 (.Q(counter_2_q), .clk(main_1__0_8));  // open: load, D, count, carry, clr
  and and_1 (and_1_out, clock_1_out, ENABLE);
  Multiplexer #(.width(7)) multiplexer_1 (.in0(register_1_q), .in1(adder_2_out), .out(A), .sel(and_3_out));  // open: en
  Adder #(.width(7)) adder_2 (.a(register_1_q), .b(7'b0001000), .out(adder_2_out));  // open: cin, cout
  Register #(.width(7)) register_1 (.D(subtractor_1_out), .Q(register_1_q), .clk(main_1__0_7));  // open: en, clr
  Subtractor #(.width(7)) subtractor_1 (.a(out_7), .b(counter_2_q), .out(subtractor_1_out));  // open: bin, bout
  and and_2 (and_2_out, and_1_out, ~or_3_out, comparator_1_lt);  // AND_Gate
  and and_3 (and_3_out, comparator_2_eq, or_2_out);
  or or_2 (or_2_out, main_1__0_5, main_1__0_6);
  Comparator #(.width(7), .mode("unsigned")) comparator_1 (
    .a(counter_2_q), .b(7'b0010001), .eq(FINISH), .lt(comparator_1_lt));  // open: gt
  Register #(.width(2)) register_2 (.D(DATA_IN), .Q(poprzednie__W[3:2]), .clk(main_1__0_7));  // open: en, clr
  Comparator #(.width(2), .mode("unsigned")) comparator_2 (
    .a(DATA_IN), .b(2'b01), .eq(comparator_2_eq));  // open: gt, lt
  or or_3 (or_3_out, \ZAMROŹ , FINISH);
  Multiplexer #(.select(4), .width(4)) multiplexer_2 (
    .in0(4'b0000), .in3(4'b0001), .out(multiplexer_2_out), .sel({poprzednie__W[3:2], DATA_IN}));  // open: in1, in2, in4, in5, in6, in7, in8, in9, in10, in11, in12, in13, in14, in15, en
  Multiplexer #(.width(2)) multiplexer_3 (
    .in0(multiplexer_2_out[1:0]), .in1(register_3_q), .out(DATA_OUT), .sel(main_1__0_4));  // open: en
  Comparator #(.width(4), .mode("unsigned")) comparator_3 (
    .a({poprzednie__W[3:2], DATA_IN}), .b(4'b0110), .eq(\ZAMROŹ ));  // open: gt, lt
  Register #(.width(2)) register_3 (.D(multiplexer_2_out[3:2]), .Q(register_3_q), .clk(main_1__0_6));  // open: en, clr

  assign poprzednie__W[1:0] = DATA_IN;

  // Notes on the sheet:
  //   4 w dol 7 w prawo
  //   zmodyfikowac ze dostaje prawy dolny
  //   aktualny adres weryfikowany
  //   refA
  //   aktualne (N)
endmodule
