// Logisim project obnizanie_new.circ as structural Verilog: 1 circuit, main circuit obnizanie
module obnizanie (
  input  [6:0] A1,
  input  [1:0] DATA_IN,
  input  CLK,
  input  ENABLE,
  output [6:0] A,
  output FINISH,
  output [1:0] DATA_OUT,
  output RAM_CLK
);

  wire and_1_out;

  and and_1 (and_1_out, CLK, ENABLE);
  adreso_latacz adreso_latacz_1 (.CLK(and_1_out), .ADRES_OUT(A), .FINISH(FINISH), .ADRES_ROOT(A1));
  wiersz wiersz_1 (.CLK(and_1_out), .RAM_CLK(RAM_CLK), .DATA_IN(DATA_IN), .DATA_OUT(DATA_OUT));
endmodule
