// Logisim project test_obnizenie_new.circ as structural Verilog: 1 circuit, main circuit main
module main (
  input  [6:0] in_1,
  input  in_2,
  output out_3
);

  wire clock_1_out, obnizanie_1_ram_clk;
  wire [1:0] obnizanie_1_data_out, ram_1_data;
  wire [6:0] obnizanie_1_a;

  Clock clock_1 (.out(clock_1_out));
  RAM #(.addrWidth(7), .dataWidth(2), .bus("separate")) ram_1 (
    .addr(obnizanie_1_a), .din(obnizanie_1_data_out), .data(ram_1_data), .clk(obnizanie_1_ram_clk));  // open: str, sel, ld, clr
  obnizanie obnizanie_1 (
    .ENABLE(in_2), .FINISH(out_3), .A1(in_1), .A(obnizanie_1_a), .DATA_IN(ram_1_data),
    .DATA_OUT(obnizanie_1_data_out), .CLK(clock_1_out), .RAM_CLK(obnizanie_1_ram_clk));

  // Notes on the sheet:
  //   przestrzeni 4x4 i później nadpisywania całego 4x4
  //   jest to możliwe, ale jakim kosztem
  //   może nie aż tak dużym ale jednak
  //   przebudowa tego wymagała by sprawdzania nie tylko dolnego wiersza, ale całej
  //   BUG
  //   sprawdza kolizję tylko dla dolnego wiersza, a powinno dla całości przestrzeni sprawdzić
  //   i dopiero wtedy modyfikować
  //   16 rejestrow W i 16 rejestrow N i sprawdzanie wszystkich i wtedy dopiero po kolei taktowanie po odpowiednich?
endmodule
