// Logisim project przesuwanie_prawo_bezsciany.circ as structural Verilog: 1 circuit, main circuit main
module main (
  input  [6:0] A1,
  input  [1:0] DATA_IN,
  input  CLK,
  output [6:0] A,
  output FINISH,
  output ZD_OUT,
  output RAM_CLK,
  output [1:0] DATA_OUT
);

  wire and_1_out, comparator_1_eq, comparator_2_eq, comparator_2_lt, comparator_3_gt, comparator_4_eq,
       comparator_5_eq, comparator_6_eq, or_1_out, register_1_q;
  wire [1:0] logiczno_ustawiacz_norm_1_out_0, logiczno_ustawiacz_norm_1_out_0_2,
       logiczno_ustawiacz_norm_1_out_0_3, logiczno_ustawiacz_norm_1_out_0_4,
       logiczno_ustawiacz_norm_1_out_0_5, logiczno_ustawiacz_norm_1_out_1, logiczno_ustawiacz_norm_1_out_1_2,
       logiczno_ustawiacz_norm_1_out_1_3, logiczno_ustawiacz_norm_1_out_1_4,
       logiczno_ustawiacz_norm_1_out_1_5, logiczno_ustawiacz_norm_1_out_2, logiczno_ustawiacz_norm_1_out_2_2,
       logiczno_ustawiacz_norm_1_out_2_3, logiczno_ustawiacz_norm_1_out_2_4,
       logiczno_ustawiacz_norm_1_out_2_5, logiczno_ustawiacz_norm_1_out_3, logiczno_ustawiacz_norm_1_out_3_2,
       logiczno_ustawiacz_norm_1_out_3_3, logiczno_ustawiacz_norm_1_out_3_4,
       logiczno_ustawiacz_norm_1_out_3_5, shift_register_1_q0, shift_register_1_q1, shift_register_1_q2,
       shift_register_1_q3, shift_register_1_q4, shift_register_1_q5, shift_register_1_q6,
       shift_register_1_q7, shift_register_1_q8, shift_register_1_q9, shift_register_1_q10,
       shift_register_1_q11, shift_register_1_q12, shift_register_1_q13, shift_register_1_q14,
       shift_register_1_q15, shift_register_1_q16, shift_register_1_q17, shift_register_1_q18,
       shift_register_1_q19;
  wire [4:0] counter_3_q;
  wire [5:0] counter_2_q;
  wire [6:0] adder_1_out, counter_1_q, counter_4_q, counter_5_q, multiplier_1_out;

  Counter #(.width(7), .max('h4)) counter_1 (.Q(counter_1_q), .clk(CLK));  // open: load, D, count, carry, clr
  Counter #(.width(6), .max('h27)) counter_2 (.Q(counter_2_q), .clk(CLK));  // open: load, D, count, carry, clr
  Counter #(.width(5), .max('h13)) counter_3 (.Q(counter_3_q), .clk(CLK));  // open: load, D, count, carry, clr
  Adder #(.width(7)) adder_1 (.a(A1), .b(counter_1_q), .out(adder_1_out));  // open: cin, cout
  Counter #(.width(7), .max('h3)) counter_4 (
    .Q(counter_4_q), .clk(comparator_1_eq));  // open: load, D, count, carry, clr
  Comparator #(.width(7), .mode("unsigned")) comparator_1 (
    .a(counter_1_q), .b({7{1'b0}}), .eq(comparator_1_eq));  // open: gt, lt
  Counter #(.width(7), .max('h14)) counter_5 (.Q(counter_5_q), .clk(CLK));  // open: load, D, count, carry, clr
  Comparator #(.width(6), .mode("unsigned")) comparator_2 (
    .a(counter_2_q), .b(6'b010011), .eq(comparator_2_eq), .lt(comparator_2_lt));  // open: gt
  Comparator #(.width(6), .mode("unsigned")) comparator_3 (
    .a(counter_2_q), .b(6'b010011), .gt(comparator_3_gt));  // open: eq, lt
  Adder #(.width(7)) adder_2 (.a(adder_1_out), .b(multiplier_1_out), .out(A));  // open: cin, cout
  Multiplier #(.width(7)) multiplier_1 (.a(counter_4_q), .b(7'b0001000), .out(multiplier_1_out));  // open: cin, cout
  Comparator #(.width(7), .mode("unsigned")) comparator_4 (
    .a(counter_5_q), .b({7{1'b0}}), .eq(comparator_4_eq));  // open: gt, lt
  Register #(.width(1)) register_1 (
    .D(1'b1), .Q(register_1_q), .clk(comparator_6_eq), .clr(comparator_5_eq));  // open: en
  Comparator #(.width(7), .mode("unsigned")) comparator_5 (
    .a(counter_5_q), .b(7'b0000001), .eq(comparator_5_eq));  // open: gt, lt
  Comparator #(.width(7), .mode("unsigned")) comparator_6 (
    .a(counter_5_q), .b(7'b0000010), .eq(comparator_6_eq));  // open: gt, lt
  and and_1 (and_1_out, or_1_out, CLK);
  or or_1 (or_1_out, comparator_2_eq, comparator_2_lt);
  and and_2 (RAM_CLK, CLK, comparator_3_gt);
  and and_3 (FINISH, comparator_4_eq, register_1_q);
  Shift_Register #(.width(2), .length(20)) shift_register_1 (
    .in(DATA_IN), .clk(and_1_out), .q0(shift_register_1_q0), .q1(shift_register_1_q1),
    .q2(shift_register_1_q2), .q3(shift_register_1_q3), .q4(shift_register_1_q4), .q5(shift_register_1_q5),
    .q6(shift_register_1_q6), .q7(shift_register_1_q7), .q8(shift_register_1_q8), .q9(shift_register_1_q9),
    .q10(shift_register_1_q10), .q11(shift_register_1_q11), .q12(shift_register_1_q12),
    .q13(shift_register_1_q13), .q14(shift_register_1_q14), .q15(shift_register_1_q15),
    .q16(shift_register_1_q16), .q17(shift_register_1_q17), .q18(shift_register_1_q18),
    .q19(shift_register_1_q19));  // open: shift, out, load, clr, d0, d1, d2, d3, d4, d5, d6, d7, d8, d9, d10, d11, d12, d13, d14, d15, d16, d17, d18, d19
  logiczno_ustawiacz_norm logiczno_ustawiacz_norm_1 (
    .REG_0(shift_register_1_q19), .REG_1(shift_register_1_q18), .REG_2(shift_register_1_q17),
    .REG_3(shift_register_1_q16), .REG_0_2(shift_register_1_q15), .REG_1_2(shift_register_1_q14),
    .REG_2_2(shift_register_1_q13), .REG_3_2(shift_register_1_q12), .REG_0_3(shift_register_1_q11),
    .REG_1_3(shift_register_1_q10), .REG_2_3(shift_register_1_q9), .REG_3_3(shift_register_1_q8),
    .REG_0_4(shift_register_1_q7), .REG_1_4(shift_register_1_q6), .REG_2_4(shift_register_1_q5),
    .REG_3_4(shift_register_1_q4), .REG_0_5(shift_register_1_q3), .REG_1_5(shift_register_1_q2),
    .REG_2_5(shift_register_1_q1), .REG_3_5(shift_register_1_q0), .OUT_0(logiczno_ustawiacz_norm_1_out_0),
    .OUT_1(logiczno_ustawiacz_norm_1_out_1), .OUT_2(logiczno_ustawiacz_norm_1_out_2),
    .OUT_3(logiczno_ustawiacz_norm_1_out_3), .OUT_0_2(logiczno_ustawiacz_norm_1_out_0_2),
    .OUT_1_2(logiczno_ustawiacz_norm_1_out_1_2), .OUT_2_2(logiczno_ustawiacz_norm_1_out_2_2),
    .OUT_3_2(logiczno_ustawiacz_norm_1_out_3_2), .OUT_0_3(logiczno_ustawiacz_norm_1_out_0_3),
    .OUT_1_3(logiczno_ustawiacz_norm_1_out_1_3), .OUT_2_3(logiczno_ustawiacz_norm_1_out_2_3),
    .OUT_3_3(logiczno_ustawiacz_norm_1_out_3_3), .OUT_0_4(logiczno_ustawiacz_norm_1_out_0_4),
    .OUT_1_4(logiczno_ustawiacz_norm_1_out_1_4), .OUT_2_4(logiczno_ustawiacz_norm_1_out_2_4),
    .OUT_3_4(logiczno_ustawiacz_norm_1_out_3_4), .OUT_0_5(logiczno_ustawiacz_norm_1_out_0_5),
    .OUT_1_5(logiczno_ustawiacz_norm_1_out_1_5), .OUT_2_5(logiczno_ustawiacz_norm_1_out_2_5),
    .OUT_3_5(logiczno_ustawiacz_norm_1_out_3_5), .ZD_OUT(ZD_OUT));
  Multiplexer #(.select(5), .width(2)) multiplexer_1 (
    .in0(logiczno_ustawiacz_norm_1_out_0), .in1(logiczno_ustawiacz_norm_1_out_1),
    .in2(logiczno_ustawiacz_norm_1_out_2), .in3(logiczno_ustawiacz_norm_1_out_3),
    .in4(logiczno_ustawiacz_norm_1_out_0_2), .in5(logiczno_ustawiacz_norm_1_out_1_2),
    .in6(logiczno_ustawiacz_norm_1_out_2_2), .in7(logiczno_ustawiacz_norm_1_out_3_2),
    .in8(logiczno_ustawiacz_norm_1_out_0_3), .in9(logiczno_ustawiacz_norm_1_out_1_3),
    .in10(logiczno_ustawiacz_norm_1_out_2_3), .in11(logiczno_ustawiacz_norm_1_out_3_3),
    .in12(logiczno_ustawiacz_norm_1_out_0_4), .in13(logiczno_ustawiacz_norm_1_out_1_4),
    .in14(logiczno_ustawiacz_norm_1_out_2_4), .in15(logiczno_ustawiacz_norm_1_out_3_4),
    .in16(logiczno_ustawiacz_norm_1_out_0_5), .in17(logiczno_ustawiacz_norm_1_out_1_5),
    .in18(logiczno_ustawiacz_norm_1_out_2_5), .in19(logiczno_ustawiacz_norm_1_out_3_5), .out(DATA_OUT),
    .sel(counter_3_q));  // open: in20, in21, in22, in23, in24, in25, in26, in27, in28, in29, in30, in31, en

  // Notes on the sheet:
  //   tu
  //   tu prawie na pewno naprawic
  //   NOWE A1 dać poziom wyżej
endmodule
