// Logisim project sprawdzenie_kolizji_prawo_bezsciany.circ as structural Verilog: 1 circuit, main circuit czy_zderzenie
module czy_zderzenie (
  input  [1:0] L,
  input  [1:0] P,
  output OUT
);

  Multiplexer #(.select(4), .disabled(0)) multiplexer_1 (
    .in0(1'b0), .in1(1'b0), .in2(1'b0), .in3(1'b0), .in4(1'b0), .in5(1'b0), .in6(1'b1), .in7(1'b0),
    .in8(1'b0), .in9(1'b0), .in10(1'b0), .in11(1'b0), .in12(1'b0), .in13(1'b0), .in14(1'b0), .in15(1'b0),
    .out(OUT), .sel({P, L}));  // open: en
endmodule
