// Logisim project ustawiacz_prawo_bezsciany.circ as structural Verilog: 1 circuit, main circuit logiczno-ustawiacz_norm
module logiczno_ustawiacz_norm (
  input  [1:0] REG_0,
  input  [1:0] REG_1,
  input  [1:0] REG_2,
  input  [1:0] REG_3,
  input  [1:0] REG_0_2,
  input  [1:0] REG_1_2,
  input  [1:0] REG_2_2,
  input  [1:0] REG_3_2,
  input  [1:0] REG_0_3,
  input  [1:0] REG_1_3,
  input  [1:0] REG_2_3,
  input  [1:0] REG_3_3,
  input  [1:0] REG_0_4,
  input  [1:0] REG_1_4,
  input  [1:0] REG_2_4,
  input  [1:0] REG_3_4,
  input  [1:0] REG_0_5,
  input  [1:0] REG_1_5,
  input  [1:0] REG_2_5,
  input  [1:0] REG_3_5,
  output [1:0] OUT_0,
  output [1:0] OUT_1,
  output [1:0] OUT_2,
  output [1:0] OUT_3,
  output [1:0] OUT_0_2,
  output [1:0] OUT_1_2,
  output [1:0] OUT_2_2,
  output [1:0] OUT_3_2,
  output [1:0] OUT_0_3,
  output [1:0] OUT_1_3,
  output [1:0] OUT_2_3,
  output [1:0] OUT_3_3,
  output [1:0] OUT_0_4,
  output [1:0] OUT_1_4,
  output [1:0] OUT_2_4,
  output [1:0] OUT_3_4,
  output [1:0] OUT_0_5,
  output [1:0] OUT_1_5,
  output [1:0] OUT_2_5,
  output [1:0] OUT_3_5,
  output ZD_OUT
);

  wire czy_zderzenie_1_out, czy_zderzenie_2_out, czy_zderzenie_3_out, czy_zderzenie_4_out,
       czy_zderzenie_5_out, czy_zderzenie_6_out, czy_zderzenie_7_out, czy_zderzenie_8_out,
       czy_zderzenie_9_out, czy_zderzenie_10_out, czy_zderzenie_11_out, czy_zderzenie_12_out,
       czy_zderzenie_13_out, czy_zderzenie_14_out, czy_zderzenie_15_out, czy_zderzenie_16_out, or_1_out,
       or_2_out, or_3_out, or_4_out;
  wire [1:0] zamieniacz_1_l_2, zamieniacz_2_l_2, zamieniacz_3_l_2, zamieniacz_4_l_2, zamieniacz_5_l_2,
       zamieniacz_6_l_2, zamieniacz_7_l_2, zamieniacz_8_l_2, zamieniacz_9_l_2, zamieniacz_10_l_2,
       zamieniacz_11_l_2, zamieniacz_12_l_2;

  czy_zderzenie czy_zderzenie_1 (.L(REG_0), .P(REG_1), .OUT(czy_zderzenie_1_out));
  czy_zderzenie czy_zderzenie_2 (.L(REG_1), .P(REG_2), .OUT(czy_zderzenie_2_out));
  czy_zderzenie czy_zderzenie_3 (.L(REG_2), .P(REG_3), .OUT(czy_zderzenie_3_out));
  czy_zderzenie czy_zderzenie_4 (.L(REG_3), .P(REG_0_2), .OUT(czy_zderzenie_4_out));
  zamieniacz zamieniacz_1 (.L(REG_3), .P(REG_0_2), .L_2(zamieniacz_1_l_2), .P_2(OUT_0_2), .WYSTAPILO_ZDERZENIE(ZD_OUT));
  zamieniacz zamieniacz_2 (
    .L(REG_0_3), .P(REG_1_3), .L_2(zamieniacz_2_l_2), .P_2(OUT_1_3), .WYSTAPILO_ZDERZENIE(ZD_OUT));
  zamieniacz zamieniacz_3 (
    .L(REG_1_4), .P(REG_2_4), .L_2(zamieniacz_3_l_2), .P_2(OUT_2_4), .WYSTAPILO_ZDERZENIE(ZD_OUT));
  zamieniacz zamieniacz_4 (
    .L(REG_2_5), .P(REG_3_5), .L_2(zamieniacz_4_l_2), .P_2(OUT_3_5), .WYSTAPILO_ZDERZENIE(ZD_OUT));
  or or_1 (or_1_out, czy_zderzenie_1_out, czy_zderzenie_2_out, czy_zderzenie_3_out, czy_zderzenie_4_out);
  czy_zderzenie czy_zderzenie_5 (.L(REG_1_2), .P(REG_2_2), .OUT(czy_zderzenie_5_out));
  czy_zderzenie czy_zderzenie_6 (.L(REG_2_2), .P(REG_3_2), .OUT(czy_zderzenie_6_out));
  czy_zderzenie czy_zderzenie_7 (.L(REG_3_2), .P(REG_0_3), .OUT(czy_zderzenie_7_out));
  czy_zderzenie czy_zderzenie_8 (.L(REG_0_3), .P(REG_1_3), .OUT(czy_zderzenie_8_out));
  zamieniacz zamieniacz_5 (
    .L(REG_2), .P(zamieniacz_1_l_2), .L_2(zamieniacz_5_l_2), .P_2(OUT_3), .WYSTAPILO_ZDERZENIE(ZD_OUT));
  zamieniacz zamieniacz_6 (
    .L(REG_3_2), .P(zamieniacz_2_l_2), .L_2(zamieniacz_6_l_2), .P_2(OUT_0_3), .WYSTAPILO_ZDERZENIE(ZD_OUT));
  zamieniacz zamieniacz_7 (
    .L(REG_0_4), .P(zamieniacz_3_l_2), .L_2(zamieniacz_7_l_2), .P_2(OUT_1_4), .WYSTAPILO_ZDERZENIE(ZD_OUT));
  zamieniacz zamieniacz_8 (
    .L(REG_1_5), .P(zamieniacz_4_l_2), .L_2(zamieniacz_8_l_2), .P_2(OUT_2_5), .WYSTAPILO_ZDERZENIE(ZD_OUT));
  or or_2 (or_2_out, czy_zderzenie_5_out, czy_zderzenie_6_out, czy_zderzenie_7_out, czy_zderzenie_8_out);
  zamieniacz zamieniacz_9 (
    .L(REG_1), .P(zamieniacz_5_l_2), .L_2(zamieniacz_9_l_2), .P_2(OUT_2), .WYSTAPILO_ZDERZENIE(ZD_OUT));
  zamieniacz zamieniacz_10 (
    .L(REG_2_2), .P(zamieniacz_6_l_2), .L_2(zamieniacz_10_l_2), .P_2(OUT_3_2), .WYSTAPILO_ZDERZENIE(ZD_OUT));
  zamieniacz zamieniacz_11 (
    .L(REG_3_3), .P(zamieniacz_7_l_2), .L_2(zamieniacz_11_l_2), .P_2(OUT_0_4), .WYSTAPILO_ZDERZENIE(ZD_OUT));
  zamieniacz zamieniacz_12 (
    .L(REG_0_5), .P(zamieniacz_8_l_2), .L_2(zamieniacz_12_l_2), .P_2(OUT_1_5), .WYSTAPILO_ZDERZENIE(ZD_OUT));
  czy_zderzenie czy_zderzenie_9 (.L(REG_2_3), .P(REG_3_3), .OUT(czy_zderzenie_9_out));
  czy_zderzenie czy_zderzenie_10 (.L(REG_3_3), .P(REG_0_4), .OUT(czy_zderzenie_10_out));
  czy_zderzenie czy_zderzenie_11 (.L(REG_0_4), .P(REG_1_4), .OUT(czy_zderzenie_11_out));
  czy_zderzenie czy_zderzenie_12 (.L(REG_1_4), .P(REG_2_4), .OUT(czy_zderzenie_12_out));
  zamieniacz zamieniacz_13 (.L(REG_0), .P(zamieniacz_9_l_2), .L_2(OUT_0), .P_2(OUT_1), .WYSTAPILO_ZDERZENIE(ZD_OUT));
  zamieniacz zamieniacz_14 (
    .L(REG_1_2), .P(zamieniacz_10_l_2), .L_2(OUT_1_2), .P_2(OUT_2_2), .WYSTAPILO_ZDERZENIE(ZD_OUT));
  zamieniacz zamieniacz_15 (
    .L(REG_2_3), .P(zamieniacz_11_l_2), .L_2(OUT_2_3), .P_2(OUT_3_3), .WYSTAPILO_ZDERZENIE(ZD_OUT));
  zamieniacz zamieniacz_16 (
    .L(REG_3_4), .P(zamieniacz_12_l_2), .L_2(OUT_3_4), .P_2(OUT_0_5), .WYSTAPILO_ZDERZENIE(ZD_OUT));
  or or_3 (or_3_out, czy_zderzenie_9_out, czy_zderzenie_10_out, czy_zderzenie_11_out, czy_zderzenie_12_out);
  czy_zderzenie czy_zderzenie_13 (.L(REG_3_4), .P(REG_0_5), .OUT(czy_zderzenie_13_out));
  czy_zderzenie czy_zderzenie_14 (.L(REG_0_5), .P(REG_1_5), .OUT(czy_zderzenie_14_out));
  czy_zderzenie czy_zderzenie_15 (.L(REG_1_5), .P(REG_2_5), .OUT(czy_zderzenie_15_out));
  czy_zderzenie czy_zderzenie_16 (.L(REG_2_5), .P(REG_3_5), .OUT(czy_zderzenie_16_out));
  or or_4 (or_4_out, czy_zderzenie_13_out, czy_zderzenie_14_out, czy_zderzenie_15_out, czy_zderzenie_16_out);
  or or_5 (ZD_OUT, or_4_out, or_3_out, or_2_out, or_1_out);

  // Other names for the same wires on the sheet: _0[1:0] = REG_0; _1[1:0] = REG_1; _2[1:0] = REG_2; _3[1:0] = REG_3;
  //   _4[1:0] = REG_0_2; _5[1:0] = REG_1_2; _6[1:0] = REG_2_2; _7[1:0] = REG_3_2; _8[1:0] = REG_0_3;
  //   _9[1:0] = REG_1_3; _10[1:0] = REG_2_3; _11[1:0] = REG_3_3; _12[1:0] = REG_0_4; _13[1:0] = REG_1_4;
  //   _14[1:0] = REG_2_4; _15[1:0] = REG_3_4; _16[1:0] = REG_0_5; _17[1:0] = REG_1_5; _18[1:0] = REG_2_5;
  //   _19[1:0] = REG_3_5; OUT_4[1:0] = OUT_0_2; OUT_5[1:0] = OUT_1_2; OUT_6[1:0] = OUT_2_2; OUT_7[1:0] = OUT_3_2;
  //   OUT_8[1:0] = OUT_0_3; OUT_9[1:0] = OUT_1_3; OUT_10[1:0] = OUT_2_3; OUT_11[1:0] = OUT_3_3; OUT_12[1:0] = OUT_0_4;
  //   OUT_13[1:0] = OUT_1_4; OUT_14[1:0] = OUT_2_4; OUT_15[1:0] = OUT_3_4; OUT_16[1:0] = OUT_0_5;
  //   OUT_17[1:0] = OUT_1_5; OUT_18[1:0] = OUT_2_5; OUT_19[1:0] = OUT_3_5; ZD = ZD_OUT

  // Notes on the sheet:
  //   wiersz 1
  //   wiersz 2
  //   wiersz 3
  //   wiersz 4
  //   ZDERZENIE
  //   wiersz 1
  //   wiersz 2
  //   wiersz 3
  //   wiersz 4
endmodule
