// Logisim project przesuwanie.circ as structural Verilog: 1 circuit, main circuit main
module main (
  input  [6:0] A1,
  input  CLK,
  input  ENABLE,
  input  [1:0] DATA_IN,
  input  FLAGA,
  output [6:0] NOWE_A1,
  output [1:0] DATA_OUT,
  output RAM_CLK,
  output ZD,
  output [6:0] A,
  output FINISH
);

  wire and_1_out, demultiplexer_2_out1, main_2_finish, main_2_ram_clk, main_2_zd_out;
  wire [1:0] demultiplexer_3_out1, main_2_data_out, TRYB;
  wire [6:0] demultiplexer_1_out1, main_2_a;

  and and_1 (and_1_out, CLK, ENABLE);
  trybo_selektor_main main_1 (.A1(A1), .FLAGA(FLAGA), .NOWE_A1(NOWE_A1), .TRYB(TRYB));
  Demultiplexer #(.select(2), .width(7)) demultiplexer_1 (
    .out1(demultiplexer_1_out1), .in(A1), .sel(TRYB));  // open: out0, out2, out3, en
  Demultiplexer #(.select(2)) demultiplexer_2 (
    .out1(demultiplexer_2_out1), .in(and_1_out), .sel(TRYB));  // open: out0, out2, out3, en
  Demultiplexer #(.select(2), .width(2)) demultiplexer_3 (
    .out1(demultiplexer_3_out1), .in(DATA_IN), .sel(TRYB));  // open: out0, out2, out3, en
  przesuwanie_prawo_bezsciany_main main_2 (
    .A1(demultiplexer_1_out1), .DATA_IN(demultiplexer_3_out1), .CLK(demultiplexer_2_out1),
    .ZD_OUT(main_2_zd_out), .A(main_2_a), .FINISH(main_2_finish), .RAM_CLK(main_2_ram_clk),
    .DATA_OUT(main_2_data_out));
  Multiplexer #(.select(2), .width(2)) multiplexer_1 (
    .in0(main_2_data_out), .in1(main_2_data_out), .out(DATA_OUT), .sel(TRYB));  // open: in2, in3, en
  Multiplexer #(.select(2)) multiplexer_2 (.in1(main_2_ram_clk), .out(RAM_CLK), .sel(TRYB));  // open: in0, in2, in3, en
  Multiplexer #(.select(2)) multiplexer_3 (.in1(main_2_zd_out), .out(ZD), .sel(TRYB));  // open: in0, in2, in3, en
  Multiplexer #(.select(2), .width(7)) multiplexer_4 (.in1(main_2_a), .out(A), .sel(TRYB));  // open: in0, in2, in3, en
  Multiplexer #(.select(2)) multiplexer_5 (.in1(main_2_finish), .out(FINISH), .sel(TRYB));  // open: in0, in2, in3, en
endmodule
