// Logisim project testowanie.circ as structural Verilog: 1 circuit, main circuit main
module main (
  input  [6:0] A1,
  input  ENABLE,
  output [6:0] NOWE_A1,
  output \CZY_RUCH_BYŁ_ZABLOKOWANY ,
  output FINISH
);

  wire clock_1_out, keyboard_1_avail, main_1_ram_clk, main_2_flaga, main_2_flaga_2;
  wire [1:0] main_1_data_out, ram_1_data;
  wire [6:0] keyboard_1_data, main_1_a;

  Clock clock_1 (.out(clock_1_out));
  RAM #(.addrWidth(7), .dataWidth(2), .bus("separate")) ram_1 (
    .addr(main_1_a), .din(main_1_data_out), .data(ram_1_data), .clk(main_1_ram_clk));  // open: str, sel, ld, clr
  przesuwanie_main main_1 (
    .A1(A1), .CLK(clock_1_out), .ENABLE(ENABLE), .DATA_IN(ram_1_data), .FLAGA(main_2_flaga),
    .NOWE_A1(NOWE_A1), .DATA_OUT(main_1_data_out), .RAM_CLK(main_1_ram_clk), .ZD(\CZY_RUCH_BYŁ_ZABLOKOWANY ),
    .A(main_1_a), .FINISH(FINISH));
  Keyboard keyboard_1 (.clk(clock_1_out), .avail(keyboard_1_avail), .data(keyboard_1_data));  // open: re, clr
  koder_klawiatura_main main_2 (
    .wejscie_ASCI(keyboard_1_data), .CLK(keyboard_1_avail), .RESET(FINISH), .FLAGA(main_2_flaga),
    .FLAGA_2(main_2_flaga_2));  // open: RESET_2, TRWAJACA_AKCJA

  // Notes on the sheet:
  //   JEDNAK DO E/Q zrobic osobne K!, bo osobne finishe je powinny resetowac
  //   do rotacji na przyszlosc
endmodule
