// Logisim project koder_klawiatura.circ as structural Verilog: 1 circuit, main circuit main
module main (
  input  [6:0] wejscie_ASCI,
  input  CLK,
  input  RESET,
  output FLAGA,
  output FLAGA_2
);

  wire [1:0] comparator_1_eq, comparator_3_eq;
  wire [6:0] register_1_q;

  Register #(.width(7)) register_1 (.D(wejscie_ASCI), .Q(register_1_q), .clk(CLK), .clr(RESET));  // open: en
  Comparator #(.width(7), .mode("unsigned")) comparator_1 (
    .a(register_1_q), .b(7'b1100100), .eq(comparator_1_eq[0]));  // open: gt, lt
  Comparator #(.width(7), .mode("unsigned")) comparator_2 (
    .a(register_1_q), .b(7'b1100001), .eq(comparator_1_eq[1]));  // open: gt, lt
  Comparator #(.width(7), .mode("unsigned")) comparator_3 (
    .a(register_1_q), .b(7'b1110001), .eq(comparator_3_eq[0]));  // open: gt, lt
  Comparator #(.width(7), .mode("unsigned")) comparator_4 (
    .a(register_1_q), .b(7'b1100101), .eq(comparator_3_eq[1]));  // open: gt, lt
  Multiplexer #(.select(2), .disabled(0)) multiplexer_1 (
    .in0(1'b0), .in1(1'b1), .in2(1'b0), .out(FLAGA), .sel(comparator_1_eq));  // open: in3, en
  Multiplexer #(.select(2), .disabled(0)) multiplexer_2 (
    .in0(1'b0), .in1(1'b1), .in2(1'b0), .out(FLAGA_2), .sel(comparator_3_eq));  // open: in3, en

  // Notes on the sheet:
  //   q - rot lewo
  //   e - rot prawo
endmodule
