// Logisim project rotacja.circ as structural Verilog: 1 circuit, main circuit main
module main (
  input  [6:0] A1,
  input  CLK,
  input  ENABLE,
  input  [1:0] DATA_IN,
  input  FLAGA,
  output [1:0] DATA_OUT,
  output RAM_CLK,
  output ZD,
  output [6:0] A,
  output FINISH
);

  wire and_1_out, demultiplexer_2_out0, main_1_finish, main_1_ram_clk, main_1_zd_out, multiplexer_3_out;
  wire [1:0] demultiplexer_3_out0, main_1_data_out;
  wire [6:0] demultiplexer_1_out0, main_1_a;

  and and_1 (and_1_out, CLK, ENABLE);
  Demultiplexer #(.width(7)) demultiplexer_1 (.out0(demultiplexer_1_out0), .in(A1), .sel(FLAGA));  // open: out1, en
  Demultiplexer demultiplexer_2 (.out0(demultiplexer_2_out0), .in(and_1_out), .sel(FLAGA));  // open: out1, en
  Demultiplexer #(.width(2)) demultiplexer_3 (
    .out0(demultiplexer_3_out0), .in(DATA_IN), .sel(FLAGA));  // open: out1, en
  rotacja_lewo_main main_1 (
    .A1(demultiplexer_1_out0), .DATA_IN(demultiplexer_3_out0), .CLK(demultiplexer_2_out0),
    .ZD_OUT(main_1_zd_out), .A(main_1_a), .FINISH(main_1_finish), .RAM_CLK(main_1_ram_clk),
    .DATA_OUT(main_1_data_out));
  Multiplexer #(.width(2)) multiplexer_1 (.in0(main_1_data_out), .out(DATA_OUT), .sel(FLAGA));  // open: in1, en
  Multiplexer multiplexer_2 (.in0(main_1_ram_clk), .out(RAM_CLK), .sel(FLAGA));  // open: in1, en
  Multiplexer multiplexer_3 (.in0(main_1_zd_out), .out(multiplexer_3_out), .sel(FLAGA));  // open: in1, en
  Multiplexer #(.width(7)) multiplexer_4 (.in0(main_1_a), .out(A), .sel(FLAGA));  // open: in1, en
  Multiplexer multiplexer_5 (.in0(main_1_finish), .out(FINISH), .sel(FLAGA));  // open: in1, en
  and and_2 (ZD, multiplexer_3_out, FINISH);

  // Notes on the sheet:
  //   0 to lewo | 1 to prawo
endmodule
