// Logisim project generacja.circ as structural Verilog: 1 circuit, main circuit main
module main (
  input  RESET,
  input  [1:0] DATA_IN,
  input  CLK,
  input  ENABLE,
  output [6:0] A,
  output [6:0] NOWE_A1,
  output FINISH,
  output ZD_OUT,
  output [1:0] DATA_OUT,
  output RAM_CLK
);

  wire and_2_out, CLK_t, comparator_1_eq, comparator_2_eq, comparator_2_gt, comparator_2_lt, comparator_3_eq,
       comparator_4_eq, comparator_5_eq, logiczno_ustawiacz_norm_1_zd_out, or_1_out, or_2_out, register_1_q;
  wire [1:0] logiczno_ustawiacz_norm_1_out_0, logiczno_ustawiacz_norm_1_out_0_2,
       logiczno_ustawiacz_norm_1_out_0_3, logiczno_ustawiacz_norm_1_out_0_4, logiczno_ustawiacz_norm_1_out_1,
       logiczno_ustawiacz_norm_1_out_1_2, logiczno_ustawiacz_norm_1_out_1_3,
       logiczno_ustawiacz_norm_1_out_1_4, logiczno_ustawiacz_norm_1_out_2, logiczno_ustawiacz_norm_1_out_2_2,
       logiczno_ustawiacz_norm_1_out_2_3, logiczno_ustawiacz_norm_1_out_2_4, logiczno_ustawiacz_norm_1_out_3,
       logiczno_ustawiacz_norm_1_out_3_2, logiczno_ustawiacz_norm_1_out_3_3,
       logiczno_ustawiacz_norm_1_out_3_4, main_1_data_out_0, main_1_data_out_1, main_1_data_out_2,
       main_1_data_out_3, main_1_data_out_4, main_1_data_out_5, main_1_data_out_6, main_1_data_out_7,
       main_1_data_out_8, main_1_data_out_9, main_1_data_out_10, main_1_data_out_11, main_1_data_out_12,
       main_1_data_out_13, main_1_data_out_14, main_1_data_out_15;
  wire [2:0] random_1_out;
  wire [3:0] counter_3_q;
  wire [5:0] counter_2_q;
  wire [6:0] adder_1_out, counter_1_q, counter_4_q, counter_5_q, multiplier_1_out;

  and and_1 (CLK_t, CLK, ENABLE);
  Counter #(.width(7), .max('h3)) counter_1 (.Q(counter_1_q), .clk(CLK_t), .clr(RESET));  // open: load, D, count, carry
  Counter #(.width(6), .max('h1f)) counter_2 (
    .Q(counter_2_q), .clk(CLK_t), .clr(RESET));  // open: load, D, count, carry
  Counter #(.width(4), .max('hf)) counter_3 (
    .Q(counter_3_q), .clk(RAM_CLK), .clr(RESET));  // open: load, D, count, carry
  Adder #(.width(7)) adder_1 (.a(NOWE_A1), .b(counter_1_q), .out(adder_1_out));  // open: cin, cout
  Counter #(.width(7), .max('h3)) counter_4 (
    .Q(counter_4_q), .clk(comparator_1_eq), .clr(RESET));  // open: load, D, count, carry
  Comparator #(.width(7), .mode("unsigned")) comparator_1 (
    .a(counter_1_q), .b({7{1'b0}}), .eq(comparator_1_eq));  // open: gt, lt
  Counter #(.width(7), .max('h1f)) counter_5 (
    .Q(counter_5_q), .clk(CLK_t), .clr(RESET));  // open: load, D, count, carry
  Comparator #(.width(6), .mode("unsigned")) comparator_2 (
    .a(counter_2_q), .b(6'b010001), .gt(comparator_2_gt), .eq(comparator_2_eq), .lt(comparator_2_lt));
  Adder #(.width(7)) adder_2 (.a(adder_1_out), .b(multiplier_1_out), .out(A));  // open: cin, cout
  Multiplier #(.width(7)) multiplier_1 (.a(counter_4_q), .b(7'b0001000), .out(multiplier_1_out));  // open: cin, cout
  Comparator #(.width(7), .mode("unsigned")) comparator_3 (
    .a(counter_5_q), .b({7{1'b0}}), .eq(comparator_3_eq));  // open: gt, lt
  Register #(.width(1)) register_1 (.D(1'b1), .Q(register_1_q), .clk(comparator_5_eq), .clr(or_2_out));  // open: en
  Comparator #(.width(7), .mode("unsigned")) comparator_4 (
    .a(counter_5_q), .b(7'b0000001), .eq(comparator_4_eq));  // open: gt, lt
  Comparator #(.width(7), .mode("unsigned")) comparator_5 (
    .a(counter_5_q), .b(7'b0000011), .eq(comparator_5_eq));  // open: gt, lt
  and and_2 (and_2_out, comparator_2_lt, CLK_t);
  or or_1 (or_1_out, comparator_2_gt, comparator_2_eq);
  and and_3 (FINISH, comparator_3_eq, register_1_q);
  or or_2 (or_2_out, comparator_4_eq, RESET);
  and and_4 (RAM_CLK, CLK_t, or_1_out);
  MEGA_register_16_main main_1 (
    .DATA_IN(DATA_IN), .CLK(and_2_out), .DATA_OUT_0(main_1_data_out_0), .DATA_OUT_1(main_1_data_out_1),
    .DATA_OUT_2(main_1_data_out_2), .DATA_OUT_3(main_1_data_out_3), .DATA_OUT_4(main_1_data_out_4),
    .DATA_OUT_5(main_1_data_out_5), .DATA_OUT_6(main_1_data_out_6), .DATA_OUT_7(main_1_data_out_7),
    .DATA_OUT_8(main_1_data_out_8), .DATA_OUT_9(main_1_data_out_9), .DATA_OUT_10(main_1_data_out_10),
    .DATA_OUT_11(main_1_data_out_11), .DATA_OUT_12(main_1_data_out_12), .DATA_OUT_13(main_1_data_out_13),
    .DATA_OUT_14(main_1_data_out_14), .DATA_OUT_15(main_1_data_out_15), .RESET(RESET));
  logiczno_ustawiacz_norm logiczno_ustawiacz_norm_1 (
    .REG_0(main_1_data_out_0), .REG_1(main_1_data_out_1), .REG_2(main_1_data_out_2),
    .REG_3(main_1_data_out_3), .REG_0_2(main_1_data_out_4), .REG_1_2(main_1_data_out_5),
    .REG_2_2(main_1_data_out_6), .REG_3_2(main_1_data_out_7), .REG_0_3(main_1_data_out_8),
    .REG_1_3(main_1_data_out_9), .REG_2_3(main_1_data_out_10), .REG_3_3(main_1_data_out_11),
    .REG_0_4(main_1_data_out_12), .REG_1_4(main_1_data_out_13), .REG_2_4(main_1_data_out_14),
    .REG_3_4(main_1_data_out_15), .OUT_0(logiczno_ustawiacz_norm_1_out_0),
    .OUT_1(logiczno_ustawiacz_norm_1_out_1), .OUT_2(logiczno_ustawiacz_norm_1_out_2),
    .OUT_3(logiczno_ustawiacz_norm_1_out_3), .OUT_0_2(logiczno_ustawiacz_norm_1_out_0_2),
    .OUT_1_2(logiczno_ustawiacz_norm_1_out_1_2), .OUT_2_2(logiczno_ustawiacz_norm_1_out_2_2),
    .OUT_3_2(logiczno_ustawiacz_norm_1_out_3_2), .OUT_0_3(logiczno_ustawiacz_norm_1_out_0_3),
    .OUT_1_3(logiczno_ustawiacz_norm_1_out_1_3), .OUT_2_3(logiczno_ustawiacz_norm_1_out_2_3),
    .OUT_3_3(logiczno_ustawiacz_norm_1_out_3_3), .OUT_0_4(logiczno_ustawiacz_norm_1_out_0_4),
    .OUT_1_4(logiczno_ustawiacz_norm_1_out_1_4), .OUT_2_4(logiczno_ustawiacz_norm_1_out_2_4),
    .OUT_3_4(logiczno_ustawiacz_norm_1_out_3_4), .ZD_OUT(logiczno_ustawiacz_norm_1_zd_out), .RANDOM_CLK(RESET));
  Multiplexer #(.select(4), .width(2)) multiplexer_1 (
    .in0(logiczno_ustawiacz_norm_1_out_0), .in1(logiczno_ustawiacz_norm_1_out_1),
    .in2(logiczno_ustawiacz_norm_1_out_2), .in3(logiczno_ustawiacz_norm_1_out_3),
    .in4(logiczno_ustawiacz_norm_1_out_0_2), .in5(logiczno_ustawiacz_norm_1_out_1_2),
    .in6(logiczno_ustawiacz_norm_1_out_2_2), .in7(logiczno_ustawiacz_norm_1_out_3_2),
    .in8(logiczno_ustawiacz_norm_1_out_0_3), .in9(logiczno_ustawiacz_norm_1_out_1_3),
    .in10(logiczno_ustawiacz_norm_1_out_2_3), .in11(logiczno_ustawiacz_norm_1_out_3_3),
    .in12(logiczno_ustawiacz_norm_1_out_0_4), .in13(logiczno_ustawiacz_norm_1_out_1_4),
    .in14(logiczno_ustawiacz_norm_1_out_2_4), .in15(logiczno_ustawiacz_norm_1_out_3_4), .out(DATA_OUT),
    .sel(counter_3_q));  // open: en
  Random #(.width(3)) random_1 (.clk(RESET), .out(random_1_out));  // open: next, clr
  and and_5 (ZD_OUT, FINISH, logiczno_ustawiacz_norm_1_zd_out);
  Multiplexer #(.select(3), .width(7)) multiplexer_2 (
    .in0({7{1'b0}}), .in1(7'b0000001), .in2(7'b0000010), .in3(7'b0000011), .in4(7'b0000100),
    .in5(7'b0000101), .in6(7'b0000010), .in7(7'b0000011), .out(NOWE_A1), .sel(random_1_out));  // open: en

  // Other names for the same wires on the sheet: R = RESET; WYBRANE_A[6:0] = NOWE_A1

  // Notes on the sheet:
  //   tu
endmodule
