// Logisim project kwadrat.circ as structural Verilog: 1 circuit, main circuit main
module main (
  output _0,
  output _1,
  output _2,
  output _3,
  output _4,
  output _5,
  output _6,
  output _7,
  output _8,
  output _9,
  output _10,
  output _11,
  output _12,
  output _13,
  output _14,
  output _15
);


  assign _0 = 1'b0;
  assign _1 = 1'b1;
  assign _2 = 1'b1;
  assign _3 = 1'b0;
  assign _4 = 1'b0;
  assign _5 = 1'b1;
  assign _6 = 1'b1;
  assign _7 = 1'b0;
  assign _8 = 1'b0;
  assign _9 = 1'b0;
  assign _10 = 1'b0;
  assign _11 = 1'b0;
  assign _12 = 1'b0;
  assign _13 = 1'b0;
  assign _14 = 1'b0;
  assign _15 = 1'b0;
endmodule
