// Logisim project ustawiacz_generacja.circ as structural Verilog: 1 circuit, main circuit logiczno-ustawiacz_norm
module logiczno_ustawiacz_norm (
  input  [1:0] REG_0,
  input  [1:0] REG_1,
  input  [1:0] REG_2,
  input  [1:0] REG_3,
  input  [1:0] REG_0_2,
  input  [1:0] REG_1_2,
  input  [1:0] REG_2_2,
  input  [1:0] REG_3_2,
  input  [1:0] REG_0_3,
  input  [1:0] REG_1_3,
  input  [1:0] REG_2_3,
  input  [1:0] REG_3_3,
  input  [1:0] REG_0_4,
  input  [1:0] REG_1_4,
  input  [1:0] REG_2_4,
  input  [1:0] REG_3_4,
  input  RANDOM_CLK,
  output [1:0] OUT_0,
  output [1:0] OUT_1,
  output [1:0] OUT_2,
  output [1:0] OUT_3,
  output [1:0] OUT_0_2,
  output [1:0] OUT_1_2,
  output [1:0] OUT_2_2,
  output [1:0] OUT_3_2,
  output [1:0] OUT_0_3,
  output [1:0] OUT_1_3,
  output [1:0] OUT_2_3,
  output [1:0] OUT_3_3,
  output [1:0] OUT_0_4,
  output [1:0] OUT_1_4,
  output [1:0] OUT_2_4,
  output [1:0] OUT_3_4,
  output ZD_OUT
);

  wire B0, B1, B2, B3, B4, B5, B6, B7, B8, B9, B10, B11, B12, B13, B14, B15, czy_zderzenie_1_out,
       czy_zderzenie_2_out, czy_zderzenie_3_out, czy_zderzenie_4_out, czy_zderzenie_5_out,
       czy_zderzenie_6_out, czy_zderzenie_7_out, czy_zderzenie_8_out, czy_zderzenie_9_out,
       czy_zderzenie_10_out, czy_zderzenie_11_out, czy_zderzenie_12_out, czy_zderzenie_13_out,
       czy_zderzenie_14_out, czy_zderzenie_15_out, czy_zderzenie_16_out, or_1_out, or_2_out, or_3_out,
       or_4_out;

  blok_main main_1 (
    ._0(B0), ._1(B1), ._2(B2), ._3(B3), ._4(B4), ._5(B5), ._6(B6), ._7(B7), ._8(B8), ._9(B9), ._10(B10),
    ._11(B11), ._12(B12), ._13(B13), ._14(B14), ._15(B15), .RAND_CLK(RANDOM_CLK));
  Multiplexer #(.select(2), .width(2)) multiplexer_1 (
    .in0(REG_0), .in1(2'b10), .in2(REG_0), .in3(REG_0), .out(OUT_0), .sel({ZD_OUT, B0}));  // open: en
  Multiplexer #(.select(2), .width(2)) multiplexer_2 (
    .in0(REG_0_2), .in1(2'b10), .in2(REG_0_2), .in3(REG_0_2), .out(OUT_0_2), .sel({ZD_OUT, B4}));  // open: en
  Multiplexer #(.select(2), .width(2)) multiplexer_3 (
    .in0(REG_0_3), .in1(2'b10), .in2(REG_0_3), .in3(REG_0_3), .out(OUT_0_3), .sel({ZD_OUT, B8}));  // open: en
  Multiplexer #(.select(2), .width(2)) multiplexer_4 (
    .in0(REG_0_4), .in1(2'b10), .in2(REG_0_4), .in3(REG_0_4), .out(OUT_0_4), .sel({ZD_OUT, B12}));  // open: en
  Multiplexer #(.select(2), .width(2)) multiplexer_5 (
    .in0(REG_1), .in1(2'b10), .in2(REG_1), .in3(REG_1), .out(OUT_1), .sel({ZD_OUT, B1}));  // open: en
  Multiplexer #(.select(2), .width(2)) multiplexer_6 (
    .in0(REG_1_2), .in1(2'b10), .in2(REG_1_2), .in3(REG_1_2), .out(OUT_1_2), .sel({ZD_OUT, B5}));  // open: en
  Multiplexer #(.select(2), .width(2)) multiplexer_7 (
    .in0(REG_1_3), .in1(2'b10), .in2(REG_1_3), .in3(REG_1_3), .out(OUT_1_3), .sel({ZD_OUT, B9}));  // open: en
  Multiplexer #(.select(2), .width(2)) multiplexer_8 (
    .in0(REG_1_4), .in1(2'b10), .in2(REG_1_4), .in3(REG_1_4), .out(OUT_1_4), .sel({ZD_OUT, B13}));  // open: en
  czy_zderzenie czy_zderzenie_1 (.N(B8), .S(REG_0_3), .OUT(czy_zderzenie_1_out));
  czy_zderzenie czy_zderzenie_2 (.N(B9), .S(REG_1_3), .OUT(czy_zderzenie_2_out));
  czy_zderzenie czy_zderzenie_3 (.N(B10), .S(REG_2_3), .OUT(czy_zderzenie_3_out));
  czy_zderzenie czy_zderzenie_4 (.N(B11), .S(REG_3_3), .OUT(czy_zderzenie_4_out));
  czy_zderzenie czy_zderzenie_5 (.N(B12), .S(REG_0_4), .OUT(czy_zderzenie_5_out));
  czy_zderzenie czy_zderzenie_6 (.N(B13), .S(REG_1_4), .OUT(czy_zderzenie_6_out));
  czy_zderzenie czy_zderzenie_7 (.N(B14), .S(REG_2_4), .OUT(czy_zderzenie_7_out));
  czy_zderzenie czy_zderzenie_8 (.N(B15), .S(REG_3_4), .OUT(czy_zderzenie_8_out));
  or or_1 (or_1_out, czy_zderzenie_1_out, czy_zderzenie_2_out, czy_zderzenie_3_out, czy_zderzenie_4_out);
  or or_2 (or_2_out, czy_zderzenie_5_out, czy_zderzenie_6_out, czy_zderzenie_7_out, czy_zderzenie_8_out);
  Multiplexer #(.select(2), .width(2)) multiplexer_9 (
    .in0(REG_2), .in1(2'b10), .in2(REG_2), .in3(REG_2), .out(OUT_2), .sel({ZD_OUT, B2}));  // open: en
  Multiplexer #(.select(2), .width(2)) multiplexer_10 (
    .in0(REG_2_2), .in1(2'b10), .in2(REG_2_2), .in3(REG_2_2), .out(OUT_2_2), .sel({ZD_OUT, B6}));  // open: en
  Multiplexer #(.select(2), .width(2)) multiplexer_11 (
    .in0(REG_2_3), .in1(2'b10), .in2(REG_2_3), .in3(REG_2_3), .out(OUT_2_3), .sel({ZD_OUT, B10}));  // open: en
  Multiplexer #(.select(2), .width(2)) multiplexer_12 (
    .in0(REG_2_4), .in1(2'b10), .in2(REG_2_4), .in3(REG_2_4), .out(OUT_2_4), .sel({ZD_OUT, B14}));  // open: en
  czy_zderzenie czy_zderzenie_9 (.N(B4), .S(REG_0_2), .OUT(czy_zderzenie_9_out));
  czy_zderzenie czy_zderzenie_10 (.N(B5), .S(REG_1_2), .OUT(czy_zderzenie_10_out));
  czy_zderzenie czy_zderzenie_11 (.N(B6), .S(REG_2_2), .OUT(czy_zderzenie_11_out));
  czy_zderzenie czy_zderzenie_12 (.N(B7), .S(REG_3_2), .OUT(czy_zderzenie_12_out));
  or or_3 (or_3_out, czy_zderzenie_9_out, czy_zderzenie_10_out, czy_zderzenie_11_out, czy_zderzenie_12_out);
  Multiplexer #(.select(2), .width(2)) multiplexer_13 (
    .in0(REG_3), .in1(2'b10), .in2(REG_3), .in3(REG_3), .out(OUT_3), .sel({ZD_OUT, B3}));  // open: en
  Multiplexer #(.select(2), .width(2)) multiplexer_14 (
    .in0(REG_3_2), .in1(2'b10), .in2(REG_3_2), .in3(REG_3_2), .out(OUT_3_2), .sel({ZD_OUT, B7}));  // open: en
  Multiplexer #(.select(2), .width(2)) multiplexer_15 (
    .in0(REG_3_3), .in1(2'b10), .in2(REG_3_3), .in3(REG_3_3), .out(OUT_3_3), .sel({ZD_OUT, B11}));  // open: en
  Multiplexer #(.select(2), .width(2)) multiplexer_16 (
    .in0(REG_3_4), .in1(2'b10), .in2(REG_3_4), .in3(REG_3_4), .out(OUT_3_4), .sel({ZD_OUT, B15}));  // open: en
  czy_zderzenie czy_zderzenie_13 (.N(B0), .S(REG_0), .OUT(czy_zderzenie_13_out));
  czy_zderzenie czy_zderzenie_14 (.N(B1), .S(REG_1), .OUT(czy_zderzenie_14_out));
  czy_zderzenie czy_zderzenie_15 (.N(B2), .S(REG_2), .OUT(czy_zderzenie_15_out));
  czy_zderzenie czy_zderzenie_16 (.N(B3), .S(REG_3), .OUT(czy_zderzenie_16_out));
  or or_4 (or_4_out, czy_zderzenie_13_out, czy_zderzenie_14_out, czy_zderzenie_15_out, czy_zderzenie_16_out);
  or or_5 (ZD_OUT, or_4_out, or_3_out, or_1_out, or_2_out);

  // Other names for the same wires on the sheet: ZD = ZD_OUT; _0[1:0] = REG_0; _1[1:0] = REG_1; _2[1:0] = REG_2;
  //   _3[1:0] = REG_3; _4[1:0] = REG_0_2; _5[1:0] = REG_1_2; _6[1:0] = REG_2_2; _7[1:0] = REG_3_2; _8[1:0] = REG_0_3;
  //   _9[1:0] = REG_1_3; _10[1:0] = REG_2_3; _11[1:0] = REG_3_3; _12[1:0] = REG_0_4; _13[1:0] = REG_1_4;
  //   _14[1:0] = REG_2_4; _15[1:0] = REG_3_4; OUT_4[1:0] = OUT_0_2; OUT_5[1:0] = OUT_1_2; OUT_6[1:0] = OUT_2_2;
  //   OUT_7[1:0] = OUT_3_2; OUT_8[1:0] = OUT_0_3; OUT_9[1:0] = OUT_1_3; OUT_10[1:0] = OUT_2_3; OUT_11[1:0] = OUT_3_3;
  //   OUT_12[1:0] = OUT_0_4; OUT_13[1:0] = OUT_1_4; OUT_14[1:0] = OUT_2_4; OUT_15[1:0] = OUT_3_4

  // Notes on the sheet:
  //   ZDERZENIE
endmodule
