// Logisim project kwadrat.circ as structural Verilog: 1 circuit, main circuit main
module main (
  output [1:0] _0,
  output [1:0] _1,
  output [1:0] _2,
  output [1:0] _3,
  output [1:0] _4,
  output [1:0] _5,
  output [1:0] _6,
  output [1:0] _7,
  output [1:0] _8,
  output [1:0] _9,
  output [1:0] _10,
  output [1:0] _11,
  output [1:0] _12,
  output [1:0] _13,
  output [1:0] _14,
  output [1:0] _15
);


  assign _0 = 2'b00;
  assign _1 = 2'b10;
  assign _2 = 2'b10;
  assign _3 = 2'b00;
  assign _4 = 2'b00;
  assign _5 = 2'b10;
  assign _6 = 2'b10;
  assign _7 = 2'b00;
  assign _8 = 2'b00;
  assign _9 = 2'b00;
  assign _10 = 2'b00;
  assign _11 = 2'b00;
  assign _12 = 2'b00;
  assign _13 = 2'b00;
  assign _14 = 2'b00;
  assign _15 = 2'b00;
endmodule
