// Logisim project ustawiacz_generacja.circ as structural Verilog: 1 circuit, main circuit logiczno-ustawiacz_norm
module logiczno_ustawiacz_norm (
  input  [1:0] REG_0,
  input  [1:0] REG_1,
  input  [1:0] REG_2,
  input  [1:0] REG_3,
  input  [1:0] REG_0_2,
  input  [1:0] REG_1_2,
  input  [1:0] REG_2_2,
  input  [1:0] REG_3_2,
  input  [1:0] REG_0_3,
  input  [1:0] REG_1_3,
  input  [1:0] REG_2_3,
  input  [1:0] REG_3_3,
  input  [1:0] REG_0_4,
  input  [1:0] REG_1_4,
  input  [1:0] REG_2_4,
  input  [1:0] REG_3_4,
  input  RANDOM_CLK,
  output [1:0] OUT_0,
  output [1:0] OUT_1,
  output [1:0] OUT_2,
  output [1:0] OUT_3,
  output [1:0] OUT_0_2,
  output [1:0] OUT_1_2,
  output [1:0] OUT_2_2,
  output [1:0] OUT_3_2,
  output [1:0] OUT_0_3,
  output [1:0] OUT_1_3,
  output [1:0] OUT_2_3,
  output [1:0] OUT_3_3,
  output [1:0] OUT_0_4,
  output [1:0] OUT_1_4,
  output [1:0] OUT_2_4,
  output [1:0] OUT_3_4,
  output ZD_OUT
);

  wire czy_zderzenie_1_out, czy_zderzenie_2_out, czy_zderzenie_3_out, czy_zderzenie_4_out,
       czy_zderzenie_5_out, czy_zderzenie_6_out, czy_zderzenie_7_out, czy_zderzenie_8_out,
       czy_zderzenie_9_out, czy_zderzenie_10_out, czy_zderzenie_11_out, czy_zderzenie_12_out,
       czy_zderzenie_13_out, czy_zderzenie_14_out, czy_zderzenie_15_out, czy_zderzenie_16_out, or_1_out,
       or_3_out, or_4_out, or_5_out;
  wire [1:0] A0, A1, A2, A3, A4, A5, A6, A7, A8, A9, A10, A11, A12, A13, A14, A15, P0, P1, P2, P3, P4, P5,
       P6, P7, P8, P9, P10, P11, P12, P13, P14, P15;

  kwadrat_main main_1 (
    ._0(A0), ._1(A1), ._2(A2), ._3(A3), ._4(A4), ._5(A5), ._6(A6), ._7(A7), ._8(A8), ._9(A9), ._10(A10),
    ._11(A11), ._12(A12), ._13(A13), ._14(A14), ._15(A15));
  Random #(.width(2)) random_1 (.clk(RANDOM_CLK));  // open: next, out, clr
  Multiplexer #(.select(2), .width(2)) multiplexer_1 (.in0(A0), .out(P0), .sel(2'b00));  // open: in1, in2, in3, en
  Multiplexer #(.select(2), .width(2)) multiplexer_2 (.in0(A2), .out(P2), .sel(2'b00));  // open: in1, in2, in3, en
  Multiplexer #(.select(2), .width(2)) multiplexer_3 (.in0(A4), .out(P4), .sel(2'b00));  // open: in1, in2, in3, en
  Multiplexer #(.select(2), .width(2)) multiplexer_4 (.in0(A6), .out(P6), .sel(2'b00));  // open: in1, in2, in3, en
  Multiplexer #(.select(2), .width(2)) multiplexer_5 (.in0(A8), .out(P8), .sel(2'b00));  // open: in1, in2, in3, en
  Multiplexer #(.select(2), .width(2)) multiplexer_6 (.in0(A10), .out(P10), .sel(2'b00));  // open: in1, in2, in3, en
  Multiplexer #(.select(2), .width(2)) multiplexer_7 (.in0(A12), .out(P12), .sel(2'b00));  // open: in1, in2, in3, en
  Multiplexer #(.select(2), .width(2)) multiplexer_8 (.in0(A14), .out(P14), .sel(2'b00));  // open: in1, in2, in3, en
  Multiplexer #(.width(2)) multiplexer_9 (.in1(REG_0), .out(OUT_0), .sel(ZD_OUT));  // open: in0, en
  Multiplexer #(.select(2), .width(2)) multiplexer_10 (.in0(A1), .out(P1), .sel(2'b00));  // open: in1, in2, in3, en
  Multiplexer #(.select(2), .width(2)) multiplexer_11 (.in0(A3), .out(P3), .sel(2'b00));  // open: in1, in2, in3, en
  Multiplexer #(.select(2), .width(2)) multiplexer_12 (.in0(A5), .out(P5), .sel(2'b00));  // open: in1, in2, in3, en
  Multiplexer #(.select(2), .width(2)) multiplexer_13 (.in0(A7), .out(P7), .sel(2'b00));  // open: in1, in2, in3, en
  Multiplexer #(.select(2), .width(2)) multiplexer_14 (.in0(A9), .out(P9), .sel(2'b00));  // open: in1, in2, in3, en
  Multiplexer #(.select(2), .width(2)) multiplexer_15 (.in0(A11), .out(P11), .sel(2'b00));  // open: in1, in2, in3, en
  Multiplexer #(.select(2), .width(2)) multiplexer_16 (.in0(A13), .out(P13), .sel(2'b00));  // open: in1, in2, in3, en
  Multiplexer #(.select(2), .width(2)) multiplexer_17 (.in0(A15), .out(P15), .sel(2'b00));  // open: in1, in2, in3, en
  czy_zderzenie czy_zderzenie_1 (.N(P0), .S(REG_0), .OUT(czy_zderzenie_1_out));
  czy_zderzenie czy_zderzenie_2 (.N(P1), .S(REG_1), .OUT(czy_zderzenie_2_out));
  czy_zderzenie czy_zderzenie_3 (.N(P2), .S(REG_2), .OUT(czy_zderzenie_3_out));
  czy_zderzenie czy_zderzenie_4 (.N(P3), .S(REG_3), .OUT(czy_zderzenie_4_out));
  or or_1 (or_1_out, czy_zderzenie_1_out, czy_zderzenie_2_out, czy_zderzenie_3_out, czy_zderzenie_4_out);
  czy_zderzenie czy_zderzenie_5 (.N(P4), .S(REG_0_2), .OUT(czy_zderzenie_5_out));
  czy_zderzenie czy_zderzenie_6 (.N(P5), .S(REG_1_2), .OUT(czy_zderzenie_6_out));
  czy_zderzenie czy_zderzenie_7 (.N(P6), .S(REG_2_2), .OUT(czy_zderzenie_7_out));
  czy_zderzenie czy_zderzenie_8 (.N(P7), .S(REG_3_2), .OUT(czy_zderzenie_8_out));
  czy_zderzenie czy_zderzenie_9 (.N(P8), .S(REG_0_3), .OUT(czy_zderzenie_9_out));
  czy_zderzenie czy_zderzenie_10 (.N(P9), .S(REG_1_3), .OUT(czy_zderzenie_10_out));
  czy_zderzenie czy_zderzenie_11 (.N(P10), .S(REG_2_3), .OUT(czy_zderzenie_11_out));
  czy_zderzenie czy_zderzenie_12 (.N(P11), .S(REG_3_3), .OUT(czy_zderzenie_12_out));
  czy_zderzenie czy_zderzenie_13 (.N(P12), .S(REG_0_4), .OUT(czy_zderzenie_13_out));
  czy_zderzenie czy_zderzenie_14 (.N(P13), .S(REG_1_4), .OUT(czy_zderzenie_14_out));
  czy_zderzenie czy_zderzenie_15 (.N(P14), .S(REG_2_4), .OUT(czy_zderzenie_15_out));
  czy_zderzenie czy_zderzenie_16 (.N(P15), .S(REG_3_4), .OUT(czy_zderzenie_16_out));
  or or_2 (ZD_OUT, or_1_out, or_3_out, or_4_out, or_5_out);
  or or_3 (or_3_out, czy_zderzenie_5_out, czy_zderzenie_6_out, czy_zderzenie_7_out, czy_zderzenie_8_out);
  or or_4 (or_4_out, czy_zderzenie_9_out, czy_zderzenie_10_out, czy_zderzenie_11_out, czy_zderzenie_12_out);
  or or_5 (or_5_out, czy_zderzenie_13_out, czy_zderzenie_14_out, czy_zderzenie_15_out, czy_zderzenie_16_out);

  // Other names for the same wires on the sheet: _0[1:0] = REG_0; _1[1:0] = REG_1; _2[1:0] = REG_2; _3[1:0] = REG_3;
  //   _4[1:0] = REG_0_2; _5[1:0] = REG_1_2; _6[1:0] = REG_2_2; _7[1:0] = REG_3_2; _8[1:0] = REG_0_3;
  //   _9[1:0] = REG_1_3; _10[1:0] = REG_2_3; _11[1:0] = REG_3_3; _12[1:0] = REG_0_4; _13[1:0] = REG_1_4;
  //   _14[1:0] = REG_2_4; _15[1:0] = REG_3_4; OUT_4[1:0] = OUT_0_2; OUT_5[1:0] = OUT_1_2; OUT_6[1:0] = OUT_2_2;
  //   OUT_7[1:0] = OUT_3_2; OUT_8[1:0] = OUT_0_3; OUT_9[1:0] = OUT_1_3; OUT_10[1:0] = OUT_2_3; OUT_11[1:0] = OUT_3_3;
  //   OUT_12[1:0] = OUT_0_4; OUT_13[1:0] = OUT_1_4; OUT_14[1:0] = OUT_2_4; OUT_15[1:0] = OUT_3_4; ZD = ZD_OUT

  // Notes on the sheet:
  //   ZDERZENIE
endmodule
