// Logisim project kaskader_8bit.circ as structural Verilog: 1 circuit, main circuit main
module main (
  input  [1:0] DATA,
  input  CLK,
  input  \PODŁOGA ,
  output [1:0] Q6,
  output [1:0] Q4,
  output [1:0] Q5,
  output [1:0] Q6_2,
  output [1:0] Q3,
  output [1:0] Q0,
  output [1:0] Q2,
  output [1:0] Q1
);

  wire [1:0] main_1_wyjscie, main_2_wyjscie, main_3_wyjscie, main_4_wyjscie, main_5_wyjscie, main_6_wyjscie,
       main_7_wyjscie, main_8_wyjscie;

  kaskader_1bit_main main_1 (.DATA_INPUT(DATA), .CLOCK(CLK), .WYJSCIE(main_1_wyjscie), .KTORY_W_KOLEJNOSCI(3'b000));
  kaskader_1bit_main main_2 (.DATA_INPUT(DATA), .CLOCK(CLK), .WYJSCIE(main_2_wyjscie), .KTORY_W_KOLEJNOSCI(3'b001));
  Multiplexer #(.width(2)) multiplexer_1 (.in0(main_1_wyjscie), .in1(2'b10), .out(Q0), .sel(\PODŁOGA ));  // open: en
  kaskader_1bit_main main_3 (.DATA_INPUT(DATA), .CLOCK(CLK), .WYJSCIE(main_3_wyjscie), .KTORY_W_KOLEJNOSCI(3'b010));
  Multiplexer #(.width(2)) multiplexer_2 (.in0(main_2_wyjscie), .in1(2'b10), .out(Q1), .sel(\PODŁOGA ));  // open: en
  kaskader_1bit_main main_4 (.DATA_INPUT(DATA), .CLOCK(CLK), .WYJSCIE(main_4_wyjscie), .KTORY_W_KOLEJNOSCI(3'b011));
  Multiplexer #(.width(2)) multiplexer_3 (.in0(main_3_wyjscie), .in1(2'b10), .out(Q2), .sel(\PODŁOGA ));  // open: en
  Multiplexer #(.width(2)) multiplexer_4 (.in0(main_4_wyjscie), .in1(2'b10), .out(Q3), .sel(\PODŁOGA ));  // open: en
  kaskader_1bit_main main_5 (.DATA_INPUT(DATA), .CLOCK(CLK), .WYJSCIE(main_5_wyjscie), .KTORY_W_KOLEJNOSCI(3'b100));
  Multiplexer #(.width(2)) multiplexer_5 (.in0(main_5_wyjscie), .in1(2'b10), .out(Q4), .sel(\PODŁOGA ));  // open: en
  kaskader_1bit_main main_6 (.DATA_INPUT(DATA), .CLOCK(CLK), .WYJSCIE(main_6_wyjscie), .KTORY_W_KOLEJNOSCI(3'b101));
  Multiplexer #(.width(2)) multiplexer_6 (.in0(main_6_wyjscie), .in1(2'b10), .out(Q5), .sel(\PODŁOGA ));  // open: en
  kaskader_1bit_main main_7 (.DATA_INPUT(DATA), .CLOCK(CLK), .WYJSCIE(main_7_wyjscie), .KTORY_W_KOLEJNOSCI(3'b110));
  Multiplexer #(.width(2)) multiplexer_7 (.in0(main_8_wyjscie), .in1(2'b10), .out(Q6), .sel(\PODŁOGA ));  // open: en
  Multiplexer #(.width(2)) multiplexer_8 (.in0(main_7_wyjscie), .in1(2'b10), .out(Q6_2), .sel(\PODŁOGA ));  // open: en
  kaskader_1bit_main main_8 (.DATA_INPUT(DATA), .CLOCK(CLK), .WYJSCIE(main_8_wyjscie), .KTORY_W_KOLEJNOSCI(3'b111));
endmodule
