// Logisim project pamiec.circ as structural Verilog: 1 circuit, main circuit main
module main (
  input  [6:0] GPU_ADRES,
  input  CLOCK,
  output [1:0] WYJSCIE
);

  wire [1:0] main_1_p2, main_1_p3, main_1_p4, main_1_p5, main_1_p6, main_1_p7, main_1_p9, main_1_p10,
       multiplexer_1_out;
  wire [2:0] counter_1_q;

  RAM #(.addrWidth(7), .dataWidth(2), .bus("separate")) ram_1 (
    .addr(GPU_ADRES), .data(WYJSCIE));  // open: din, str, sel, clk, ld, clr
  // kaskader_8bit_main main_1: pin names not known; wires that end beside it: WYJSCIE, main_1_p2, main_1_p3, main_1_p4, main_1_p5, main_1_p6, main_1_p7, CLOCK, main_1_p9, main_1_p10
  Counter #(.width(3), .max('h7)) counter_1 (.Q(counter_1_q), .clk(CLOCK));  // open: load, D, count, carry, clr
  Multiplexer #(.select(3), .width(2)) multiplexer_1 (
    .in0(main_1_p2), .in1(main_1_p3), .in2(main_1_p4), .in3(main_1_p5), .in4(main_1_p6), .in5(main_1_p7),
    .in6(main_1_p9), .in7(main_1_p10), .out(multiplexer_1_out), .sel(counter_1_q));  // open: en
  \porównywacz_v1_dzialajace_main  main_2 (
    .BLOK_WYZEJ_WARTOSC(multiplexer_1_out), .BLOK_NIZEJ_WARTOSC(WYJSCIE));  // open: A, B, C, C_2

  // Notes on the sheet:
  //   PAMIEc ktora na adres ma 1 wyzej niz to co w GPU adress i tam ustawiajaca to co ma sie ustawic
  //   rozwazyc wprowadzenie czwartego stanu puste-w sensie nie nadpisuj w glownej pamieci
  //   chociaz mozliwe ze nie bedzie potrzebne, jesli bedzie poprawnie przeiterowywac
  //   TODO ZAPIS POCZĄTKOWY NA PAMIĘĆ
  //   nastepnie gdy obiekt przeiteruje do tego miejsca to ustawiajaca w glownej pamieci to co ma
  //   TODO ZAPISYWANIE W RAM
  //   ZALEZNIE OD STANU
endmodule
