// Logisim project 7bit comparator.circ as structural Verilog: 1 circuit, main circuit 7bit comparator
module _7bit_comparator (
  input  [6:0] gen_adress,
  input  [6:0] game_adress,
  output out_3,
  output out_4,
  output out_5
);

  wire main_1_out_4, main_1_out_5, main_1_out_6, main_2_out_4, main_2_out_5, main_2_out_6, main_3_out_4,
       main_3_out_5, main_3_out_6, main_4_out_4, main_4_out_5, main_4_out_6, main_5_out_4, main_5_out_5,
       main_5_out_6, main_6_out_4, main_6_out_5, main_6_out_6, main_7_out_4, main_7_out_6;

  _1bitcomp_main main_1 (
    .in_3(1'b1), .B(game_adress[6]), .A(gen_adress[6]), .out_4(main_1_out_4), .out_5(main_1_out_5),
    .out_6(main_1_out_6));
  _1bitcomp_main main_2 (
    .in_3(main_1_out_5), .B(game_adress[5]), .A(gen_adress[5]), .out_4(main_2_out_4), .out_5(main_2_out_5),
    .out_6(main_2_out_6));
  _1bitcomp_main main_3 (
    .in_3(main_2_out_5), .B(game_adress[4]), .A(gen_adress[4]), .out_4(main_3_out_4), .out_5(main_3_out_5),
    .out_6(main_3_out_6));
  _1bitcomp_main main_4 (
    .in_3(main_3_out_5), .B(game_adress[3]), .A(gen_adress[3]), .out_4(main_4_out_4), .out_5(main_4_out_5),
    .out_6(main_4_out_6));
  _1bitcomp_main main_5 (
    .in_3(main_4_out_5), .B(game_adress[2]), .A(gen_adress[2]), .out_4(main_5_out_4), .out_5(main_5_out_5),
    .out_6(main_5_out_6));
  _1bitcomp_main main_6 (
    .in_3(main_5_out_5), .B(game_adress[1]), .A(gen_adress[1]), .out_4(main_6_out_4), .out_5(main_6_out_5),
    .out_6(main_6_out_6));
  _1bitcomp_main main_7 (
    .in_3(main_6_out_5), .B(game_adress[0]), .A(gen_adress[0]), .out_4(main_7_out_4), .out_5(out_4),
    .out_6(main_7_out_6));
  nand nand_1 (out_3, ~main_1_out_4, ~main_2_out_4, ~main_3_out_4, ~main_4_out_4, ~main_5_out_4, ~main_6_out_4, ~main_7_out_4);  // NAND_Gate
  nand nand_2 (out_5, ~main_7_out_6, ~main_6_out_6, ~main_5_out_6, ~main_4_out_6, ~main_3_out_6, ~main_2_out_6, ~main_1_out_6);  // NAND_Gate
endmodule
