// Logisim project Block randomizer.circ as structural Verilog: 1 circuit, main circuit BLC RAND
module BLC_RAND (
  input  CLK,
  input  START,
  input  [1:0] CURRENT_GAME_STATE,
  output [6:0] OUT_A,
  output [1:0] OUT_D,
  output GAME_OVER,
  output OUT_B
);

  wire controlled_buffer_1_out, controlled_buffer_3_out, controlled_buffer_4_out, controlled_buffer_5_out,
       controlled_buffer_6_out, controlled_buffer_17_out, controlled_buffer_23_out, controlled_buffer_32_out,
       counter_1_carry, counter_2_carry, counter_3_carry, counter_5_carry, main_1_a_b_2, main_2_a_b_2,
       main_3_a_b_2, main_4_a_b_2, main_8_a_b_2, main_10_a_b_2, not_1_out, not_2_out, not_3_out, not_4_out,
       not_5_out, not_6_out, not_7_out, not_8_out, not_9_out, not_10_out, not_11_out, not_12_out, not_13_out,
       not_14_out, not_15_out, pull_resistor_1_node, pull_resistor_9_node, pull_resistor_18_node;
  wire [1:0] controlled_buffer_9_out, controlled_buffer_26_out, controlled_buffer_29_out, counter_4_q,
       counter_6_q, main_5_out_4, main_6_out_4, main_7_out_4, n2x2_block_1_out_4, pull_resistor_22_node,
       rand_1_out;
  wire [6:0] controlled_buffer_7_out, controlled_buffer_12_out, controlled_buffer_18_out, counter_3_q,
       counter_5_q, main_5_out_3, main_6_out_3, main_7_out_3, n2x2_block_1_out_3, pull_resistor_14_node;

  Pull_Resistor pull_resistor_1 (.node(pull_resistor_1_node));
  Counter #(.width(1), .max('h1), .ongoal("stay")) counter_1 (
    .carry(counter_1_carry), .clk(counter_2_carry), .clr(not_2_out));  // open: load, D, count, Q
  not not_1 (not_1_out, counter_1_carry);
  Counter #(.width(4), .max('hf), .trigger("falling")) counter_2 (
    .carry(counter_2_carry), .clk(controlled_buffer_1_out), .clr(not_2_out));  // open: load, D, count, Q
  assign controlled_buffer_1_out = not_1_out ? controlled_buffer_3_out : 1'bz;  // Controlled_Buffer controlled_buffer_1
  Pull_Resistor pull_resistor_2 (.node(controlled_buffer_1_out));
  assign pull_resistor_1_node = START ? CLK : 1'bz;  // Controlled_Buffer controlled_buffer_2
  assign controlled_buffer_3_out = main_8_a_b_2 ? pull_resistor_1_node : 1'bz;  // Controlled_Buffer controlled_buffer_3
  Pull_Resistor pull_resistor_3 (.node(controlled_buffer_3_out));
  not not_2 (not_2_out, START);
  assign controlled_buffer_4_out = not_3_out ? controlled_buffer_3_out : 1'bz;  // Controlled_Buffer controlled_buffer_4
  not not_3 (not_3_out, counter_1_carry);
  Pull_Resistor pull_resistor_4 (.node(controlled_buffer_4_out));
  RAND rand_1 (.CLK(counter_2_carry), .OUT(rand_1_out));
  assign controlled_buffer_5_out = counter_1_carry ? CLK : 1'bz;  // Controlled_Buffer controlled_buffer_5
  Pull_Resistor pull_resistor_5 (.node(controlled_buffer_5_out));
  assign controlled_buffer_6_out = not_5_out ? CLK : 1'bz;  // Controlled_Buffer controlled_buffer_6
  Pull_Resistor pull_resistor_6 (.node(controlled_buffer_6_out));
  _2bit_comparator_main main_1 (.in_1(2'b00), .in_2(rand_1_out), .A_B_2(main_1_a_b_2));  // open: A_B, A_B_3
  _2bit_comparator_main main_2 (.in_1(2'b01), .in_2(rand_1_out), .A_B_2(main_2_a_b_2));  // open: A_B, A_B_3
  _2bit_comparator_main main_3 (.in_1(2'b10), .in_2(rand_1_out), .A_B_2(main_3_a_b_2));  // open: A_B, A_B_3
  _2bit_comparator_main main_4 (.in_1(2'b11), .in_2(rand_1_out), .A_B_2(main_4_a_b_2));  // open: A_B, A_B_3
  Counter #(.width(7), .max('h20)) counter_3 (
    .Q(counter_3_q), .carry(counter_3_carry), .clk(controlled_buffer_5_out), .clr(not_2_out));  // open: load, D, count
  Counter #(.width(2), .max('h2), .trigger("falling")) counter_4 (
    .Q(counter_4_q), .clk(counter_3_carry), .clr(not_2_out));  // open: load, D, count, carry
  _1x4_Block_main main_5 (
    .START_GEN(main_1_a_b_2), .CLK(controlled_buffer_4_out), .out_3(main_5_out_3), .out_4(main_5_out_4));  // open: out_5
  _2x2_Block u_2x2_block_1 (
    .in_1(controlled_buffer_4_out), .in_2(main_2_a_b_2), .out_3(n2x2_block_1_out_3),
    .out_4(n2x2_block_1_out_4));  // open: out_5
  T_Block_main main_6 (
    .START_GEN(main_3_a_b_2), .CLK(controlled_buffer_4_out), .out_3(main_6_out_3), .out_4(main_6_out_4));  // open: out_5
  L_Block_main main_7 (
    .START_GEN(main_4_a_b_2), .CLK(controlled_buffer_4_out), .out_3(main_7_out_3), .out_4(main_7_out_4));  // open: out_5
  Counter #(.width(7), .max('h20), .trigger("falling")) counter_5 (
    .Q(counter_5_q), .carry(counter_5_carry), .clk(controlled_buffer_6_out), .clr(not_2_out));  // open: load, D, count
  Counter #(.width(2), .max('h2), .trigger("falling")) counter_6 (
    .Q(counter_6_q), .clk(counter_5_carry), .clr(not_2_out));  // open: load, D, count, carry
  assign controlled_buffer_7_out = main_1_a_b_2 ? main_5_out_3 : 7'bz;  // Controlled_Buffer controlled_buffer_7
  assign controlled_buffer_7_out = main_2_a_b_2 ? n2x2_block_1_out_3 : 7'bz;  // Controlled_Buffer controlled_buffer_8
  assign controlled_buffer_9_out = main_2_a_b_2 ? n2x2_block_1_out_4 : 2'bz;  // Controlled_Buffer controlled_buffer_9
  assign controlled_buffer_7_out = main_3_a_b_2 ? main_6_out_3 : 7'bz;  // Controlled_Buffer controlled_buffer_10
  assign controlled_buffer_7_out = main_4_a_b_2 ? main_7_out_3 : 7'bz;  // Controlled_Buffer controlled_buffer_11
  assign controlled_buffer_12_out = not_4_out ? counter_3_q : 7'bz;  // Controlled_Buffer controlled_buffer_12
  not not_4 (not_4_out, not_5_out);
  assign controlled_buffer_9_out = main_1_a_b_2 ? main_5_out_4 : 2'bz;  // Controlled_Buffer controlled_buffer_13
  assign controlled_buffer_9_out = main_3_a_b_2 ? main_6_out_4 : 2'bz;  // Controlled_Buffer controlled_buffer_14
  assign controlled_buffer_9_out = main_4_a_b_2 ? main_7_out_4 : 2'bz;  // Controlled_Buffer controlled_buffer_15
  Pull_Resistor pull_resistor_7 (.node(controlled_buffer_12_out));
  assign controlled_buffer_12_out = not_5_out ? counter_5_q : 7'bz;  // Controlled_Buffer controlled_buffer_16
  not not_5 (not_5_out, main_8_a_b_2);
  _2bit_comparator_main main_8 (.in_1(counter_6_q), .in_2(2'b10), .A_B_2(main_8_a_b_2));  // open: A_B, A_B_3
  not not_6 (not_6_out, not_5_out);
  assign controlled_buffer_17_out = counter_1_carry ? controlled_buffer_5_out : 1'bz;  // Controlled_Buffer controlled_buffer_17
  assign controlled_buffer_18_out = not_6_out ? controlled_buffer_7_out : 7'bz;  // Controlled_Buffer controlled_buffer_18
  assign OUT_A = pull_resistor_9_node ? controlled_buffer_18_out : 7'bz;  // Controlled_Buffer controlled_buffer_19
  Pull_Resistor pull_resistor_8 (.node(controlled_buffer_18_out));
  Pull_Resistor pull_resistor_9 (.node(pull_resistor_9_node));
  assign pull_resistor_9_node = not_7_out ? not_4_out : 1'bz;  // Controlled_Buffer controlled_buffer_20
  not not_7 (not_7_out, counter_1_carry);
  _2bit_comparator_main main_9 (.in_1(counter_4_q), .in_2(2'b10), .A_B_2(OUT_B));  // open: A_B, A_B_3
  Pull_Resistor pull_resistor_10 (.node(controlled_buffer_17_out));
  assign controlled_buffer_17_out = not_8_out ? CLK : 1'bz;  // Controlled_Buffer controlled_buffer_21
  not not_8 (not_8_out, counter_1_carry);
  not not_9 (not_9_out, pull_resistor_9_node);
  Pull_Resistor pull_resistor_11 (.node(OUT_A));
  assign OUT_A = counter_1_carry ? counter_3_q : 7'bz;  // Controlled_Buffer controlled_buffer_22
  GAME_OVER game_over_1 (
    .GAME_ADRESS(controlled_buffer_12_out), .GAME_CLK(controlled_buffer_17_out),
    .GAME_STATE(CURRENT_GAME_STATE), .GAME_OVER(GAME_OVER));
  assign controlled_buffer_23_out = not_9_out ? not_10_out : 1'bz;  // Controlled_Buffer controlled_buffer_23
  Pull_Resistor pull_resistor_12 (.node(controlled_buffer_23_out));
  not not_10 (not_10_out, counter_1_carry);
  Pull_Resistor pull_resistor_13 (.node(OUT_A));
  assign OUT_A = controlled_buffer_23_out ? pull_resistor_14_node : 7'bz;  // Controlled_Buffer controlled_buffer_24
  Pull_Resistor pull_resistor_14 (.node(pull_resistor_14_node));
  assign pull_resistor_14_node = not_5_out ? counter_5_q : 7'bz;  // Controlled_Buffer controlled_buffer_25
  assign controlled_buffer_26_out = not_11_out ? controlled_buffer_9_out : 2'bz;  // Controlled_Buffer controlled_buffer_26
  not not_11 (not_11_out, main_10_a_b_2);
  _2bit_comparator_main main_10 (
    .in_1(controlled_buffer_9_out), .in_2(2'b00), .A_B_2(main_10_a_b_2));  // open: A_B, A_B_3
  assign controlled_buffer_26_out = main_10_a_b_2 ? CURRENT_GAME_STATE : 2'bz;  // Controlled_Buffer controlled_buffer_27
  Pull_Resistor pull_resistor_15 (.node(controlled_buffer_26_out));
  not not_12 (not_12_out, not_5_out);
  Pull_Resistor pull_resistor_16 (.node(controlled_buffer_26_out));
  assign OUT_D = pull_resistor_18_node ? controlled_buffer_29_out : 2'bz;  // Controlled_Buffer controlled_buffer_28
  assign controlled_buffer_29_out = not_12_out ? controlled_buffer_26_out : 2'bz;  // Controlled_Buffer controlled_buffer_29
  Pull_Resistor pull_resistor_17 (.node(controlled_buffer_29_out));
  Pull_Resistor pull_resistor_18 (.node(pull_resistor_18_node));
  assign pull_resistor_18_node = not_13_out ? not_4_out : 1'bz;  // Controlled_Buffer controlled_buffer_30
  not not_13 (not_13_out, counter_1_carry);
  not not_14 (not_14_out, pull_resistor_18_node);
  Pull_Resistor pull_resistor_19 (.node(OUT_D));
  assign OUT_D = counter_1_carry ? CURRENT_GAME_STATE : 2'bz;  // Controlled_Buffer controlled_buffer_31
  assign controlled_buffer_32_out = not_14_out ? not_15_out : 1'bz;  // Controlled_Buffer controlled_buffer_32
  Pull_Resistor pull_resistor_20 (.node(controlled_buffer_32_out));
  not not_15 (not_15_out, counter_1_carry);
  Pull_Resistor pull_resistor_21 (.node(OUT_D));
  assign OUT_D = controlled_buffer_32_out ? pull_resistor_22_node : 2'bz;  // Controlled_Buffer controlled_buffer_33
  Pull_Resistor pull_resistor_22 (.node(pull_resistor_22_node));
  assign pull_resistor_22_node = not_5_out ? CURRENT_GAME_STATE : 2'bz;  // Controlled_Buffer controlled_buffer_34

  // Notes on the sheet:
  //   OUT_A - code for coordinates of current block
  //   OUT_B - if 1 - block finished its work
  //   OUT_D - is current block solid/air
endmodule
