// Logisim project Randomizer.circ as structural Verilog: 1 circuit, main circuit main
module main (
  input  CLK,
  output [1:0] OUT
);

  wire counter_1_q, d_ff_5_q, not_1_out, xor_2_out;
  wire [4:0] d_ff_4_q;

  Counter #(.width(1), .max('h1), .ongoal("stay")) counter_1 (
    .D(1'b1), .Q(counter_1_q), .clk(CLK));  // open: load, count, carry, clr
  not not_1 (not_1_out, counter_1_q);
  xor xor_1 (d_ff_4_q[4], xor_2_out, not_1_out);
  D_Flip_Flop d_ff_1 (.clk(CLK), .D(d_ff_4_q[4]), .Q(d_ff_4_q[3]));  // open: Qn, preset, en, reset
  D_Flip_Flop d_ff_2 (.clk(CLK), .D(d_ff_4_q[3]), .Q(d_ff_4_q[2]));  // open: Qn, preset, en, reset
  xor xor_2 (xor_2_out, d_ff_5_q, d_ff_4_q[2]);
  D_Flip_Flop d_ff_3 (.clk(CLK), .D(d_ff_4_q[2]), .Q(d_ff_4_q[1]));  // open: Qn, preset, en, reset
  D_Flip_Flop d_ff_4 (.clk(CLK), .D(d_ff_4_q[1]), .Q(d_ff_4_q[0]));  // open: Qn, preset, en, reset
  D_Flip_Flop d_ff_5 (.clk(CLK), .D(d_ff_4_q[0]), .Q(d_ff_5_q));  // open: Qn, preset, en, reset
  Multiplexer #(.select(5), .width(2), .enable("false")) multiplexer_1 (
    .in0(2'b00), .in1(2'b01), .in2(2'b10), .in3(2'b11), .in4(2'b00), .in5(2'b01), .in6(2'b10), .in7(2'b11),
    .in8(2'b00), .in9(2'b01), .in10(2'b10), .in11(2'b11), .in12(2'b00), .in13(2'b01), .in14(2'b10),
    .in15(2'b11), .in16(2'b00), .in17(2'b01), .in18(2'b10), .in19(2'b11), .in20(2'b00), .in21(2'b01),
    .in22(2'b10), .in23(2'b11), .in24(2'b00), .in25(2'b01), .in26(2'b10), .in27(2'b11), .in28(2'b00),
    .in29(2'b01), .in30(2'b10), .in31(2'b11), .out(OUT), .sel(d_ff_4_q));
endmodule
