// Logisim project obnizanie_new.circ as structural Verilog: 1 circuit, main circuit obnizanie
module obnizanie (
  input  [6:0] A1,
  input  in_2,
  input  in_3,
  input  in_4,
  input  in_5,
  input  in_6,
  input  in_7,
  input  [1:0] DATA_IN,
  input  CLK,
  input  ENABLE,
  output [6:0] A,
  output FINISH,
  output [1:0] DATA_OUT,
  output RAM_CLK
);

  wire and_1_out, shift_register_1_q0;

  and and_1 (and_1_out, CLK, ENABLE);
  adreso_latacz adreso_latacz_1 (.CLK(and_1_out), .ADRES_OUT(A), .FINISH(FINISH), .ADRES_ROOT(A1));
  wiersz wiersz_1 (.CLK(and_1_out), .RAM_CLK(RAM_CLK), .DATA_IN(DATA_IN), .DATA_OUT(DATA_OUT));
  Shift_Register shift_register_1 (
    .shift(in_6), .in(in_5), .clk(in_7), .load(in_4), .d0(in_3), .q0(shift_register_1_q0), .d1(in_2));  // open: out, clr, q1, d2, q2, d3, q3, d4, q4, d5, q5, d6, q6, d7, q7
endmodule
