// Logisim project StateSelector.circ as structural Verilog: 1 circuit, main circuit State Selector
module State_Selector (
  input  Keyboard__Input_Happened,
  input  Render,
  input  New_Block_Request,
  input  Generating_Ended,
  input  Player_Input_Ended,
  input  Shifting_Down_Ended,
  output [2:0] out_7
);

  wire d_ff_1_q, or_1_out;
  wire [2:0] multiplexer_1_out, multiplexer_2_out, register_1_q;

  Multiplexer #(.width(3)) multiplexer_1 (
    .in0(3'b010), .in1(3'b011), .out(multiplexer_1_out), .sel(Keyboard__Input_Happened));  // open: en
  Multiplexer #(.select(4), .width(3)) multiplexer_2 (
    .in0(3'b000), .in1(3'b010), .in2(multiplexer_1_out), .in4(multiplexer_1_out), .in8(3'b100),
    .out(multiplexer_2_out),
    .sel({New_Block_Request, Generating_Ended, Shifting_Down_Ended, Player_Input_Ended}));  // open: in3, in5, in6, in7, in9, in10, in11, in12, in13, in14, in15, en
  Register #(.width(3), .trigger("falling")) register_1 (
    .D(multiplexer_2_out), .Q(register_1_q), .clk(or_1_out));  // open: en, clr
  or or_1 (or_1_out, New_Block_Request, Generating_Ended, Shifting_Down_Ended, Player_Input_Ended);
  Multiplexer #(.width(3)) multiplexer_3 (.in0(register_1_q), .in1(3'b001), .out(out_7), .sel(d_ff_1_q));  // open: en
  D_Flip_Flop d_ff_1 (.clk(or_1_out), .D(1'b1), .Q(d_ff_1_q), .reset(Render));  // open: Qn, preset, en

  // Notes on the sheet:
  //   1 Rendering
  //   2 Falling
  //   3 Player Input actions
  //   4 Generating Blocks
  //   If state is 0 something is wrong
endmodule
