// Logisim project Usuwanierzedow.circ as structural Verilog: 1 circuit, main circuit main
module main (
  output out_1,
  output [2:0] out_2
);

  wire and_1_out, and_2_out, and_3_out, and_4_out, bitselector_1_out, CLK, CLR, comparator_2_eq,
       comparator_3_eq, controlled_buffer_3_out, controlled_buffer_4_out, counter_1_carry, d_ff_1_q,
       pull_resistor_1_node;
  wire [1:0] bit_extender_1_out, counter_2_q, ram_1_data;
  wire [2:0] bit_extender_3_out;
  wire [3:0] bit_extender_2_out, counter_3_q, multiplexer_1_out, not_3_out;
  wire [6:0] counter_1_q, divider_1_out, divider_1_rem, register_9_q, register_10_q;
  wire [7:0] not_2_out, ram_2_data, register_8_q;

  Button button_1 (.out(CLK));
  Counter #(.width(7), .max('h7f)) counter_1 (
    .load(1'b1), .Q(counter_1_q), .carry(counter_1_carry), .clk(CLK), .clr(out_1));  // open: D, count
  Comparator #(.width(2)) comparator_1 (.a(2'b11), .b(counter_2_q), .eq(CLR));  // open: gt, lt
  Counter #(.width(2), .max('h3)) counter_2 (
    .Q(counter_2_q), .clk(counter_1_carry), .clr(CLR));  // open: load, D, count, carry
  assign bit_extender_1_out = {{1{1'b0}}, bitselector_1_out};  // Bit_Extender bit_extender_1
  BitSelector bitselector_1 (.in(ram_2_data), .out(bitselector_1_out), .sel(out_2));
  RAM #(.addrWidth(7), .dataWidth(2), .bus("separate")) ram_1 (
    .addr(counter_1_q), .din(bit_extender_1_out), .data(ram_1_data), .clk(pull_resistor_1_node));  // open: str, sel, ld, clr
  Pull_Resistor pull_resistor_1 (.node(pull_resistor_1_node));
  assign pull_resistor_1_node = d_ff_1_q ? CLK : 1'bz;  // Controlled_Buffer controlled_buffer_1
  D_Flip_Flop d_ff_1 (.clk(out_1), .D(1'b1), .Q(d_ff_1_q), .reset(CLR));  // open: Qn, preset, en
  Register #(.width(1)) register_1 (.D(ram_1_data[0]), .Q(register_8_q[7]), .clk(CLK), .clr(CLR));  // open: en
  assign out_2 = ~bit_extender_3_out;  // NOT_Gate not_1, 3 bits wide
  Register #(.width(1)) register_2 (.D(register_8_q[6]), .Q(register_8_q[5]), .clk(CLK), .clr(CLR));  // open: en
  Register #(.width(1)) register_3 (.D(register_8_q[7]), .Q(register_8_q[6]), .clk(CLK), .clr(CLR));  // open: en
  Register #(.width(1)) register_4 (.D(register_8_q[5]), .Q(register_8_q[4]), .clk(CLK), .clr(CLR));  // open: en
  assign not_2_out = ~register_8_q;  // NOT_Gate not_2, 8 bits wide
  Register #(.width(1)) register_5 (.D(register_8_q[4]), .Q(register_8_q[3]), .clk(CLK), .clr(CLR));  // open: en
  Register #(.width(1)) register_6 (.D(register_8_q[3]), .Q(register_8_q[2]), .clk(CLK), .clr(CLR));  // open: en
  and and_1 (and_1_out, register_8_q[0], register_8_q[1], register_8_q[2], register_8_q[3], register_8_q[5], register_8_q[6], register_8_q[7], register_8_q[4]);
  and and_2 (and_2_out, not_2_out[0], not_2_out[1], not_2_out[2], not_2_out[3], not_2_out[5], not_2_out[6], not_2_out[7], not_2_out[4]);
  Register #(.width(1)) register_7 (.D(register_8_q[2]), .Q(register_8_q[1]), .clk(CLK), .clr(CLR));  // open: en
  Register #(.width(1)) register_8 (.D(register_8_q[1]), .Q(register_8_q[0]), .clk(CLK), .clr(CLR));  // open: en
  assign out_1 = and_4_out ? and_2_out : 1'bz;  // Controlled_Buffer controlled_buffer_2
  Pull_Resistor pull_resistor_2 (.node(out_1));
  Counter #(.width(4), .max('hf)) counter_3 (
    .Q(counter_3_q), .clk(controlled_buffer_3_out), .clr(CLR));  // open: load, D, count, carry
  assign controlled_buffer_3_out = and_3_out ? CLK : 1'bz;  // Controlled_Buffer controlled_buffer_3
  and and_3 (and_3_out, ~and_1_out, ~d_ff_1_q, and_4_out);  // AND_Gate
  Divider #(.width(7)) divider_1 (
    .a(counter_1_q), .b(7'b0001000), .out(divider_1_out), .rem(divider_1_rem));  // open: upper
  Multiplexer #(.width(4), .enable("false")) multiplexer_1 (
    .in0(counter_3_q), .in1(not_3_out), .out(multiplexer_1_out), .sel(d_ff_1_q));
  Bit_Extender #(.in_width(7), .out_width(4)) bit_extender_2 (.in(divider_1_out), .out(bit_extender_2_out));
  Register #(.width(7)) register_9 (.D(divider_1_rem), .Q(register_9_q), .clk(CLK));  // open: en, clr
  Bit_Extender #(.in_width(7), .out_width(3)) bit_extender_3 (.in(divider_1_rem), .out(bit_extender_3_out));
  assign controlled_buffer_4_out = and_3_out ? CLK : 1'bz;  // Controlled_Buffer controlled_buffer_4
  assign not_3_out = ~bit_extender_2_out;  // NOT_Gate not_3, 4 bits wide
  Comparator #(.width(7)) comparator_2 (.a({7{1'b0}}), .b(register_9_q), .eq(comparator_2_eq));  // open: gt, lt
  Comparator #(.width(7)) comparator_3 (.a(7'b0000001), .b(register_10_q), .eq(comparator_3_eq));  // open: gt, lt
  Register #(.width(7)) register_10 (.D(register_9_q), .Q(register_10_q), .clk(CLK));  // open: en, clr
  RAM #(.addrWidth(4), .bus("separate")) ram_2 (
    .addr(multiplexer_1_out), .din(register_8_q), .data(ram_2_data), .clk(controlled_buffer_4_out), .clr(CLR));  // open: str, sel, ld
  and and_4 (and_4_out, comparator_2_eq, comparator_3_eq);
endmodule
