// Logisim project kaskader_1bit.circ as structural Verilog: 1 circuit, main circuit main
module main (
  input  [1:0] DATA_INPUT,
  input  CLOCK,
  input  [2:0] KTORY_W_KOLEJNOSCI,
  output [1:0] WYJSCIE
);

  wire comparator_1_eq;
  wire [2:0] counter_1_q;

  Counter #(.width(3), .max('h7)) counter_1 (.Q(counter_1_q), .clk(CLOCK));  // open: load, D, count, carry, clr
  Comparator #(.width(3)) comparator_1 (.a(counter_1_q), .b(KTORY_W_KOLEJNOSCI), .eq(comparator_1_eq));  // open: gt, lt
  Register #(.width(2)) register_1 (.D(DATA_INPUT), .Q(WYJSCIE), .clk(comparator_1_eq));  // open: en, clr
endmodule
