// Logisim project pamiec - testowe2testv1.circ as structural Verilog: 1 circuit, main circuit main
module main (
  input  [3:0] _1_0_N,
  input  [6:0] ADRES,
  input  CLOCK,
  output [1:0] out_4,
  output [1:0] out_5,
  output [1:0] out_6,
  output [1:0] out_7,
  output [3:0] out_8,
  output [1:0] out_9,
  output [1:0] out_10,
  output [2:0] out_11,
  output [1:0] out_12,
  output [1:0] out_13,
  output [1:0] out_14,
  output [1:0] out_15,
  output [3:0] out_16,
  output [1:0] out_17
);

  wire comparator_1_eq, comparator_2_eq, comparator_3_eq, comparator_4_eq, or_1_out;
  wire [1:0] counter_1_q;
  wire [2:0] counter_3_q;
  wire [6:0] adder_1_out, counter_2_q, multiplexer_1_out, negator_1_out;

  Counter #(.width(2), .max('h3)) counter_1 (.Q(counter_1_q), .clk(CLOCK));  // open: load, D, count, carry, clr
  Comparator #(.width(2), .mode("unsigned")) comparator_1 (
    .a(counter_1_q), .b(2'b11), .eq(comparator_1_eq));  // open: gt, lt
  Comparator #(.width(2), .mode("unsigned")) comparator_2 (
    .a(counter_1_q), .b(2'b10), .eq(comparator_2_eq));  // open: gt, lt
  Comparator #(.width(2), .mode("unsigned")) comparator_3 (
    .a(counter_1_q), .b(2'b01), .eq(comparator_3_eq));  // open: gt, lt
  Comparator #(.width(2), .mode("unsigned")) comparator_4 (
    .a(counter_1_q), .b(2'b00), .eq(comparator_4_eq));  // open: gt, lt
  Counter #(.width(7), .max('h7f)) counter_2 (
    .Q(counter_2_q), .clk(comparator_4_eq));  // open: load, D, count, carry, clr
  Multiplexer #(.width(7)) multiplexer_1 (
    .in0(negator_1_out), .in1(adder_1_out), .out(multiplexer_1_out), .sel(comparator_2_eq));  // open: en
  Negator #(.width(7)) negator_1 (.in(counter_2_q), .out(negator_1_out));
  Adder #(.width(7)) adder_1 (.a(negator_1_out), .b(7'b0001000), .out(adder_1_out));  // open: cin, cout
  Multiplexer #(.width(2)) multiplexer_2 (
    .in0(_1_0_N[1:0]), .in1(_1_0_N[3:2]), .out(out_5), .sel(comparator_2_eq));  // open: en
  or or_1 (or_1_out, comparator_1_eq, comparator_3_eq);
  RAM #(.addrWidth(7), .dataWidth(2), .bus("separate")) ram_1 (
    .addr(multiplexer_1_out), .din(out_5), .data(out_16[1:0]), .clk(or_1_out));  // open: str, sel, ld, clr
  Multiplexer #(.select(3), .width(2)) multiplexer_3 (
    .in0(out_15), .in1(out_14), .in2(out_13), .in3(out_12), .in4(out_10), .in5(out_9), .in6(out_7),
    .in7(out_6), .out(out_4), .sel(out_11));  // open: en
  // kaskader_8bit_main main_1: pin names not known; wires that end beside it: out_16[1:0], out_15, out_14, out_13, out_12, out_10, out_9, comparator_3_eq, out_7, out_6
  Adder #(.width(3)) adder_2 (.a(counter_3_q), .b(3'b001), .out(out_11));  // open: cin, cout
  Counter #(.width(3), .max('h7)) counter_3 (
    .Q(counter_3_q), .clk(comparator_4_eq));  // open: load, D, count, carry, clr
  Multiplexer #(.select(4), .width(4)) multiplexer_4 (
    .in8(4'b0010), .out(out_8), .sel({out_4, out_16[1:0]}));  // open: in0, in1, in2, in3, in4, in5, in6, in7, in9, in10, in11, in12, in13, in14, in15, en

  assign out_16[3:2] = out_4;
  assign out_17 = out_16[1:0];

  // Notes on the sheet:
  //   2-3 W
  //   TODO zrobić wsteczny iterator i sprawdzić czy switcth 4-bit starczy (czy clock na temp pamiec odpowiednio wbija)
  //   jak W: ruchomy N: powietrze to W-> powietrze N:ruchomy
  //   jak W-ruchomy N-ruchomy to nic?
endmodule
