// Logisim project pamiec - testowe3_zmiana_iteracji.circ as structural Verilog: 1 circuit, main circuit main
module main (
  input  [3:0] _1_0_N,
  input  [6:0] ADRES,
  output [1:0] out_3,
  output [1:0] out_4,
  output [1:0] out_5,
  output [1:0] out_6,
  output [3:0] out_7,
  output [1:0] out_8,
  output [1:0] out_9,
  output [2:0] out_10,
  output [1:0] out_11,
  output [1:0] out_12,
  output [1:0] out_13,
  output [1:0] out_14,
  output [3:0] out_15,
  output [1:0] out_16,
  output [6:0] out_17
);

  wire clock_1_out, comparator_1_lt, main_1__0_4, main_1__0_5, main_1__0_6, main_1__0_7, main_1__0_8,
       or_1_out;
  wire [2:0] counter_1_q, counter_3_q;
  wire [3:0] joystick_1_x, joystick_1_y;
  wire [6:0] adder_1_out, counter_2_q, multiplexer_1_out, multiplexer_3_out;

  switch8bit_main main_1 (
    .INPUT(counter_1_q), ._0_4(main_1__0_4), ._0_5(main_1__0_5), ._0_6(main_1__0_6), ._0_7(main_1__0_7),
    ._0_8(main_1__0_8));  // open: _0, _0_2, _0_3
  Counter #(.width(3), .max('h7)) counter_1 (.Q(counter_1_q), .clk(clock_1_out));  // open: load, D, count, carry, clr
  Clock clock_1 (.out(clock_1_out));
  Multiplexer #(.width(7)) multiplexer_1 (
    .in0(out_17), .in1(adder_1_out), .out(multiplexer_1_out), .sel(main_1__0_5));  // open: en
  Negator #(.width(7)) negator_1 (.in(multiplexer_3_out), .out(out_17));
  Adder #(.width(7)) adder_1 (.a(out_17), .b(7'b0001000), .out(adder_1_out));  // open: cin, cout
  Multiplexer #(.width(2)) multiplexer_2 (
    .in0(_1_0_N[1:0]), .in1(_1_0_N[3:2]), .out(out_4), .sel(main_1__0_5));  // open: en
  or or_1 (or_1_out, main_1__0_4, main_1__0_6);
  Comparator #(.width(7), .mode("unsigned")) comparator_1 (
    .a(counter_2_q), .b(7'b0000001), .lt(comparator_1_lt));  // open: gt, eq
  RAM #(.addrWidth(7), .dataWidth(2), .bus("separate")) ram_1 (
    .addr(multiplexer_1_out), .din(out_4), .data(out_15[1:0]), .clk(or_1_out));  // open: str, sel, ld, clr
  Counter #(.width(7), .max('h7f)) counter_2 (.Q(counter_2_q), .clk(main_1__0_8));  // open: load, D, count, carry, clr
  Multiplexer #(.width(7)) multiplexer_3 (
    .in0(counter_2_q), .in1(7'b0000001), .out(multiplexer_3_out), .sel(comparator_1_lt));  // open: en
  Multiplexer #(.select(3), .width(2)) multiplexer_4 (
    .in0(out_14), .in1(out_13), .in2(out_12), .in3(out_11), .in4(out_9), .in5(out_8), .in6(out_6),
    .in7(out_5), .out(out_3), .sel(out_10));  // open: en
  kaskader_8bit_main main_2 (
    .DATA(out_15[1:0]), .CLK(main_1__0_7), .Q0(out_14), .Q2(out_12), .Q1(out_13), .Q3(out_11), .Q4(out_9),
    .Q5(out_8), .Q6_2(out_6), .Q6(out_5), .\PODŁOGA (comparator_1_lt));
  Adder #(.width(3)) adder_2 (.a(counter_3_q), .b(3'b001), .out(out_10));  // open: cin, cout
  Counter #(.width(3), .max('h7)) counter_3 (.Q(counter_3_q), .clk(main_1__0_8));  // open: load, D, count, carry, clr
  Multiplexer #(.select(4), .width(4)) multiplexer_5 (
    .in8(4'b0010), .out(out_7), .sel({out_3, out_15[1:0]}));  // open: in0, in1, in2, in3, in4, in5, in6, in7, in9, in10, in11, in12, in13, in14, in15, en
  Joystick joystick_1 (.x(joystick_1_x), .y(joystick_1_y));

  assign out_15[3:2] = out_3;
  assign out_16 = out_15[1:0];

  // Notes on the sheet:
  //   2-3 W
  //   TODO z zerowaniem wiersza to mozna zrobic przelacznik ze jak wykryje ze caly wiersz to pelny to korzysta z innego muxa
  //   TODO teraz: nowy kaskader z MUXA na D-Flop ktory dodatkowo ma mozliwosc ustawienia wszystkich naraz jak sie da mu sygnal podloga
  //   jak W: ruchomy N: powietrze to W-> powietrze N:ruchomy
  //   jak W-ruchomy N-ruchomy to nic?
endmodule
