// Logisim project smart_selector.circ as structural Verilog: 1 circuit, main circuit main
module main (
  input  _0_0,
  input  _0_1,
  input  _1_0,
  input  _1_1,
  input  _2_0,
  input  _2_1,
  output [1:0] OUT
);

  wire [2:0] or_1_out;

  or or_1 (or_1_out[0], _0_0, _0_1);
  Multiplexer #(.select(3), .width(2), .disabled(0)) multiplexer_1 (
    .in0(2'b00), .in1(2'b01), .in2(2'b10), .in4(2'b11), .out(OUT), .sel(or_1_out));  // open: in3, in5, in6, in7, en
  or or_2 (or_1_out[1], _1_0, _1_1);
  or or_3 (or_1_out[2], _2_0, _2_1);
endmodule
