// Logisim project test_obnizanenie_1.circ as structural Verilog: 1 circuit, main circuit main
module main (
  input  [6:0] in_1,
  input  in_2,
  output out_3,
  output out_4
);

  wire clock_1_out, main_1_ram_clk;
  wire [1:0] main_1_data_out, ram_1_data;
  wire [6:0] main_1_a;

  Clock clock_1 (.out(clock_1_out));
  RAM #(.addrWidth(7), .dataWidth(2), .bus("separate")) ram_1 (
    .addr(main_1_a), .din(main_1_data_out), .data(ram_1_data), .clk(main_1_ram_clk));  // open: str, sel, ld, clr
  obnizanie_do_bloczku3_main main_1 (
    .ENABLE(in_2), .\ZAMROŹ (out_3), .FINISH(out_4), .A1(in_1), .A(main_1_a), .DATA_IN(ram_1_data),
    .DATA_OUT(main_1_data_out), .CLK(clock_1_out), .RAM_CLK(main_1_ram_clk));  // open: out_5, poprzednie__W
endmodule
