// Logisim project switch8bit.circ as structural Verilog: 1 circuit, main circuit main
module main (
  input  [2:0] INPUT,
  output _0,
  output _0_2,
  output _0_3,
  output _0_4,
  output _0_5,
  output _0_6,
  output _0_7,
  output _0_8
);

  Comparator #(.width(3), .mode("unsigned")) comparator_1 (.a(INPUT), .b(3'b111), .eq(_0));  // open: gt, lt
  Comparator #(.width(3), .mode("unsigned")) comparator_2 (.a(INPUT), .b(3'b110), .eq(_0_2));  // open: gt, lt
  Comparator #(.width(3), .mode("unsigned")) comparator_3 (.a(INPUT), .b(3'b101), .eq(_0_3));  // open: gt, lt
  Comparator #(.width(3), .mode("unsigned")) comparator_4 (.a(INPUT), .b(3'b100), .eq(_0_4));  // open: gt, lt
  Comparator #(.width(3), .mode("unsigned")) comparator_5 (.a(INPUT), .b(3'b011), .eq(_0_5));  // open: gt, lt
  Comparator #(.width(3), .mode("unsigned")) comparator_6 (.a(INPUT), .b(3'b010), .eq(_0_6));  // open: gt, lt
  Comparator #(.width(3), .mode("unsigned")) comparator_7 (.a(INPUT), .b(3'b001), .eq(_0_7));  // open: gt, lt
  Comparator #(.width(3), .mode("unsigned")) comparator_8 (.a(INPUT), .b(3'b000), .eq(_0_8));  // open: gt, lt

  // Notes on the sheet:
  //   od liczbo-stano-wybierato-inator
  //   czyli switch: case
endmodule
