// Logisim project 7I1O tflop.circ as structural Verilog: 1 circuit, main circuit 7I1O TFlop
module _7I1O_TFlop (
  input  [6:0] in_1,
  input  in_2,
  output out_3
);

  wire t_ff_1_q, t_ff_2_q, t_ff_3_q, t_ff_4_q, t_ff_5_q, t_ff_6_q, t_ff_7_q;

  T_Flip_Flop t_ff_1 (.clk(in_2), .T(in_1[0]), .Q(t_ff_1_q));  // open: Qn, preset, reset, en
  T_Flip_Flop t_ff_2 (.clk(in_2), .T(in_1[1]), .Q(t_ff_2_q));  // open: Qn, preset, reset, en
  T_Flip_Flop t_ff_3 (.clk(in_2), .T(in_1[2]), .Q(t_ff_3_q));  // open: Qn, preset, reset, en
  T_Flip_Flop t_ff_4 (.clk(in_2), .T(in_1[3]), .Q(t_ff_4_q));  // open: Qn, preset, reset, en
  T_Flip_Flop t_ff_5 (.clk(in_2), .T(in_1[4]), .Q(t_ff_5_q));  // open: Qn, preset, reset, en
  T_Flip_Flop t_ff_6 (.clk(in_2), .T(in_1[5]), .Q(t_ff_6_q));  // open: Qn, preset, reset, en
  T_Flip_Flop t_ff_7 (.clk(in_2), .T(in_1[6]), .Q(t_ff_7_q));  // open: Qn, preset, reset, en
  or or_1 (out_3, t_ff_1_q, t_ff_2_q, t_ff_3_q, t_ff_4_q, t_ff_5_q, t_ff_6_q, t_ff_7_q);
endmodule
