// Logisim project GPUman.circ as structural Verilog: 1 circuit, main circuit GPU manager
module GPU_manager (
  input  [1:0] in_1,
  input  in_2,
  output [6:0] out_3,
  output [6:0] out_4,
  output out_5,
  output out_6,
  output out_7
);

  wire and_1_out, and_2_out, comparator_1_eq, counter_1_carry, d_ff_1_qn, d_ff_2_qn, multiplexer_1_out,
       or_1_out, or_2_out, pull_resistor_1_node, t_ff_1_q, t_ff_1_qn;
  wire [1:1] d_ff_1_q;
  wire [2:2] t_ff_2_q;

  and and_1 (and_1_out, ~out_5, ~d_ff_1_q[1], t_ff_2_q[2]);  // AND_Gate
  Counter #(.width(7), .max('h7f), .trigger("falling")) counter_1 (
    .Q(out_3), .carry(counter_1_carry), .clk(pull_resistor_1_node));  // open: load, D, count, clr
  Pull_Resistor pull_resistor_1 (.node(pull_resistor_1_node));
  assign pull_resistor_1_node = t_ff_1_q ? in_2 : 1'bz;  // Controlled_Buffer controlled_buffer_1
  or or_1 (or_1_out, counter_1_carry, and_1_out);
  Comparator #(.width(7)) comparator_1 (.a(out_3), .b({7{1'b0}}), .eq(comparator_1_eq));  // open: gt, lt
  T_Flip_Flop t_ff_1 (.clk(in_2), .T(or_1_out), .Q(t_ff_1_q), .Qn(t_ff_1_qn));  // open: preset, reset, en
  T_Flip_Flop t_ff_2 (.clk(in_2), .T(comparator_1_eq), .Q(t_ff_2_q[2]));  // open: Qn, preset, reset, en
  D_Flip_Flop d_ff_1 (.clk(t_ff_2_q[2]), .D(d_ff_1_qn), .Q(d_ff_1_q[1]), .Qn(d_ff_1_qn));  // open: preset, en, reset
  or or_2 (or_2_out, in_1[0], in_1[1]);
  and and_2 (and_2_out, d_ff_1_q[1], out_5);
  D_Flip_Flop d_ff_2 (.clk(d_ff_1_qn), .D(d_ff_2_qn), .Q(out_5), .Qn(d_ff_2_qn));  // open: preset, en, reset
  Multiplexer #(.disabled(0)) multiplexer_1 (
    .in0(or_2_out), .in1(and_2_out), .out(multiplexer_1_out), .sel(t_ff_1_qn));  // open: en
  assign out_6 = multiplexer_1_out ? in_2 : 1'bz;  // Controlled_Buffer controlled_buffer_2
  Pull_Resistor pull_resistor_2 (.node(out_6));
  and and_3 (out_7, d_ff_1_q[1], ~out_5);  // AND_Gate

  assign out_4 = out_3;
endmodule
