// Logisim project 1IO buffer.circ as structural Verilog: 1 circuit, main circuit 1IO Buffer
module _1IO_Buffer (
  input  [7:0] in_1,
  input  in_2,
  input  in_3,
  input  in_4,
  output [7:0] out_5
);

  wire [7:0] multiplexer_1_out, or_1_out, register_1_q;

  assign or_1_out = register_1_q | in_1;  // OR_Gate or_1, 8 bits wide
  Multiplexer #(.width(8)) multiplexer_1 (
    .in0(or_1_out), .in1({8{1'b0}}), .out(multiplexer_1_out), .sel(in_2));  // open: en
  Register register_1 (.D(multiplexer_1_out), .Q(register_1_q), .clk(in_3));  // open: en, clr
  Register register_2 (.D(register_1_q), .Q(out_5), .clk(in_4));  // open: en, clr
endmodule
