// Logisim project 1x4 Block.circ as structural Verilog: 1 circuit, main circuit main
module main (
  input  START_GEN,
  input  CLK,
  output [6:0] out_3,
  output [1:0] out_4,
  output out_5
);

  wire pull_resistor_1_node, rom_1_data;
  wire [1:0] bit_extender_2_out;
  wire [3:0] counter_1_q;
  wire [6:0] adder_1_out, bit_extender_1_out, divider_1_out, divider_1_rem, multiplier_1_out;

  Counter #(.width(4), .max('hf)) counter_1 (
    .Q(counter_1_q), .carry(out_5), .clk(pull_resistor_1_node));  // open: load, D, count, clr
  Pull_Resistor pull_resistor_1 (.node(pull_resistor_1_node));
  assign pull_resistor_1_node = CLK ? START_GEN : 1'bz;  // Controlled_Buffer controlled_buffer_1
  assign bit_extender_1_out = {{3{1'b0}}, counter_1_q};  // Bit_Extender bit_extender_1
  Divider #(.width(7)) divider_1 (
    .a(bit_extender_1_out), .b(7'b0000100), .out(divider_1_out), .rem(divider_1_rem));  // open: upper
  ROM #(.addrWidth(4), .dataWidth(1)) rom_1 (.addr(counter_1_q), .data(rom_1_data));  // open: sel
  Multiplier #(.width(7)) multiplier_1 (.a(7'b0001000), .b(divider_1_out), .out(multiplier_1_out));  // open: cin, cout
  Adder #(.width(7)) adder_1 (.a(divider_1_rem), .b(7'b0000010), .out(adder_1_out));  // open: cin, cout
  assign bit_extender_2_out = {{1{1'b0}}, rom_1_data};  // Bit_Extender bit_extender_2
  Adder #(.width(7)) adder_2 (.a(multiplier_1_out), .b(adder_1_out), .out(out_3));  // open: cin, cout
  Multiplier #(.width(2)) multiplier_2 (.a(bit_extender_2_out), .b(2'b10), .out(out_4));  // open: cin, cout

  // Notes on the sheet:
  //   contents of rom_1 (hex, n*v repeats v):
  //   0 1 0 0 0 1 0 0 0 1 0 0 0 1
endmodule
