// Logisim project main.circ as structural Verilog: 1 circuit, main circuit main
module main (
  input  in_1,
  input  in_2,
  input  in_3,
  output [1:0] out_4
);

  wire and_1_out, and_2_out, blc_rand_1_p2, comparator_2_eq, controlled_buffer_2_out, counter_2_carry,
       d_ff_1_q, gpu_manager_1_out_5, gpu_manager_1_out_6, gpu_manager_1_out_7, or_1_out,
       pull_resistor_1_node, pull_resistor_2_node, xor_1_out;
  wire [1:0] blc_rand_1_p4, multiplexer_2_out, multiplexer_4_out, ram_2_data, ram_3_data, undriven;
  wire [6:0] adder_1_out, blc_rand_1_p3, counter_1_q, demultiplexer_1_out0, demultiplexer_1_out1,
       divider_1_rem, gpu_manager_1_out_3, gpu_manager_1_out_4, multiplexer_1_out, multiplexer_3_out;
  wire [7:0] gpu_1_p5, gpu_1_p6, gpu_1_p7, gpu_1_p8, gpu_1_p9, gpu_1_p10, gpu_1_p11, gpu_1_p12, gpu_1_p13,
       gpu_1_p14, gpu_1_p15, gpu_1_p16, gpu_1_p17, gpu_1_p18, gpu_1_p19, gpu_1_p20;

  Counter #(.width(7), .max('h7f)) counter_1 (
    .load(1'b1), .Q(counter_1_q), .clk(pull_resistor_1_node));  // open: D, count, carry, clr
  Pull_Resistor pull_resistor_1 (.node(pull_resistor_1_node));
  assign pull_resistor_1_node = d_ff_1_q ? blc_rand_1_p2 : 1'bz;  // Controlled_Buffer controlled_buffer_1
  // BLC_RAND blc_rand_1: pin names not known; wires that end beside it: in_1, blc_rand_1_p2, blc_rand_1_p3, blc_rand_1_p4
  and and_1 (and_1_out, in_2, pull_resistor_2_node);
  Adder #(.width(7)) adder_1 (.a(counter_1_q), .b(multiplexer_1_out), .out(adder_1_out));  // open: cin, cout
  Multiplexer #(.width(7)) multiplexer_1 (
    .in0({7{1'b0}}), .in1(7'b0001000), .out(multiplexer_1_out), .sel(and_1_out));  // open: en
  Pull_Resistor pull_resistor_2 (.node(pull_resistor_2_node));
  D_Flip_Flop d_ff_1 (.clk(blc_rand_1_p2), .D(xor_1_out), .Q(d_ff_1_q));  // open: Qn, preset, en, reset
  xor xor_1 (xor_1_out, pull_resistor_2_node, ~in_3);  // XOR_Gate
  Multiplexer #(.width(2)) multiplexer_2 (
    .in0(undriven), .in1(blc_rand_1_p4), .out(multiplexer_2_out), .sel(in_1));  // open: en
  Multiplexer #(.width(7)) multiplexer_3 (
    .in0(adder_1_out), .in1(blc_rand_1_p3), .out(multiplexer_3_out), .sel(in_1));  // open: en
  Comparator #(.width(2)) comparator_1 (.a(2'b00), .b(out_4), .eq(pull_resistor_2_node));  // open: gt, lt
  Clock clock_1 (.out(blc_rand_1_p2));
  RAM #(.addrWidth(7), .dataWidth(2), .bus("separate")) ram_1 (
    .addr(multiplexer_3_out), .din(multiplexer_2_out), .data(out_4), .str(in_1), .sel(1'b1),
    .clk(blc_rand_1_p2));  // open: ld, clr
  or or_1 (or_1_out, out_4[0], out_4[1]);
  assign controlled_buffer_2_out = or_1_out ? blc_rand_1_p2 : 1'bz;  // Controlled_Buffer controlled_buffer_2
  Pull_Resistor pull_resistor_3 (.node(controlled_buffer_2_out));
  Divider #(.width(7)) divider_1 (.a(multiplexer_3_out), .b(7'b0001000), .rem(divider_1_rem));  // open: out, upper
  Counter #(.width(3), .max('h7)) counter_2 (
    .carry(counter_2_carry), .clk(controlled_buffer_2_out));  // open: load, D, count, Q, clr
  Comparator #(.width(7)) comparator_2 (.a({7{1'b0}}), .b(divider_1_rem), .eq(comparator_2_eq));  // open: gt, lt
  and and_2 (and_2_out, comparator_2_eq, counter_2_carry);
  Demultiplexer #(.width(7)) demultiplexer_1 (
    .out0(demultiplexer_1_out0), .out1(demultiplexer_1_out1), .in(gpu_manager_1_out_3));  // open: sel, en
  RAM #(.addrWidth(7), .dataWidth(2), .bus("separate")) ram_2 (
    .addr(demultiplexer_1_out0), .data(ram_2_data));  // open: din, str, sel, clk, ld, clr
  RAM #(.addrWidth(7), .dataWidth(2), .bus("separate")) ram_3 (
    .addr(demultiplexer_1_out1), .data(ram_3_data));  // open: din, str, sel, clk, ld, clr
  Multiplexer #(.width(2)) multiplexer_4 (
    .in0(ram_2_data), .in1(ram_3_data), .out(multiplexer_4_out));  // open: sel, en
  GPU_manager gpu_manager_1 (
    .in_1(multiplexer_4_out), .out_3(gpu_manager_1_out_3), .out_4(gpu_manager_1_out_4),
    .out_5(gpu_manager_1_out_5), .out_6(gpu_manager_1_out_6), .out_7(gpu_manager_1_out_7));  // open: in_2
  // GPU gpu_1: pin names not known; wires that end beside it: gpu_manager_1_out_4, gpu_manager_1_out_5, gpu_manager_1_out_6, gpu_manager_1_out_7, gpu_1_p5, gpu_1_p6, gpu_1_p7, gpu_1_p8, gpu_1_p9, gpu_1_p10, gpu_1_p11, gpu_1_p12, gpu_1_p13, gpu_1_p14, gpu_1_p15, gpu_1_p16, gpu_1_p17, gpu_1_p18, gpu_1_p19, gpu_1_p20
  DotMatrix #(.inputtype("row"), .matrixcols(8), .matrixrows(16)) dotmatrix_1 (
    .row0(gpu_1_p5), .row1(gpu_1_p6), .row2(gpu_1_p7), .row3(gpu_1_p8), .row4(gpu_1_p9), .row5(gpu_1_p10),
    .row6(gpu_1_p11), .row7(gpu_1_p12), .row8(gpu_1_p13), .row9(gpu_1_p14), .row10(gpu_1_p15),
    .row11(gpu_1_p16), .row12(gpu_1_p17), .row13(gpu_1_p18), .row14(gpu_1_p19), .row15(gpu_1_p20));
endmodule
