// Logisim project GPU.circ as structural Verilog: 1 circuit, main circuit GPU
module GPU (
  input  [3:0] Score,
  input  [6:0] in_2,
  input  Game_Over,
  input  in_4,
  input  in_5,
  input  in_6,
  output [7:0] out_7,
  output [7:0] out_8,
  output [7:0] out_9,
  output [7:0] out_10,
  output [7:0] out_11,
  output [7:0] out_12,
  output [7:0] out_13,
  output [7:0] out_14,
  output [7:0] out_15,
  output [7:0] out_16,
  output [7:0] out_17,
  output [7:0] out_18,
  output [7:0] out_19,
  output [7:0] out_20,
  output [7:0] out_21,
  output [7:0] out_22
);

  wire pull_resistor_1_node;
  wire [2:0] counter_1_q;
  wire [3:0] bit_extender_3_out, multiplexer_1_out;
  wire [6:0] adder_1_out, adder_2_out, bit_extender_1_out, bit_extender_2_out, divider_1_out, divider_1_rem,
       divider_2_out, divider_2_rem, multiplier_1_out, multiplier_2_out;
  wire [7:0] demultiplexer_1_out7, demultiplexer_2_out0, demultiplexer_2_out1, demultiplexer_2_out2,
       demultiplexer_2_out3, demultiplexer_2_out4, demultiplexer_2_out5, demultiplexer_2_out6,
       demultiplexer_2_out7, demultiplexer_2_out8, demultiplexer_2_out9, demultiplexer_2_out10,
       demultiplexer_2_out11, demultiplexer_2_out12, demultiplexer_2_out13, demultiplexer_2_out14,
       demultiplexer_2_out15, multiplexer_2_out, rom_2_data;

  Pull_Resistor pull_resistor_1 (.node(pull_resistor_1_node));
  assign bit_extender_1_out = {{3{1'b0}}, Score};  // Bit_Extender bit_extender_1
  Counter #(.width(3), .max('h7), .ongoal("stay")) counter_1 (
    .Q(counter_1_q), .clk(pull_resistor_1_node));  // open: load, D, count, carry, clr
  assign pull_resistor_1_node = Game_Over ? in_5 : 1'bz;  // Controlled_Buffer controlled_buffer_1
  Divider #(.width(7)) divider_1 (
    .a(bit_extender_1_out), .b(7'b0001010), .out(divider_1_out), .rem(divider_1_rem));  // open: upper
  Multiplier #(.width(7)) multiplier_1 (.a(divider_1_out), .b(7'b0001000), .out(multiplier_1_out));  // open: cin, cout
  Multiplier #(.width(7)) multiplier_2 (.a(divider_1_rem), .b(7'b0001000), .out(multiplier_2_out));  // open: cin, cout
  assign bit_extender_2_out = {{4{1'b0}}, counter_1_q};  // Bit_Extender bit_extender_2
  Divider #(.width(7)) divider_2 (.a(in_2), .b(7'b0001000), .out(divider_2_out), .rem(divider_2_rem));  // open: upper
  Adder #(.width(7)) adder_1 (.a(multiplier_1_out), .b(bit_extender_2_out), .out(adder_1_out));  // open: cin, cout
  Adder #(.width(7)) adder_2 (.a(multiplier_2_out), .b(bit_extender_2_out), .out(adder_2_out));  // open: cin, cout
  assign bit_extender_3_out = {{1{1'b0}}, counter_1_q};  // Bit_Extender bit_extender_3
  Demultiplexer #(.select(3)) demultiplexer_1 (
    .out0(demultiplexer_1_out7[7]), .out1(demultiplexer_1_out7[6]), .out2(demultiplexer_1_out7[5]),
    .out3(demultiplexer_1_out7[4]), .out4(demultiplexer_1_out7[3]), .out5(demultiplexer_1_out7[2]),
    .out6(demultiplexer_1_out7[1]), .out7(demultiplexer_1_out7[0]), .in(1'b1), .sel(divider_2_rem[2:0]));  // open: en
  Multiplexer #(.width(4), .enable("false")) multiplexer_1 (
    .in0(divider_2_out[3:0]), .in1(bit_extender_3_out), .out(multiplexer_1_out), .sel(Game_Over));
  ROM #(.addrWidth(7), .dataWidth(4)) rom_1 (.addr(adder_1_out), .data(rom_2_data[7:4]));  // open: sel
  ROM #(.addrWidth(7), .dataWidth(4)) rom_2 (.addr(adder_2_out), .data(rom_2_data[3:0]));  // open: sel
  Multiplexer #(.width(8), .enable("false")) multiplexer_2 (
    .in0(demultiplexer_1_out7), .in1(rom_2_data), .out(multiplexer_2_out), .sel(Game_Over));
  Demultiplexer #(.select(4), .width(8)) demultiplexer_2 (
    .out0(demultiplexer_2_out0), .out1(demultiplexer_2_out1), .out2(demultiplexer_2_out2),
    .out3(demultiplexer_2_out3), .out4(demultiplexer_2_out4), .out5(demultiplexer_2_out5),
    .out6(demultiplexer_2_out6), .out7(demultiplexer_2_out7), .out8(demultiplexer_2_out8),
    .out9(demultiplexer_2_out9), .out10(demultiplexer_2_out10), .out11(demultiplexer_2_out11),
    .out12(demultiplexer_2_out12), .out13(demultiplexer_2_out13), .out14(demultiplexer_2_out14),
    .out15(demultiplexer_2_out15), .in(multiplexer_2_out), .sel(multiplexer_1_out));  // open: en
  _8IO_Buffer u_8io_buffer_1 (
    .in_1(demultiplexer_2_out8), .in_2(demultiplexer_2_out9), .in_3(demultiplexer_2_out10),
    .in_4(demultiplexer_2_out11), .in_5(demultiplexer_2_out12), .in_6(demultiplexer_2_out13),
    .in_7(demultiplexer_2_out14), .in_8(demultiplexer_2_out15), .out_12(out_15), .out_13(out_16),
    .out_14(out_17), .out_15(out_18), .out_16(out_19), .out_17(out_20), .out_18(out_21), .out_19(out_22),
    .in_9(in_4), .in_10(in_5), .in_11(in_6));
  _8IO_Buffer u_8io_buffer_2 (
    .in_1(demultiplexer_2_out0), .in_2(demultiplexer_2_out1), .in_3(demultiplexer_2_out2),
    .in_4(demultiplexer_2_out3), .in_5(demultiplexer_2_out4), .in_6(demultiplexer_2_out5),
    .in_7(demultiplexer_2_out6), .in_8(demultiplexer_2_out7), .out_12(out_7), .out_13(out_8), .out_14(out_9),
    .out_15(out_10), .out_16(out_11), .out_17(out_12), .out_18(out_13), .out_19(out_14), .in_9(in_4),
    .in_10(in_5), .in_11(in_6));

  // Notes on the sheet:
  //   contents of rom_1 (hex, n*v repeats v):
  //   6 6*9 6 1 3 5 5*1 6 9 2 4 4 8 8 f e 1 1 6 1 1 1 e 8 8 a a f 2 2 2 f 8 8 e 1 1 1 e 0 3 4 8 e 9 9 6 f
  //   1 1 2 7 4 8 8 6 9 9 6 9 9 9 6 6 9 9 7 2 4 c
  //   contents of rom_2 (hex, n*v repeats v):
  //   6 6*9 6 1 3 5 5*1 6 9 2 4 4 8 8 f e 1 1 6 1 1 1 e 8 8 a a f 2 2 2 f 8 8 e 1 1 1 e 0 3 4 8 e 9 9 6 f
  //   1 1 2 7 4 8 8 6 9 9 6 9 9 9 6 6 9 9 7 2 4 c
endmodule
