// Logisim project GPUman.circ as structural Verilog: 1 circuit, main circuit GPU manager
module GPU_manager (
  input  [1:0] in_1,
  input  ENABLE,
  input  in_3,
  output [6:0] out_4,
  output [6:0] out_5,
  output out_6,
  output out_7,
  output out_8,
  output out_9
);

  wire and_1_out, and_2_out, and_3_out, comparator_1_eq, counter_1_carry, d_ff_2_qn, d_ff_3_qn,
       multiplexer_1_out, or_1_out, or_2_out, pull_resistor_1_node, t_ff_1_q, t_ff_1_qn;
  wire [1:1] d_ff_2_q;
  wire [2:2] t_ff_2_q;

  D_Flip_Flop d_ff_1 (.clk(in_3), .D(counter_1_carry), .Q(out_9));  // open: Qn, preset, en, reset
  and and_1 (and_1_out, ENABLE, in_3);
  and and_2 (and_2_out, ~out_6, ~d_ff_2_q[1], t_ff_2_q[2]);  // AND_Gate
  Counter #(.width(7), .max('h7f), .trigger("falling")) counter_1 (
    .Q(out_4), .carry(counter_1_carry), .clk(pull_resistor_1_node));  // open: load, D, count, clr
  Pull_Resistor pull_resistor_1 (.node(pull_resistor_1_node));
  assign pull_resistor_1_node = t_ff_1_q ? and_1_out : 1'bz;  // Controlled_Buffer controlled_buffer_1
  or or_1 (or_1_out, counter_1_carry, and_2_out);
  Comparator #(.width(7)) comparator_1 (.a(out_4), .b({7{1'b0}}), .eq(comparator_1_eq));  // open: gt, lt
  T_Flip_Flop t_ff_1 (.clk(and_1_out), .T(or_1_out), .Q(t_ff_1_q), .Qn(t_ff_1_qn));  // open: preset, reset, en
  D_Flip_Flop d_ff_2 (.clk(t_ff_2_q[2]), .D(d_ff_2_qn), .Q(d_ff_2_q[1]), .Qn(d_ff_2_qn));  // open: preset, en, reset
  T_Flip_Flop t_ff_2 (.clk(and_1_out), .T(comparator_1_eq), .Q(t_ff_2_q[2]));  // open: Qn, preset, reset, en
  or or_2 (or_2_out, in_1[0], in_1[1]);
  and and_3 (and_3_out, d_ff_2_q[1], out_6);
  D_Flip_Flop d_ff_3 (.clk(d_ff_2_qn), .D(d_ff_3_qn), .Q(out_6), .Qn(d_ff_3_qn));  // open: preset, en, reset
  Multiplexer #(.disabled(0)) multiplexer_1 (
    .in0(or_2_out), .in1(and_3_out), .out(multiplexer_1_out), .sel(t_ff_1_qn));  // open: en
  assign out_7 = multiplexer_1_out ? and_1_out : 1'bz;  // Controlled_Buffer controlled_buffer_2
  Pull_Resistor pull_resistor_2 (.node(out_7));
  and and_4 (out_8, d_ff_2_q[1], ~out_6);  // AND_Gate

  assign out_5 = out_4;
endmodule
