// Logisim project Game_over.circ as structural Verilog: 1 circuit, main circuit GAME_OVER
module GAME_OVER (
  input  [6:0] GAME_ADRESS,
  input  GAME_CLK,
  input  [1:0] GAME_STATE,
  output GAME_OVER
);

  wire and_1_out, and_2_out, controlled_buffer_1_out, main_1_a_b_2, main_2_a_b_2, main_3_a_b_2,
       n7bit_comparator_1_out_3, n7bit_comparator_2_out_5, n7bit_comparator_3_out_4, not_1_out, or_1_out;
  wire [1:0] ram_1_data, ram_2_data;
  wire [6:0] divider_1_out, multiplier_1_out, subtractor_1_out;

  RAM #(.addrWidth(7), .dataWidth(2), .bus("separate")) ram_1 (
    .addr(GAME_ADRESS), .din(GAME_STATE), .data(ram_1_data), .clk(GAME_CLK));  // open: str, sel, ld, clr
  Divider #(.width(7)) divider_1 (.a(GAME_ADRESS), .b(7'b0001000), .out(divider_1_out));  // open: upper, rem
  Multiplier #(.width(7)) multiplier_1 (.a(divider_1_out), .b(7'b0001000), .out(multiplier_1_out));  // open: cin, cout
  not not_1 (not_1_out, GAME_CLK);
  Subtractor #(.width(7)) subtractor_1 (
    .a(GAME_ADRESS), .b(multiplier_1_out), .out(subtractor_1_out));  // open: bin, bout
  _7bit_comparator u_7bit_comparator_1 (
    .gen_adress(subtractor_1_out), .game_adress(7'b0000001), .out_3(n7bit_comparator_1_out_3));  // open: out_4, out_5
  _7bit_comparator u_7bit_comparator_2 (
    .gen_adress(subtractor_1_out), .game_adress(7'b0000110), .out_5(n7bit_comparator_2_out_5));  // open: out_3, out_4
  and and_1 (and_1_out, n7bit_comparator_1_out_3, n7bit_comparator_2_out_5);
  assign controlled_buffer_1_out = and_1_out ? not_1_out : 1'bz;  // Controlled_Buffer controlled_buffer_1
  Pull_Resistor pull_resistor_1 (.node(controlled_buffer_1_out));
  _7bit_comparator u_7bit_comparator_3 (
    .gen_adress(GAME_ADRESS), .game_adress(GAME_ADRESS), .out_4(n7bit_comparator_3_out_4));  // open: out_3, out_5
  _2bit_comparator_main main_1 (.in_1(ram_1_data), .in_2(2'b10), .A_B_2(main_1_a_b_2));  // open: A_B, A_B_3
  _2bit_comparator_main main_2 (.in_1(ram_2_data), .in_2(2'b01), .A_B_2(main_2_a_b_2));  // open: A_B, A_B_3
  or or_1 (or_1_out, main_2_a_b_2, main_3_a_b_2);
  _2bit_comparator_main main_3 (.in_1(ram_2_data), .in_2(2'b10), .A_B_2(main_3_a_b_2));  // open: A_B, A_B_3
  RAM #(.addrWidth(7), .dataWidth(2), .bus("separate")) ram_2 (
    .addr(GAME_ADRESS), .din(ram_1_data), .data(ram_2_data), .clk(controlled_buffer_1_out));  // open: str, sel, ld, clr
  assign GAME_OVER = n7bit_comparator_3_out_4 ? and_2_out : 1'bz;  // Controlled_Buffer controlled_buffer_2
  and and_2 (and_2_out, or_1_out, main_1_a_b_2);
  Pull_Resistor pull_resistor_2 (.node(GAME_OVER));
endmodule
