// Logisim project MemorySelector.circ as structural Verilog: 1 circuit, main circuit MemorySelection
module MemorySelection (
  input  [6:0] Adress_1,
  input  [1:0] Data_Output_1,
  input  [1:0] Data_Output_2,
  input  [1:0] Data_Input_1,
  input  [1:0] Data_Input_2,
  input  [6:0] Adress_2,
  input  Select,
  input  Store_1_Input,
  input  Store_2_Input,
  input  Ram_1_Input,
  input  Ram_2_Input,
  output [6:0] Adress_1_2,
  output [1:0] Data_Output_1_2,
  output [1:0] Data_Output_2_2,
  output [1:0] Data_Input_1_2,
  output [1:0] Data_Input_2_2,
  output [6:0] Adress_2_2,
  output Store_1_Output,
  output Store_2_Output,
  output Ram_1_Output,
  output Ram_2_Output
);

  wire not_1_out, not_2_out, not_3_out, not_4_out, not_5_out;

  Multiplexer #(.width(7)) multiplexer_1 (.in0(Adress_1), .in1(Adress_2), .out(Adress_1_2), .sel(Select));  // open: en
  Multiplexer #(.width(7)) multiplexer_2 (
    .in0(Adress_1), .in1(Adress_2), .out(Adress_2_2), .sel(not_1_out));  // open: en
  not not_1 (not_1_out, Select);
  Multiplexer #(.width(2)) multiplexer_3 (
    .in0(Data_Input_1), .in1(Data_Input_2), .out(Data_Input_1_2), .sel(Select));  // open: en
  Multiplexer multiplexer_4 (.in0(Store_1_Input), .in1(Store_2_Input), .out(Store_1_Output), .sel(Select));  // open: en
  not not_2 (not_2_out, Select);
  Multiplexer multiplexer_5 (.in0(Ram_1_Input), .in1(Ram_2_Input), .out(Ram_1_Output), .sel(Select));  // open: en
  not not_3 (not_3_out, Select);
  Multiplexer #(.width(2)) multiplexer_6 (
    .in0(Data_Input_1), .in1(Data_Input_2), .out(Data_Input_2_2), .sel(not_4_out));  // open: en
  not not_4 (not_4_out, Select);
  Multiplexer multiplexer_7 (
    .in0(Store_1_Input), .in1(Store_2_Input), .out(Store_2_Output), .sel(not_2_out));  // open: en
  Multiplexer multiplexer_8 (.in0(Ram_1_Input), .in1(Ram_2_Input), .out(Ram_2_Output), .sel(not_3_out));  // open: en
  Multiplexer #(.width(2)) multiplexer_9 (
    .in0(Data_Output_1), .in1(Data_Output_2), .out(Data_Output_1_2), .sel(Select));  // open: en
  not not_5 (not_5_out, Select);
  Multiplexer #(.width(2)) multiplexer_10 (
    .in0(Data_Output_2), .in1(Data_Output_1), .out(Data_Output_2_2), .sel(not_5_out));  // open: en
endmodule
