// Logisim project StateSelector.circ as structural Verilog: 1 circuit, main circuit State Selector
module State_Selector (
  input  Keyboard__Input_Happened,
  input  GO,
  input  Deleting_Rows_Ended,
  input  Render,
  input  New_Block_Request,
  input  Generating_Ended,
  input  Player_Input_Ended,
  input  Falling_Ended,
  output [2:0] out_9
);

  wire and_1_out, comparator_1_eq, d_ff_1_q, not_1_out, or_1_out, pull_resistor_1_node;
  wire [2:0] multiplexer_1_out, multiplexer_2_out, register_1_q;

  and and_1 (and_1_out, comparator_1_eq, Keyboard__Input_Happened);
  Comparator #(.width(3)) comparator_1 (.a(3'b001), .b(out_9), .eq(comparator_1_eq));  // open: gt, lt
  Multiplexer #(.width(3)) multiplexer_1 (
    .in0(3'b010), .in1(3'b011), .out(multiplexer_1_out), .sel(and_1_out));  // open: en
  Multiplexer #(.select(5), .width(3)) multiplexer_2 (
    .in0(3'b000), .in1(3'b010), .in2(multiplexer_1_out), .in4(multiplexer_1_out), .in8(3'b101),
    .in16(3'b100), .out(multiplexer_2_out),
    .sel({Deleting_Rows_Ended, New_Block_Request, Generating_Ended, Falling_Ended, Player_Input_Ended}));  // open: in3, in5, in6, in7, in9, in10, in11, in12, in13, in14, in15, in17, in18, in19, in20, in21, in22, in23, in24, in25, in26, in27, in28, in29, in30, in31, en
  Register #(.width(3), .trigger("falling")) register_1 (
    .D(multiplexer_2_out), .Q(register_1_q), .clk(or_1_out));  // open: en, clr
  or or_1 (or_1_out, New_Block_Request, Generating_Ended, Deleting_Rows_Ended, Falling_Ended, Player_Input_Ended);
  Multiplexer #(.width(3)) multiplexer_3 (.in0(register_1_q), .in1(3'b001), .out(out_9), .sel(d_ff_1_q));  // open: en
  D_Flip_Flop d_ff_1 (.clk(or_1_out), .D(1'b1), .Q(d_ff_1_q), .reset(pull_resistor_1_node));  // open: Qn, preset, en
  Pull_Resistor pull_resistor_1 (.node(pull_resistor_1_node));
  assign pull_resistor_1_node = not_1_out ? Render : 1'bz;  // Controlled_Buffer controlled_buffer_1
  not not_1 (not_1_out, GO);

  // Notes on the sheet:
  //   1 Rendering
  //   2 Falling
  //   3 Player Input actions
  //   4 Generating Blocks
  //   5 Deleting Rows
  //   If state is 0 something is wrong
endmodule
