// Logisim project Usuwanierzedow.circ as structural Verilog: 1 circuit, main circuit Deleting Rows
module Deleting_Rows (
  input  in_1,
  input  [1:0] FROM_RAM_D,
  input  If_1_enables_circuit,
  input  CLK_input,
  output [7:0] out_5,
  output out_6,
  output [6:0] TO_RAM_adress,
  output [1:0] TO_RAM_D,
  output TO_RAM_CLK
);

  wire and_2_out, and_3_out, and_4_out, and_5_out, and_6_out, and_7_out, bitselector_1_out, CLK, CLR,
       comparator_1_eq, comparator_2_eq, comparator_3_lt, comparator_4_eq, comparator_5_eq,
       controlled_buffer_3_out, controlled_buffer_4_out, controlled_buffer_5_out, controlled_buffer_6_out,
       counter_1_carry, d_ff_1_q, or_1_out;
  wire [1:0] bit_extender_1_out, counter_2_q;
  wire [2:0] bit_extender_3_out, not_1_out;
  wire [3:0] bit_extender_2_out, counter_3_q, multiplexer_1_out, not_3_out;
  wire [6:0] divider_1_out, divider_1_rem, register_9_q, register_10_q;
  wire [7:0] not_2_out, ram_1_data, register_7_q;

  and and_1 (CLK, If_1_enables_circuit, CLK_input);
  or or_1 (or_1_out, counter_1_carry, CLR);
  Counter #(.width(7), .max('h7f)) counter_1 (
    .load(1'b1), .Q(TO_RAM_adress), .carry(counter_1_carry), .clk(CLK), .clr(controlled_buffer_3_out));  // open: D, count
  Comparator #(.width(2)) comparator_1 (.a(2'b10), .b(counter_2_q), .eq(comparator_1_eq));  // open: gt, lt
  Counter #(.width(2), .max('h3)) counter_2 (
    .Q(counter_2_q), .clk(or_1_out), .clr(CLR));  // open: load, D, count, carry
  Pull_Resistor pull_resistor_1 (.node(TO_RAM_D));
  assign TO_RAM_D = comparator_3_lt ? bit_extender_1_out : 2'bz;  // Controlled_Buffer controlled_buffer_1
  or or_2 (CLR, in_1, comparator_1_eq);
  assign bit_extender_1_out = {{1{1'b0}}, bitselector_1_out};  // Bit_Extender bit_extender_1
  BitSelector bitselector_1 (.in(ram_1_data), .out(bitselector_1_out), .sel(not_1_out));
  T_Flip_Flop t_ff_1 (.clk(comparator_1_eq), .T(1'b1), .Q(out_6), .reset(comparator_2_eq));  // open: Qn, preset, en
  Comparator #(.width(7)) comparator_2 (.a({7{1'b1}}), .b(TO_RAM_adress), .eq(comparator_2_eq));  // open: gt, lt
  Pull_Resistor pull_resistor_2 (.node(TO_RAM_CLK));
  assign TO_RAM_CLK = and_2_out ? CLK : 1'bz;  // Controlled_Buffer controlled_buffer_2
  and and_2 (and_2_out, comparator_3_lt, d_ff_1_q);
  Comparator #(.width(7), .mode("unsigned")) comparator_3 (
    .a(7'b0001000), .b(TO_RAM_adress), .lt(comparator_3_lt));  // open: gt, eq
  D_Flip_Flop d_ff_1 (.clk(controlled_buffer_3_out), .D(1'b1), .Q(d_ff_1_q), .reset(CLR));  // open: Qn, preset, en
  Register #(.width(1)) register_1 (.D(FROM_RAM_D[0]), .Q(register_7_q[7]), .clk(CLK), .clr(CLR));  // open: en
  assign not_1_out = ~bit_extender_3_out;  // NOT_Gate not_1, 3 bits wide
  Register #(.width(1)) register_2 (.D(register_7_q[7]), .Q(register_7_q[6]), .clk(CLK), .clr(CLR));  // open: en
  Register #(.width(1)) register_3 (.D(register_7_q[6]), .Q(register_7_q[5]), .clk(CLK), .clr(CLR));  // open: en
  Register #(.width(1)) register_4 (.D(register_7_q[5]), .Q(register_7_q[4]), .clk(CLK), .clr(CLR));  // open: en
  assign not_2_out = ~register_7_q;  // NOT_Gate not_2, 8 bits wide
  Register #(.width(1)) register_5 (.D(register_7_q[4]), .Q(register_7_q[3]), .clk(CLK), .clr(CLR));  // open: en
  Register #(.width(1)) register_6 (.D(register_7_q[3]), .Q(register_7_q[2]), .clk(CLK), .clr(CLR));  // open: en
  and and_3 (and_3_out, register_7_q[0], register_7_q[1], register_7_q[2], register_7_q[3], register_7_q[5], register_7_q[6], register_7_q[7], register_7_q[4]);
  and and_4 (and_4_out, not_2_out[0], not_2_out[1], not_2_out[2], not_2_out[3], not_2_out[5], not_2_out[6], not_2_out[7], not_2_out[4]);
  Register #(.width(1)) register_7 (.D(register_7_q[1]), .Q(register_7_q[0]), .clk(CLK), .clr(CLR));  // open: en
  Register #(.width(1)) register_8 (.D(register_7_q[2]), .Q(register_7_q[1]), .clk(CLK), .clr(CLR));  // open: en
  assign controlled_buffer_3_out = and_7_out ? and_4_out : 1'bz;  // Controlled_Buffer controlled_buffer_3
  Pull_Resistor pull_resistor_3 (.node(controlled_buffer_3_out));
  assign controlled_buffer_4_out = and_5_out ? CLK : 1'bz;  // Controlled_Buffer controlled_buffer_4
  Pull_Resistor pull_resistor_4 (.node(controlled_buffer_4_out));
  and and_5 (and_5_out, and_3_out, and_7_out);
  Counter #(.width(4), .max('hf)) counter_3 (
    .Q(counter_3_q), .clk(controlled_buffer_5_out), .clr(CLR));  // open: load, D, count, carry
  assign controlled_buffer_5_out = and_6_out ? CLK : 1'bz;  // Controlled_Buffer controlled_buffer_5
  and and_6 (and_6_out, ~and_3_out, ~d_ff_1_q, and_7_out);  // AND_Gate
  Divider #(.width(7)) divider_1 (
    .a(TO_RAM_adress), .b(7'b0001000), .out(divider_1_out), .rem(divider_1_rem));  // open: upper
  Counter counter_4 (.Q(out_5), .clk(controlled_buffer_4_out));  // open: load, D, count, carry, clr
  Multiplexer #(.width(4), .enable("false")) multiplexer_1 (
    .in0(counter_3_q), .in1(not_3_out), .out(multiplexer_1_out), .sel(d_ff_1_q));
  Bit_Extender #(.in_width(7), .out_width(4)) bit_extender_2 (.in(divider_1_out), .out(bit_extender_2_out));
  Register #(.width(7)) register_9 (.D(divider_1_rem), .Q(register_9_q), .clk(CLK), .clr(CLR));  // open: en
  Bit_Extender #(.in_width(7), .out_width(3)) bit_extender_3 (.in(divider_1_rem), .out(bit_extender_3_out));
  assign controlled_buffer_6_out = and_6_out ? CLK : 1'bz;  // Controlled_Buffer controlled_buffer_6
  assign not_3_out = ~bit_extender_2_out;  // NOT_Gate not_3, 4 bits wide
  Comparator #(.width(7)) comparator_4 (.a({7{1'b0}}), .b(register_9_q), .eq(comparator_4_eq));  // open: gt, lt
  Comparator #(.width(7)) comparator_5 (.a(7'b0000001), .b(register_10_q), .eq(comparator_5_eq));  // open: gt, lt
  Register #(.width(7)) register_10 (.D(register_9_q), .Q(register_10_q), .clk(CLK), .clr(CLR));  // open: en
  RAM #(.addrWidth(4), .bus("separate")) ram_1 (
    .addr(multiplexer_1_out), .din(register_7_q), .data(ram_1_data), .clk(controlled_buffer_6_out), .clr(CLR));  // open: str, sel, ld
  and and_7 (and_7_out, comparator_4_eq, comparator_5_eq);
endmodule
