// Logisim project blok.circ as structural Verilog: 1 circuit, main circuit main
module main (
  input  RAND_CLK,
  output _0,
  output _1,
  output _2,
  output _3,
  output _4,
  output _5,
  output _6,
  output _7,
  output _8,
  output _9,
  output _10,
  output _11,
  output _12,
  output _13,
  output _14,
  output _15
);

  wire A0, A1, A2, A3, A4, A5, A6, A7, A8, A9, A10, A11, A12, A13, A14, A15, B0, B1, B2, B3, B4, B5, B6, B7,
       B8, B9, B10, B11, B12, B13, B14, B15, C0, C1, C2, C3, C4, C5, C6, C7, C8, C9, C10, C11, C12, C13, C14,
       C15, D0, D1, D2, D3, D4, D5, D6, D7, D8, D9, D10, D11, D12, D13, D14, D15;
  wire [1:0] SELECT;

  kwadrat_main main_1 (
    ._0(A0), ._1(A1), ._2(A2), ._3(A3), ._4(A4), ._5(A5), ._6(A6), ._7(A7), ._8(A8), ._9(A9), ._10(A10),
    ._11(A11), ._12(A12), ._13(A13), ._14(A14), ._15(A15));
  linia_main main_2 (
    ._0(B0), ._1(B1), ._2(B2), ._3(B3), ._4(B4), ._5(B5), ._6(B6), ._7(B7), ._8(B8), ._9(B9), ._10(B10),
    ._11(B11), ._12(B12), ._13(B13), ._14(B14), ._15(B15));
  L_main main_3 (
    ._0(C0), ._1(C1), ._2(C2), ._3(C3), ._4(C4), ._5(C5), ._6(C6), ._7(C7), ._8(C8), ._9(C9), ._10(C10),
    ._11(C11), ._12(C12), ._13(C13), ._14(C14), ._15(C15));
  mostek_main main_4 (
    ._0(D0), ._1(D1), ._2(D2), ._3(D3), ._4(D4), ._5(D5), ._6(D6), ._7(D7), ._8(D8), ._9(D9), ._10(D10),
    ._11(D11), ._12(D12), ._13(D13), ._14(D14), ._15(D15));
  Multiplexer #(.select(2)) multiplexer_1 (.in0(A0), .in1(B0), .in2(C0), .in3(D0), .out(_0), .sel(SELECT));  // open: en
  Multiplexer #(.select(2)) multiplexer_2 (.in0(A1), .in1(B1), .in2(C1), .in3(D1), .out(_1), .sel(SELECT));  // open: en
  Multiplexer #(.select(2)) multiplexer_3 (.in0(A2), .in1(B2), .in2(C2), .in3(D2), .out(_2), .sel(SELECT));  // open: en
  Multiplexer #(.select(2)) multiplexer_4 (.in0(A3), .in1(B3), .in2(C3), .in3(D3), .out(_3), .sel(SELECT));  // open: en
  Multiplexer #(.select(2)) multiplexer_5 (.in0(A4), .in1(B4), .in2(C4), .in3(D4), .out(_4), .sel(SELECT));  // open: en
  Multiplexer #(.select(2)) multiplexer_6 (.in0(A5), .in1(B5), .in2(C5), .in3(D5), .out(_5), .sel(SELECT));  // open: en
  Multiplexer #(.select(2)) multiplexer_7 (.in0(A6), .in1(B6), .in2(C6), .in3(D6), .out(_6), .sel(SELECT));  // open: en
  Multiplexer #(.select(2)) multiplexer_8 (.in0(A7), .in1(B7), .in2(C7), .in3(D7), .out(_7), .sel(SELECT));  // open: en
  Multiplexer #(.select(2)) multiplexer_9 (.in0(A8), .in1(B8), .in2(C8), .in3(D8), .out(_8), .sel(SELECT));  // open: en
  Multiplexer #(.select(2)) multiplexer_10 (
    .in0(A9), .in1(B9), .in2(C9), .in3(D9), .out(_9), .sel(SELECT));  // open: en
  Multiplexer #(.select(2)) multiplexer_11 (
    .in0(A10), .in1(B10), .in2(C10), .in3(D10), .out(_10), .sel(SELECT));  // open: en
  Multiplexer #(.select(2)) multiplexer_12 (
    .in0(A11), .in1(B11), .in2(C11), .in3(D11), .out(_11), .sel(SELECT));  // open: en
  Multiplexer #(.select(2)) multiplexer_13 (
    .in0(A12), .in1(B12), .in2(C12), .in3(D12), .out(_12), .sel(SELECT));  // open: en
  Multiplexer #(.select(2)) multiplexer_14 (
    .in0(A13), .in1(B13), .in2(C13), .in3(D13), .out(_13), .sel(SELECT));  // open: en
  Multiplexer #(.select(2)) multiplexer_15 (
    .in0(A14), .in1(B14), .in2(C14), .in3(D14), .out(_14), .sel(SELECT));  // open: en
  Multiplexer #(.select(2)) multiplexer_16 (
    .in0(A15), .in1(B15), .in2(C15), .in3(D15), .out(_15), .sel(SELECT));  // open: en
  Random #(.width(2)) random_1 (.clk(RAND_CLK), .out(SELECT));  // open: next, clr

  // Other names for the same wires on the sheet: P0 = _0; P1 = _1; P2 = _2; P3 = _3; P4 = _4; P5 = _5; P6 = _6;
  //   P7 = _7; P8 = _8; P9 = _9; P10 = _10; P11 = _11; P12 = _12; P13 = _13; P14 = _14; P15 = _15
endmodule
