// Logisim project sprawdzenie_kolizji_generacja.circ as structural Verilog: 1 circuit, main circuit czy_zderzenie
module czy_zderzenie (
  input  N,
  input  [1:0] S,
  output OUT
);

  Multiplexer #(.select(3), .disabled(0)) multiplexer_1 (
    .in0(1'b0), .in1(1'b0), .in2(1'b0), .in3(1'b0), .in4(1'b0), .in5(1'b1), .in6(1'b0), .in7(1'b0),
    .out(OUT), .sel({N, S}));  // open: en
endmodule
