// Logisim project keyboardmanager.circ as structural Verilog: 1 circuit, main circuit Keyboard Manager
module Keyboard_Manager (
  input  [6:0] in_1,
  input  in_2,
  input  in_3,
  output [6:0] out_4,
  output out_5,
  output out_6
);

  wire comparator_1_eq, comparator_2_eq, comparator_3_eq, comparator_4_eq, comparator_5_eq, or_1_out;
  wire [6:0] controlled_buffer_1_out;

  assign controlled_buffer_1_out = comparator_5_eq ? in_1 : 7'bz;  // Controlled_Buffer controlled_buffer_1
  Pull_Resistor pull_resistor_1 (.node(controlled_buffer_1_out));
  Comparator #(.width(7)) comparator_1 (
    .a(7'b1110001), .b(controlled_buffer_1_out), .eq(comparator_1_eq));  // open: gt, lt
  Comparator #(.width(7)) comparator_2 (
    .a(controlled_buffer_1_out), .b(7'b1100101), .eq(comparator_2_eq));  // open: gt, lt
  Comparator #(.width(7)) comparator_3 (
    .a(7'b1100001), .b(controlled_buffer_1_out), .eq(comparator_3_eq));  // open: gt, lt
  Comparator #(.width(7)) comparator_4 (
    .a(controlled_buffer_1_out), .b(7'b1100100), .eq(comparator_4_eq));  // open: gt, lt
  or or_1 (or_1_out, comparator_1_eq, comparator_2_eq, comparator_3_eq, comparator_4_eq);
  Register #(.width(7)) register_1 (.D(controlled_buffer_1_out), .Q(out_4), .clk(or_1_out), .clr(in_3));  // open: en
  D_Flip_Flop d_ff_1 (.clk(or_1_out), .D(1'b1), .Q(out_6), .reset(in_3));  // open: Qn, preset, en
  Comparator #(.width(7)) comparator_5 (.a(out_4), .b({7{1'b0}}), .eq(comparator_5_eq));  // open: gt, lt

  assign out_5 = in_2;
endmodule
