// Logisim project adreso-latacz_normal.circ as structural Verilog: 1 circuit, main circuit adreso-latacz
module adreso_latacz (
  input  [6:0] ADRES_ROOT,
  input  CLK,
  input  RESET,
  output [6:0] NOWE_A1,
  output [6:0] ADRES_OUT,
  output FINISH
);

  wire comparator_1_eq, comparator_2_eq, comparator_3_eq, comparator_4_eq, or_1_out, register_1_q;
  wire [6:0] adder_1_out, counter_1_q, counter_2_q, counter_3_q, multiplier_1_out, subtractor_1_out;

  Adder #(.width(7)) adder_1 (.a(ADRES_ROOT), .b(7'b0100011), .out(adder_1_out));  // open: cin, cout
  Counter #(.width(7), .max('h3)) counter_1 (.Q(counter_1_q), .clk(CLK), .clr(RESET));  // open: load, D, count, carry
  Adder #(.width(7)) adder_2 (.a(ADRES_ROOT), .b(7'b0001000), .out(NOWE_A1));  // open: cin, cout
  Subtractor #(.width(7)) subtractor_1 (.a(adder_1_out), .b(counter_1_q), .out(subtractor_1_out));  // open: bin, bout
  Comparator #(.width(7), .mode("unsigned")) comparator_1 (
    .a(counter_1_q), .b({7{1'b0}}), .eq(comparator_1_eq));  // open: gt, lt
  Counter #(.width(7), .max('h27)) counter_2 (.Q(counter_2_q), .clk(CLK), .clr(RESET));  // open: load, D, count, carry
  Subtractor #(.width(7)) subtractor_2 (
    .a(subtractor_1_out), .b(multiplier_1_out), .out(ADRES_OUT));  // open: bin, bout
  Counter #(.width(7), .max('h4)) counter_3 (
    .Q(counter_3_q), .clk(comparator_1_eq), .clr(RESET));  // open: load, D, count, carry
  Comparator #(.width(7), .mode("unsigned")) comparator_2 (
    .a(counter_2_q), .b({7{1'b0}}), .eq(comparator_2_eq));  // open: gt, lt
  Comparator #(.width(7), .mode("unsigned")) comparator_3 (
    .a(counter_2_q), .b(7'b0000011), .eq(comparator_3_eq));  // open: gt, lt
  Comparator #(.width(7), .mode("unsigned")) comparator_4 (
    .a(counter_2_q), .b(7'b0000001), .eq(comparator_4_eq));  // open: gt, lt
  Multiplier #(.width(7)) multiplier_1 (.a(counter_3_q), .b(7'b0001000), .out(multiplier_1_out));  // open: cin, cout
  Register #(.width(1)) register_1 (.D(1'b1), .Q(register_1_q), .clk(comparator_3_eq), .clr(or_1_out));  // open: en
  or or_1 (or_1_out, comparator_4_eq, RESET);
  and and_1 (FINISH, comparator_2_eq, register_1_q);
  RAM #(.addrWidth(7), .dataWidth(2)) ram_1 (.addr(ADRES_OUT));  // open: data, sel, clk, ld, clr

  // Notes on the sheet:
  //   PRAWY DOLNY OD ROOT
endmodule
