// Logisim project polaczone_dzialanie_normal.circ as structural Verilog: 1 circuit, main circuit main
module main (
  input  [6:0] A1,
  input  [1:0] DATA_IN,
  input  CLK_ENABLED,
  input  RESET,
  output [6:0] NOWE_A1,
  output [6:0] A,
  output [1:0] DATA_OUT,
  output RAM_CLK,
  output ZDERZENIE,
  output FINISH
);

  adreso_latacz adreso_latacz_1 (
    .CLK(CLK_ENABLED), .ADRES_OUT(A), .FINISH(FINISH), .ADRES_ROOT(A1), .RESET(RESET), .NOWE_A1(NOWE_A1));
  wiersz_normal_main main_1 (
    .CLK(CLK_ENABLED), .DATA_OUT(DATA_OUT), .DATA_IN(DATA_IN), .RAM_CLK(RAM_CLK), .ZD_OUT(ZDERZENIE),
    .RESET(RESET));
endmodule
