// Logisim project opadanie.circ as structural Verilog: 1 circuit, main circuit main
module main (
  input  [6:0] A1,
  input  [1:0] DATA_IN,
  input  CLK,
  input  ENABLE,
  input  RESET,
  output [6:0] NOWE_A1,
  output [1:0] DATA_OUT,
  output [6:0] A,
  output RAM_CLK,
  output FINISH,
  output ZDERZENIE
);

  wire and_1_out, demultiplexer_3_out0, demultiplexer_3_out1, main_1_finish, main_1_ram_clk,
       main_1_zderzenie, main_2_finish, main_2_ram_clk, main_2_zderzenie, multiplexer_6_out, TRYB;
  wire [1:0] demultiplexer_2_out0, demultiplexer_2_out1, main_1_data_out, main_2_data_out;
  wire [6:0] demultiplexer_1_out0, demultiplexer_1_out1, main_1_a, main_1_nowe_a1, main_2_a, main_2_nowe_a1;

  and and_1 (and_1_out, CLK, ENABLE);
  Comparator #(.width(7), .mode("unsigned")) comparator_1 (.a(A1), .b(7'b1011111), .gt(TRYB));  // open: eq, lt
  Demultiplexer #(.width(7)) demultiplexer_1 (
    .out0(demultiplexer_1_out0), .out1(demultiplexer_1_out1), .in(A1), .sel(TRYB));  // open: en
  Demultiplexer #(.width(2)) demultiplexer_2 (
    .out0(demultiplexer_2_out0), .out1(demultiplexer_2_out1), .in(DATA_IN), .sel(TRYB));  // open: en
  Demultiplexer demultiplexer_3 (
    .out0(demultiplexer_3_out0), .out1(demultiplexer_3_out1), .in(and_1_out), .sel(TRYB));  // open: en
  polaczone_dzialanie_normal_main main_1 (
    .A1(demultiplexer_1_out0), .DATA_IN(demultiplexer_2_out0), .CLK_ENABLED(demultiplexer_3_out0),
    .A(main_1_a), .DATA_OUT(main_1_data_out), .RAM_CLK(main_1_ram_clk), .ZDERZENIE(main_1_zderzenie),
    .FINISH(main_1_finish), .RESET(RESET), .NOWE_A1(main_1_nowe_a1));
  polaczone_dzialanie_p4_main main_2 (
    .A1(demultiplexer_1_out1), .DATA_IN(demultiplexer_2_out1), .CLK_ENABLED(demultiplexer_3_out1),
    .A(main_2_a), .DATA_OUT(main_2_data_out), .RAM_CLK(main_2_ram_clk), .ZDERZENIE(main_2_zderzenie),
    .FINISH(main_2_finish), .RESET(RESET), .NOWE_A1(main_2_nowe_a1));
  Multiplexer #(.width(7)) multiplexer_1 (
    .in0(main_1_nowe_a1), .in1(main_2_nowe_a1), .out(NOWE_A1), .sel(TRYB));  // open: en
  Multiplexer #(.width(2)) multiplexer_2 (
    .in0(main_1_data_out), .in1(main_2_data_out), .out(DATA_OUT), .sel(TRYB));  // open: en
  Multiplexer #(.width(7)) multiplexer_3 (.in0(main_1_a), .in1(main_2_a), .out(A), .sel(TRYB));  // open: en
  Multiplexer multiplexer_4 (.in0(main_1_ram_clk), .in1(main_2_ram_clk), .out(RAM_CLK), .sel(TRYB));  // open: en
  Multiplexer multiplexer_5 (.in0(main_1_finish), .in1(main_2_finish), .out(FINISH), .sel(TRYB));  // open: en
  Multiplexer multiplexer_6 (
    .in0(main_1_zderzenie), .in1(main_2_zderzenie), .out(multiplexer_6_out), .sel(TRYB));  // open: en
  and and_2 (ZDERZENIE, FINISH, multiplexer_6_out);

  // Notes on the sheet:
  //   jeżeli większe niż 95 to tryb podłoga
  //   0 to normal
  //   1 to podloga
endmodule
