// Logisim project zamieniacz_prawo_bezsciany.circ as structural Verilog: 1 circuit, main circuit zamieniacz
module zamieniacz (
  input  WYSTAPILO_ZDERZENIE,
  input  [1:0] L,
  input  [1:0] P,
  output [1:0] L_2,
  output [1:0] P_2
);

  wire [3:0] undriven;
  wire [4:0] adder_1_out, multiplexer_1_out;

  Adder #(.width(5)) adder_1 (.a({1'b0, L, P}), .b(5'b10000), .out(adder_1_out));  // open: cin, cout
  Multiplexer #(.width(5)) multiplexer_1 (
    .in0({1'b0, L, P}), .in1(adder_1_out), .out(multiplexer_1_out), .sel(WYSTAPILO_ZDERZENIE));  // open: en
  Multiplexer #(.select(5), .width(4)) multiplexer_2 (
    .in0(4'b0000), .in1(4'b0001), .in2(undriven), .in4(4'b0100), .in5(4'b0101), .in8(4'b0010),
    .in16(4'b0000), .in17(4'b0001), .in18(4'b0010), .in20(4'b0100), .in21(4'b0101), .in22(4'b0110),
    .in24(4'b1000), .in25(4'b1001), .in26(4'b1010), .out({L_2, P_2}), .sel(multiplexer_1_out));  // open: in3, in6, in7, in9, in10, in11, in12, in13, in14, in15, in19, in23, in27, in28, in29, in30, in31, en
endmodule
