// Logisim project rotacja.circ as structural Verilog: 1 circuit, main circuit main
module main (
  input  [6:0] A1,
  input  RESET,
  input  CLK,
  input  ENABLE,
  input  [1:0] DATA_IN,
  input  FLAGA,
  output [1:0] DATA_OUT,
  output RAM_CLK,
  output ZD,
  output [6:0] A,
  output FINISH
);

  wire and_1_out, demultiplexer_2_out0, demultiplexer_2_out1, main_1_finish, main_1_ram_clk, main_1_zd_out,
       main_2_finish, main_2_ram_clk, main_2_zd_out, multiplexer_3_out;
  wire [1:0] demultiplexer_3_out0, demultiplexer_3_out1, main_1_data_out, main_2_data_out;
  wire [6:0] demultiplexer_1_out0, demultiplexer_1_out1, main_1_a, main_2_a;

  and and_1 (and_1_out, CLK, ENABLE);
  Demultiplexer #(.width(7)) demultiplexer_1 (
    .out0(demultiplexer_1_out0), .out1(demultiplexer_1_out1), .in(A1), .sel(FLAGA));  // open: en
  Demultiplexer demultiplexer_2 (
    .out0(demultiplexer_2_out0), .out1(demultiplexer_2_out1), .in(and_1_out), .sel(FLAGA));  // open: en
  Demultiplexer #(.width(2)) demultiplexer_3 (
    .out0(demultiplexer_3_out0), .out1(demultiplexer_3_out1), .in(DATA_IN), .sel(FLAGA));  // open: en
  rotacja_lewo_main main_1 (
    .A1(demultiplexer_1_out0), .DATA_IN(demultiplexer_3_out0), .CLK(demultiplexer_2_out0),
    .ZD_OUT(main_1_zd_out), .A(main_1_a), .FINISH(main_1_finish), .RAM_CLK(main_1_ram_clk),
    .DATA_OUT(main_1_data_out), .RESET(RESET));
  rotacja_prawo_main main_2 (
    .A1(demultiplexer_1_out1), .DATA_IN(demultiplexer_3_out1), .CLK(demultiplexer_2_out1),
    .ZD_OUT(main_2_zd_out), .A(main_2_a), .FINISH(main_2_finish), .RAM_CLK(main_2_ram_clk),
    .DATA_OUT(main_2_data_out), .RESET(RESET));
  Multiplexer #(.width(2)) multiplexer_1 (
    .in0(main_1_data_out), .in1(main_2_data_out), .out(DATA_OUT), .sel(FLAGA));  // open: en
  Multiplexer multiplexer_2 (.in0(main_1_ram_clk), .in1(main_2_ram_clk), .out(RAM_CLK), .sel(FLAGA));  // open: en
  Multiplexer multiplexer_3 (
    .in0(main_1_zd_out), .in1(main_2_zd_out), .out(multiplexer_3_out), .sel(FLAGA));  // open: en
  Multiplexer #(.width(7)) multiplexer_4 (.in0(main_1_a), .in1(main_2_a), .out(A), .sel(FLAGA));  // open: en
  Multiplexer multiplexer_5 (.in0(main_1_finish), .in1(main_2_finish), .out(FINISH), .sel(FLAGA));  // open: en
  and and_2 (ZD, multiplexer_3_out, FINISH);

  // Other names for the same wires on the sheet: R = RESET

  // Notes on the sheet:
  //   0 to lewo | 1 to prawo
endmodule
