// Logisim project test_generacja 3.circ as structural Verilog: 1 circuit, main circuit main
module main (
  input  [6:0] in_1,
  input  in_2,
  input  in_3,
  output out_4,
  output out_5
);

  wire clock_1_out, main_1_ram_clk, not_1_out;
  wire [1:0] main_1_data_out, ram_1_data;
  wire [6:0] main_1_a;

  Clock clock_1 (.out(clock_1_out));
  opadanie_main main_1 (
    .A1(in_1), .DATA_IN(ram_1_data), .CLK(clock_1_out), .ENABLE(not_1_out), .DATA_OUT(main_1_data_out),
    .A(main_1_a), .RAM_CLK(main_1_ram_clk), .FINISH(out_5), .ZDERZENIE(out_4), .RESET(in_3));
  not not_1 (not_1_out, out_5);
  RAM #(.addrWidth(7), .dataWidth(2), .bus("separate")) ram_1 (
    .addr(main_1_a), .din(main_1_data_out), .data(ram_1_data), .clk(main_1_ram_clk));  // open: str, sel, ld, clr
  RAM #(.addrWidth(7), .dataWidth(2), .bus("separate")) ram_2 (.addr(in_1));  // open: din, data, str, sel, clk, ld, clr

  // Notes on the sheet:
  //   na prezentacje: przy podlodze to od
  //   95 dec
  //   5F hex
  //   1011111 bin
  //   czyli włącznie od 1100000
  //   wchodzi w tryb p4
  //   (nie włącznie)
  //   ostatni wiersz przy 78
endmodule
