// Logisim project testowanie.circ as structural Verilog: 1 circuit, main circuit main
module main (
  input  [6:0] A1,
  input  ENABLE,
  output [6:0] NOWE_A1,
  output \CZY_RUCH_BYŁ_ZABLOKOWANY ,
  output FINISH_PRZESUW,
  output FINISH_ROT
);

  wire clock_1_out, demultiplexer_1_out0, demultiplexer_1_out1, demultiplexer_2_out0, demultiplexer_2_out1,
       keyboard_1_avail, main_1_ram_clk, main_1_zd, main_2_ram_clk, main_2_zd, main_3_flaga, main_3_flaga_2,
       main_3_trwajaca_akcja, multiplexer_2_out;
  wire [1:0] main_1_data_out, main_2_data_out, multiplexer_3_out, ram_1_data;
  wire [6:0] keyboard_1_data, main_1_a, main_2_a, multiplexer_1_out;

  Clock clock_1 (.out(clock_1_out));
  Demultiplexer demultiplexer_1 (
    .out0(demultiplexer_1_out0), .out1(demultiplexer_1_out1), .in(clock_1_out), .sel(main_3_trwajaca_akcja));  // open: en
  Demultiplexer demultiplexer_2 (
    .out0(demultiplexer_2_out0), .out1(demultiplexer_2_out1), .in(ENABLE), .sel(main_3_trwajaca_akcja));  // open: en
  Multiplexer #(.width(7)) multiplexer_1 (
    .in0(main_2_a), .in1(main_1_a), .out(multiplexer_1_out), .sel(main_3_trwajaca_akcja));  // open: en
  RAM #(.addrWidth(7), .dataWidth(2), .bus("separate")) ram_1 (
    .addr(multiplexer_1_out), .din(multiplexer_3_out), .data(ram_1_data), .clk(multiplexer_2_out));  // open: str, sel, ld, clr
  przesuwanie_main main_1 (
    .A1(A1), .CLK(demultiplexer_1_out1), .ENABLE(demultiplexer_2_out1), .DATA_IN(ram_1_data),
    .FLAGA(main_3_flaga), .NOWE_A1(NOWE_A1), .DATA_OUT(main_1_data_out), .RAM_CLK(main_1_ram_clk),
    .ZD(main_1_zd), .A(main_1_a), .FINISH(FINISH_PRZESUW));
  rotacja_main main_2 (
    .A1(A1), .CLK(demultiplexer_1_out0), .ENABLE(demultiplexer_2_out0), .DATA_IN(ram_1_data),
    .FLAGA(main_3_flaga_2), .DATA_OUT(main_2_data_out), .RAM_CLK(main_2_ram_clk), .ZD(main_2_zd),
    .A(main_2_a), .FINISH(FINISH_ROT));
  Multiplexer multiplexer_2 (
    .in0(main_2_ram_clk), .in1(main_1_ram_clk), .out(multiplexer_2_out), .sel(main_3_trwajaca_akcja));  // open: en
  Multiplexer #(.width(2)) multiplexer_3 (
    .in0(main_2_data_out), .in1(main_1_data_out), .out(multiplexer_3_out), .sel(main_3_trwajaca_akcja));  // open: en
  Keyboard keyboard_1 (.clk(clock_1_out), .avail(keyboard_1_avail), .data(keyboard_1_data));  // open: re, clr
  Multiplexer multiplexer_4 (
    .in0(main_2_zd), .in1(main_1_zd), .out(\CZY_RUCH_BYŁ_ZABLOKOWANY ), .sel(main_3_trwajaca_akcja));  // open: en
  koder_klawiatura_main main_3 (
    .wejscie_ASCI(keyboard_1_data), .CLK(keyboard_1_avail), .RESET(FINISH_PRZESUW), .FLAGA(main_3_flaga),
    .FLAGA_2(main_3_flaga_2), .RESET_2(FINISH_ROT), .TRWAJACA_AKCJA(main_3_trwajaca_akcja));

  // Notes on the sheet:
  //   ten finisz wystepuje ale od razu sie gasi, bo resetuje tez koder i zmienia flage akcji
endmodule
