// Logisim project testowanie_gen.circ as structural Verilog: 1 circuit, main circuit main
module main (
  input  in_1,
  input  ENABLE,
  output [6:0] NOWE_A1,
  output ZDERZENIE__GAME_OVER,
  output FINISH
);

  wire clock_1_out, main_1_ram_clk;
  wire [1:0] main_1_data_out, ram_1_data;
  wire [6:0] main_1_a;

  Clock clock_1 (.out(clock_1_out));
  generacja_main main_1 (
    .DATA_IN(ram_1_data), .CLK(clock_1_out), .ZD_OUT(ZDERZENIE__GAME_OVER), .A(main_1_a), .FINISH(FINISH),
    .RAM_CLK(main_1_ram_clk), .DATA_OUT(main_1_data_out), .RESET(in_1), .NOWE_A1(NOWE_A1), .ENABLE(ENABLE));
  RAM #(.addrWidth(7), .dataWidth(2), .bus("separate")) ram_1 (
    .addr(main_1_a), .din(main_1_data_out), .data(ram_1_data), .clk(main_1_ram_clk));  // open: str, sel, ld, clr
endmodule
