// Logisim project 8IO buffer.circ as structural Verilog: 1 circuit, main circuit 8IO Buffer
module _8IO_Buffer (
  input  [7:0] in_1,
  input  [7:0] in_2,
  input  [7:0] in_3,
  input  [7:0] in_4,
  input  [7:0] in_5,
  input  [7:0] in_6,
  input  [7:0] in_7,
  input  [7:0] in_8,
  input  in_9,
  input  in_10,
  input  in_11,
  output [7:0] out_12,
  output [7:0] out_13,
  output [7:0] out_14,
  output [7:0] out_15,
  output [7:0] out_16,
  output [7:0] out_17,
  output [7:0] out_18,
  output [7:0] out_19
);

  _1IO_Buffer u_1io_buffer_1 (.in_1(in_1), .out_5(out_12), .in_2(in_9), .in_3(in_10), .in_4(in_11));
  _1IO_Buffer u_1io_buffer_2 (.in_1(in_2), .out_5(out_13), .in_2(in_9), .in_3(in_10), .in_4(in_11));
  _1IO_Buffer u_1io_buffer_3 (.in_1(in_3), .out_5(out_14), .in_2(in_9), .in_3(in_10), .in_4(in_11));
  _1IO_Buffer u_1io_buffer_4 (.in_1(in_4), .out_5(out_15), .in_2(in_9), .in_3(in_10), .in_4(in_11));
  _1IO_Buffer u_1io_buffer_5 (.in_1(in_5), .out_5(out_16), .in_2(in_9), .in_3(in_10), .in_4(in_11));
  _1IO_Buffer u_1io_buffer_6 (.in_1(in_6), .out_5(out_17), .in_2(in_9), .in_3(in_10), .in_4(in_11));
  _1IO_Buffer u_1io_buffer_7 (.in_1(in_7), .out_5(out_18), .in_2(in_9), .in_3(in_10), .in_4(in_11));
  _1IO_Buffer u_1io_buffer_8 (.in_1(in_8), .out_5(out_19), .in_2(in_9), .in_3(in_10), .in_4(in_11));
endmodule
