// Logisim project kaskader_8bit.circ as structural Verilog: 1 circuit, main circuit main
module main (
  input  [1:0] DATA,
  input  CLK,
  output [1:0] Q0,
  output [1:0] Q1,
  output [1:0] Q2,
  output [1:0] Q3,
  output [1:0] Q4,
  output [1:0] Q5,
  output [1:0] Q6,
  output [1:0] Q6_2
);

  kaskader_1bit_main main_1 (.DATA_INPUT(DATA), .CLOCK(CLK), .WYJSCIE(Q0), .KTORY_W_KOLEJNOSCI(3'b000));
  kaskader_1bit_main main_2 (.DATA_INPUT(DATA), .CLOCK(CLK), .WYJSCIE(Q1), .KTORY_W_KOLEJNOSCI(3'b001));
  kaskader_1bit_main main_3 (.DATA_INPUT(DATA), .CLOCK(CLK), .WYJSCIE(Q2), .KTORY_W_KOLEJNOSCI(3'b010));
  kaskader_1bit_main main_4 (.DATA_INPUT(DATA), .CLOCK(CLK), .WYJSCIE(Q3), .KTORY_W_KOLEJNOSCI(3'b011));
  kaskader_1bit_main main_5 (.DATA_INPUT(DATA), .CLOCK(CLK), .WYJSCIE(Q4), .KTORY_W_KOLEJNOSCI(3'b100));
  kaskader_1bit_main main_6 (.DATA_INPUT(DATA), .CLOCK(CLK), .WYJSCIE(Q5), .KTORY_W_KOLEJNOSCI(3'b101));
  kaskader_1bit_main main_7 (.DATA_INPUT(DATA), .CLOCK(CLK), .WYJSCIE(Q6), .KTORY_W_KOLEJNOSCI(3'b110));
  kaskader_1bit_main main_8 (.DATA_INPUT(DATA), .CLOCK(CLK), .WYJSCIE(Q6_2), .KTORY_W_KOLEJNOSCI(3'b111));
endmodule
