// Logisim project komparator.circ as structural Verilog: 1 circuit, main circuit main
module main (
  input  A,
  input  B,
  input  poprzedni,
  output A_B,
  output A_B_2,
  output A_B_3
);

  wire nand_1_out, nand_2_out, nand_3_out, not_1_out, not_2_out;

  not not_1 (not_1_out, A);
  not not_2 (not_2_out, B);
  nand nand_1 (nand_1_out, A, not_2_out, poprzedni);
  nand nand_2 (nand_2_out, poprzedni, B, not_1_out);
  nand nand_3 (nand_3_out, nand_1_out, poprzedni, nand_2_out);
  not not_3 (A_B, nand_1_out);
  not not_4 (A_B_2, nand_3_out);
  not not_5 (A_B_3, nand_2_out);
endmodule
