// Logisim project pamiec - testowe1.circ as structural Verilog: 1 circuit, main circuit main
module main (
  input  [3:0] in_1,
  input  [6:0] GPU_ADRES,
  input  [1:0] in_3,
  input  CLOCK,
  output [1:0] out_5,
  output [1:0] out_6,
  output [1:0] out_7,
  output [1:0] out_8,
  output [1:0] out_9,
  output [1:0] out_10,
  output [1:0] out_11,
  output [1:0] out_12,
  output [3:0] out_13,
  output out_14,
  output out_15,
  output out_16,
  output out_17,
  output [1:0] out_18,
  output [1:0] WYJSCIE
);

  wire comparator_1_eq, pull_resistor_1_node, undriven;
  wire [1:0] multiplexer_1_out;
  wire [2:0] counter_2_q, counter_3_q;
  wire [6:0] counter_1_q;

  Counter #(.width(7), .max('h7f)) counter_1 (.Q(counter_1_q), .clk(CLOCK));  // open: load, D, count, carry, clr
  Clock clock_1 ();  // open: out
  Pull_Resistor pull_resistor_1 (.node(pull_resistor_1_node));
  Controlled_Buffer controlled_buffer_1 (.out(pull_resistor_1_node));  // open: in, en
  Counter #(.width(3), .max('h7), .ongoal("stay")) counter_2 (
    .Q(counter_2_q), .clk(CLOCK));  // open: load, D, count, carry, clr
  RAM #(.addrWidth(7), .dataWidth(2), .bus("separate")) ram_1 (
    .addr(counter_1_q), .din(in_3), .data(out_18), .clk(undriven));  // open: str, sel, ld, clr
  Comparator #(.width(3)) comparator_1 (.a(counter_2_q), .b(3'b111), .eq(comparator_1_eq));  // open: gt, lt
  // kaskader_8bit_main main_1: pin names not known; wires that end beside it: out_18, out_5, out_6, out_7, out_8, out_9, out_10, CLOCK, out_11, out_12
  Counter #(.width(3), .max('h7)) counter_3 (.Q(counter_3_q), .clk(CLOCK));  // open: load, D, count, carry, clr
  Multiplexer #(.select(3), .width(2)) multiplexer_1 (
    .in0(out_5), .in1(out_6), .in2(out_7), .in3(out_8), .in4(out_9), .in5(out_10), .in6(out_11),
    .in7(out_12), .out(multiplexer_1_out), .sel(counter_3_q));  // open: en
  \porównywacz_v1_dzialajace_main  main_2 (
    .BLOK_WYZEJ_WARTOSC(multiplexer_1_out), .BLOK_NIZEJ_WARTOSC(out_18), .A(out_14), .B(out_15), .C(out_16),
    .C_2(out_17));
  Multiplexer #(.select(4), .width(4)) multiplexer_2 (
    .in1(4'b0010), .in2(4'b0101), .in4(4'b0101), .out(out_13), .sel(in_1));  // open: in0, in3, in5, in6, in7, in8, in9, in10, in11, in12, in13, in14, in15, en

  assign WYJSCIE = out_18;

  // Notes on the sheet:
  //   ZROBIĆ ITEROWANIE OD DOŁU
  //   PAMIEc ktora na adres ma 1 wyzej niz to co w GPU adress i tam ustawiajaca to co ma sie ustawic
  //   rozwazyc wprowadzenie czwartego stanu puste-w sensie nie nadpisuj w glownej pamieci
  //   chociaz mozliwe ze nie bedzie potrzebne, jesli bedzie poprawnie przeiterowywac
  //   nastepnie gdy obiekt przeiteruje do tego miejsca to ustawiajaca w glownej pamieci to co ma
  //   JEDYNY POMYSŁ JAKI MAM: ZROBIĆ 16 PAMIĘCI KAŻDA OD JEDNEGO WIERSZA
  //   TODO ZAPIS POCZĄTKOWY NA PAMIĘĆ
  //   A-> ustawiamy wyzej na powietrze, nizej na ruchomy
  //   B-> wyzej na pelne, nizej na pelne
  //   A
  //   B
  //   D
  //   C
  //   TODO ZAPISYWANIE W RAM
  //   ZALEZNIE OD STANU
endmodule
