// Logisim project porównywacz_v1_dzialajace.circ as structural Verilog: 1 circuit, main circuit main
module main (
  input  [1:0] BLOK_WYZEJ_WARTOSC,
  input  [1:0] BLOK_NIZEJ_WARTOSC,
  output A,
  output B,
  output C,
  output C_2
);

  wire and_1_out, and_2_out, and_3_out, and_4_out, and_5_out, and_6_out, and_7_out, and_8_out, and_9_out,
       and_10_out, and_11_out, and_12_out, and_13_out, and_14_out, and_15_out, and_16_out, and_17_out,
       and_18_out;

  and and_1 (and_1_out, ~BLOK_WYZEJ_WARTOSC[0], 1'b1);  // AND_Gate
  and and_2 (and_2_out, BLOK_WYZEJ_WARTOSC[1], 1'b1);
  and and_3 (and_3_out, ~BLOK_NIZEJ_WARTOSC[0], 1'b1);  // AND_Gate
  and and_4 (and_4_out, ~BLOK_NIZEJ_WARTOSC[1], 1'b1);  // AND_Gate
  and and_5 (and_5_out, BLOK_NIZEJ_WARTOSC[0], 1'b1);
  and and_6 (and_6_out, ~BLOK_NIZEJ_WARTOSC[0], 1'b1);  // AND_Gate
  and and_7 (and_7_out, and_1_out, and_2_out);
  and and_8 (and_8_out, and_3_out, and_4_out);
  and and_9 (and_9_out, ~BLOK_WYZEJ_WARTOSC[0], 1'b1);  // AND_Gate
  and and_10 (and_10_out, and_9_out, and_11_out);
  and and_11 (and_11_out, BLOK_WYZEJ_WARTOSC[1], 1'b1);
  and and_12 (and_12_out, and_5_out, and_13_out);
  and and_13 (and_13_out, ~BLOK_NIZEJ_WARTOSC[1], 1'b1);  // AND_Gate
  and and_14 (and_14_out, ~BLOK_WYZEJ_WARTOSC[0], 1'b1);  // AND_Gate
  and and_15 (and_15_out, and_14_out, and_16_out);
  and and_16 (and_16_out, BLOK_WYZEJ_WARTOSC[1], 1'b1);
  and and_17 (and_17_out, and_6_out, and_18_out);
  and and_18 (and_18_out, BLOK_NIZEJ_WARTOSC[1], 1'b1);
  and and_19 (A, and_7_out, and_8_out);
  and and_20 (B, and_10_out, and_12_out);
  and and_21 (C, and_15_out, and_17_out);
  and and_22 (C_2, ~A, ~B);  // AND_Gate

  // Notes on the sheet:
  //   ruchomy 10
  //   powietrze 00
  //   pelny 01
  //   Jeżeli wyżej to ruchomy a niżej powietrze to zwróć 1 na A
  //   Jeżeli wyżej to powietrze i niżej to powietrze lub
  //   jeżeli wyżej to pełne i niżej to pełne lub
  //   jeżeli wyżej to pełne i niżej to powietrze lub
  //   jeżeli wyżej to powietrze i niżej to pełne to
  //   Jeżeli wyżej to ruchomy a niżej to pełny to zwróć jeden na B
  //   jeżeli wyżej jest ruchomy i niżej jest ruchomy to daj jeden na C
  //   lub jeżeli wyżej to powietrze/pełne a nizej to ruchomy to też
  //   nic nie rób i daj jeden na D
endmodule
