// Logisim project porównywacz_v2_porzucone.circ as structural Verilog: 1 circuit, main circuit main
module main (
  input  [1:0] BLOK_WYZEJ_WARTOSC,
  input  [1:0] BLOK_NIZEJ_WARTOSC,
  output [1:0] out_3,
  output [1:0] out_4,
  output [1:0] out_5
);

  assign out_3 = BLOK_WYZEJ_WARTOSC & 2'b10;  // AND_Gate and_1, 2 bits wide
  assign out_5 = BLOK_NIZEJ_WARTOSC & 2'b00;  // AND_Gate and_2, 2 bits wide
  assign out_4 = out_3 & out_5;  // AND_Gate and_3, 2 bits wide

  // Notes on the sheet:
  //   00 -> 0x0
  //   10-> 0x2
  //   01 -> 0x1
  //   ruchomy 10
  //   powietrze 00
  //   pelny 01
  //   Jeżeli wyżej to ruchomy a niżej powietrze to zwróć 1 na A
  //   Jeżeli wyżej to ruchomy a niżej to pełny to zwróć jeden na B
endmodule
