// Logisim project obnizanie_do_bloczku2.circ as structural Verilog: 1 circuit, main circuit main
module main (
  input  [1:0] DATA_IN,
  input  [6:0] A1,
  input  CLK,
  input  ENABLE,
  output [3:0] out_5,
  output [1:0] DATA_OUT,
  output [6:0] A,
  output [3:0] poprzednie__W,
  output \ZAMROŹ ,
  output RAM_CLK,
  output FINISH
);

  wire and_1_out, clock_1_out, main_1__0_3, main_1__0_4, main_1__0_5, main_1__0_6, main_1__0_7, main_1__0_8,
       or_2_out, or_3_out, or_4_out;
  wire [1:0] register_3_q;
  wire [2:0] counter_1_q;
  wire [6:0] adder_1_out, adder_2_out, counter_2_q, register_1_q, subtractor_1_out;

  Adder #(.width(7)) adder_1 (.a(A1), .b(7'b0011111), .out(adder_1_out));  // open: cin, cout
  Counter #(.width(3), .max('h7)) counter_1 (.Q(counter_1_q), .clk(and_1_out));  // open: load, D, count, carry, clr
  or or_1 (RAM_CLK, main_1__0_3, main_1__0_5);
  Clock clock_1 (.out(clock_1_out));
  or or_2 (or_2_out, clock_1_out, CLK);
  switch8bit_main main_1 (
    .INPUT(counter_1_q), ._0_3(main_1__0_3), ._0_4(main_1__0_4), ._0_5(main_1__0_5), ._0_6(main_1__0_6),
    ._0_7(main_1__0_7), ._0_8(main_1__0_8));  // open: _0, _0_2
  Counter #(.width(7), .max('h1f)) counter_2 (.Q(counter_2_q), .clk(main_1__0_8));  // open: load, D, count, carry, clr
  and and_1 (and_1_out, or_2_out, ENABLE);
  Multiplexer #(.width(7)) multiplexer_1 (.in0(register_1_q), .in1(adder_2_out), .out(A), .sel(or_3_out));  // open: en
  Adder #(.width(7)) adder_2 (.a(register_1_q), .b(7'b0001000), .out(adder_2_out));  // open: cin, cout
  Register #(.width(7)) register_1 (.D(subtractor_1_out), .Q(register_1_q), .clk(main_1__0_7));  // open: en, clr
  Subtractor #(.width(7)) subtractor_1 (.a(adder_1_out), .b(counter_2_q), .out(subtractor_1_out));  // open: bin, bout
  or or_3 (or_3_out, main_1__0_5, main_1__0_3, main_1__0_6);
  Comparator #(.width(7), .mode("unsigned")) comparator_1 (
    .a(counter_2_q), .b(7'b0011111), .eq(FINISH));  // open: gt, lt
  Register #(.width(2)) register_2 (.D(DATA_IN), .Q(poprzednie__W[3:2]), .clk(main_1__0_7));  // open: en, clr
  or or_4 (or_4_out, main_1__0_3, main_1__0_4);
  Multiplexer #(.select(4), .width(4)) multiplexer_2 (
    .in0(4'b0000), .in4(4'b0100));  // open: in1, in2, in3, in5, in6, in7, in8, in9, in10, in11, in12, in13, in14, in15, out, sel, en
  Multiplexer #(.width(2)) multiplexer_3 (.in0(2'b01), .in1(register_3_q), .out(DATA_OUT), .sel(or_4_out));  // open: en
  Comparator #(.width(4), .mode("unsigned")) comparator_2 (
    .a({poprzednie__W[3:2], DATA_IN}), .b(4'b0110), .eq(\ZAMROŹ ));  // open: gt, lt
  Register #(.width(2)) register_3 (.D(2'b00), .Q(register_3_q), .clk(main_1__0_6));  // open: en, clr

  assign out_5 = 4'b0001;
  assign poprzednie__W[1:0] = DATA_IN;

  // Notes on the sheet:
  //   4 w dol 7 w prawo
  //   zmodyfikowac ze dostaje prawy dolny
  //   aktualny adres weryfikowany
  //   N
  //   W
  //   refA
  //   aktualne (N)
endmodule
