// Logisim project adreso-latacz_podloga.circ as structural Verilog: 1 circuit, main circuit adreso-latacz
module adreso_latacz (
  input  [6:0] ADRES_ROOT,
  input  CLK,
  output [6:0] ADRES_OUT,
  output FINISH
);

  wire comparator_1_eq;
  wire [6:0] adder_1_out, counter_1_q, counter_2_q, counter_3_q, multiplier_1_out, subtractor_1_out;

  Adder #(.width(7)) adder_1 (.a(ADRES_ROOT), .b(7'b0011011), .out(adder_1_out));  // open: cin, cout
  Counter #(.width(7), .max('h3)) counter_1 (.Q(counter_1_q), .clk(CLK));  // open: load, D, count, carry, clr
  Subtractor #(.width(7)) subtractor_1 (.a(adder_1_out), .b(counter_1_q), .out(subtractor_1_out));  // open: bin, bout
  Comparator #(.width(7), .mode("unsigned")) comparator_1 (
    .a(counter_1_q), .b({7{1'b0}}), .eq(comparator_1_eq));  // open: gt, lt
  Counter #(.width(7), .max('h1f)) counter_2 (.Q(counter_2_q), .clk(CLK));  // open: load, D, count, carry, clr
  Subtractor #(.width(7)) subtractor_2 (
    .a(subtractor_1_out), .b(multiplier_1_out), .out(ADRES_OUT));  // open: bin, bout
  Counter #(.width(7), .max('h3)) counter_3 (
    .Q(counter_3_q), .clk(comparator_1_eq));  // open: load, D, count, carry, clr
  Comparator #(.width(7), .mode("unsigned")) comparator_2 (
    .a(counter_2_q), .b({7{1'b0}}), .eq(FINISH));  // open: gt, lt
  Multiplier #(.width(7)) multiplier_1 (.a(counter_3_q), .b(7'b0001000), .out(multiplier_1_out));  // open: cin, cout
  RAM #(.addrWidth(7), .dataWidth(2)) ram_1 (.addr(ADRES_OUT));  // open: data, sel, clk, ld, clr

  // Notes on the sheet:
  //   PRAWY DOLNY OD ROOT
endmodule
