// Logisim project warunkator.circ as structural Verilog: 1 circuit, main circuit main
module main (
  input  [6:0] A1,
  output NORMAL,
  output P4,
  output P3,
  output P2,
  output P2_2
);

  Comparator comparator_1 ();  // open: a, b, gt, eq, lt
endmodule
