// Logisim project wiersz_normal.circ as structural Verilog: 1 circuit, main circuit main
module main (
  input  [1:0] DATA_IN,
  input  CLK,
  output [1:0] DATA_OUT,
  output RAM_CLK
);

  wire and_1_out, comparator_1_eq, comparator_1_gt, comparator_1_lt, or_1_out, RESET;
  wire [1:0] logiczno_ustawiacz_norm_1_out_0, logiczno_ustawiacz_norm_1_out_0_2,
       logiczno_ustawiacz_norm_1_out_0_3, logiczno_ustawiacz_norm_1_out_0_4,
       logiczno_ustawiacz_norm_1_out_0_5, logiczno_ustawiacz_norm_1_out_1, logiczno_ustawiacz_norm_1_out_1_2,
       logiczno_ustawiacz_norm_1_out_1_3, logiczno_ustawiacz_norm_1_out_1_4,
       logiczno_ustawiacz_norm_1_out_1_5, logiczno_ustawiacz_norm_1_out_2, logiczno_ustawiacz_norm_1_out_2_2,
       logiczno_ustawiacz_norm_1_out_2_3, logiczno_ustawiacz_norm_1_out_2_4,
       logiczno_ustawiacz_norm_1_out_2_5, logiczno_ustawiacz_norm_1_out_3, logiczno_ustawiacz_norm_1_out_3_2,
       logiczno_ustawiacz_norm_1_out_3_3, logiczno_ustawiacz_norm_1_out_3_4,
       logiczno_ustawiacz_norm_1_out_3_5, main_1_data_out_0, main_1_data_out_1, main_1_data_out_2,
       main_1_data_out_3, main_1_data_out_4, main_1_data_out_5, main_1_data_out_6, main_1_data_out_7,
       main_1_data_out_8, main_1_data_out_9, main_1_data_out_10, main_1_data_out_11, main_1_data_out_12,
       main_1_data_out_13, main_1_data_out_14, main_1_data_out_15, main_1_data_out_16, main_1_data_out_17,
       main_1_data_out_18, main_1_data_out_19;
  wire [4:0] counter_3_q;
  wire [5:0] counter_1_q, counter_2_q;

  Counter #(.width(6), .max('h27)) counter_1 (.Q(counter_1_q), .clk(CLK));  // open: load, D, count, carry, clr
  Counter #(.width(6), .max('h27)) counter_2 (.Q(counter_2_q), .clk(CLK));  // open: load, D, count, carry, clr
  and and_1 (and_1_out, CLK, comparator_1_lt);
  Comparator #(.width(6), .mode("unsigned")) comparator_1 (
    .a(counter_1_q), .b(6'b010101), .gt(comparator_1_gt), .eq(comparator_1_eq), .lt(comparator_1_lt));
  Comparator #(.width(6), .mode("unsigned")) comparator_2 (.a(counter_2_q), .b({6{1'b0}}), .eq(RESET));  // open: gt, lt
  or or_1 (or_1_out, comparator_1_gt, comparator_1_eq);
  Counter #(.width(5), .max('h13)) counter_3 (.Q(counter_3_q), .clk(RAM_CLK));  // open: load, D, count, carry, clr
  logiczno_ustawiacz_norm logiczno_ustawiacz_norm_1 (
    .REG_0(main_1_data_out_0), .REG_1(main_1_data_out_1), .REG_2(main_1_data_out_2),
    .REG_3(main_1_data_out_3), .REG_0_2(main_1_data_out_4), .REG_1_2(main_1_data_out_5),
    .REG_2_2(main_1_data_out_6), .REG_3_2(main_1_data_out_7), .REG_0_3(main_1_data_out_8),
    .REG_1_3(main_1_data_out_9), .REG_2_3(main_1_data_out_10), .REG_3_3(main_1_data_out_11),
    .REG_0_4(main_1_data_out_12), .REG_1_4(main_1_data_out_13), .REG_2_4(main_1_data_out_14),
    .REG_3_4(main_1_data_out_15), .REG_0_5(main_1_data_out_16), .REG_1_5(main_1_data_out_17),
    .REG_2_5(main_1_data_out_18), .REG_3_5(main_1_data_out_19), .OUT_0(logiczno_ustawiacz_norm_1_out_0),
    .OUT_1(logiczno_ustawiacz_norm_1_out_1), .OUT_2(logiczno_ustawiacz_norm_1_out_2),
    .OUT_3(logiczno_ustawiacz_norm_1_out_3), .OUT_0_2(logiczno_ustawiacz_norm_1_out_0_2),
    .OUT_1_2(logiczno_ustawiacz_norm_1_out_1_2), .OUT_2_2(logiczno_ustawiacz_norm_1_out_2_2),
    .OUT_3_2(logiczno_ustawiacz_norm_1_out_3_2), .OUT_0_3(logiczno_ustawiacz_norm_1_out_0_3),
    .OUT_1_3(logiczno_ustawiacz_norm_1_out_1_3), .OUT_2_3(logiczno_ustawiacz_norm_1_out_2_3),
    .OUT_3_3(logiczno_ustawiacz_norm_1_out_3_3), .OUT_0_4(logiczno_ustawiacz_norm_1_out_0_4),
    .OUT_1_4(logiczno_ustawiacz_norm_1_out_1_4), .OUT_2_4(logiczno_ustawiacz_norm_1_out_2_4),
    .OUT_3_4(logiczno_ustawiacz_norm_1_out_3_4), .OUT_0_5(logiczno_ustawiacz_norm_1_out_0_5),
    .OUT_1_5(logiczno_ustawiacz_norm_1_out_1_5), .OUT_2_5(logiczno_ustawiacz_norm_1_out_2_5),
    .OUT_3_5(logiczno_ustawiacz_norm_1_out_3_5), .RESET(RESET));
  MEGA_register_normal_main main_1 (
    .DATA_IN(DATA_IN), .CLK(and_1_out), .DATA_OUT_0(main_1_data_out_0), .DATA_OUT_1(main_1_data_out_1),
    .DATA_OUT_2(main_1_data_out_2), .DATA_OUT_3(main_1_data_out_3), .DATA_OUT_4(main_1_data_out_4),
    .DATA_OUT_5(main_1_data_out_5), .DATA_OUT_6(main_1_data_out_6), .DATA_OUT_7(main_1_data_out_7),
    .DATA_OUT_8(main_1_data_out_8), .DATA_OUT_9(main_1_data_out_9), .DATA_OUT_10(main_1_data_out_10),
    .DATA_OUT_11(main_1_data_out_11), .DATA_OUT_12(main_1_data_out_12), .DATA_OUT_13(main_1_data_out_13),
    .DATA_OUT_14(main_1_data_out_14), .DATA_OUT_15(main_1_data_out_15), .DATA_OUT_16(main_1_data_out_16),
    .DATA_OUT_17(main_1_data_out_17), .DATA_OUT_18(main_1_data_out_18), .DATA_OUT_19(main_1_data_out_19));  // open: RESET
  and and_2 (RAM_CLK, or_1_out, CLK);
  Multiplexer #(.select(5), .width(2)) multiplexer_1 (
    .in0(logiczno_ustawiacz_norm_1_out_0), .in1(logiczno_ustawiacz_norm_1_out_1),
    .in2(logiczno_ustawiacz_norm_1_out_2), .in3(logiczno_ustawiacz_norm_1_out_3),
    .in4(logiczno_ustawiacz_norm_1_out_0_2), .in5(logiczno_ustawiacz_norm_1_out_1_2),
    .in6(logiczno_ustawiacz_norm_1_out_2_2), .in7(logiczno_ustawiacz_norm_1_out_3_2),
    .in8(logiczno_ustawiacz_norm_1_out_0_3), .in9(logiczno_ustawiacz_norm_1_out_1_3),
    .in10(logiczno_ustawiacz_norm_1_out_2_3), .in11(logiczno_ustawiacz_norm_1_out_3_3),
    .in12(logiczno_ustawiacz_norm_1_out_0_4), .in13(logiczno_ustawiacz_norm_1_out_1_4),
    .in14(logiczno_ustawiacz_norm_1_out_2_4), .in15(logiczno_ustawiacz_norm_1_out_3_4),
    .in16(logiczno_ustawiacz_norm_1_out_0_5), .in17(logiczno_ustawiacz_norm_1_out_1_5),
    .in18(logiczno_ustawiacz_norm_1_out_2_5), .in19(logiczno_ustawiacz_norm_1_out_3_5), .out(DATA_OUT),
    .sel(counter_3_q));  // open: in20, in21, in22, in23, in24, in25, in26, in27, in28, in29, in30, in31, en
endmodule
