// Logisim project adreso-latacz2.circ as structural Verilog: 1 circuit, main circuit adreso-latacz
module adreso_latacz (
  input  [6:0] ADRES_ROOT,
  input  CLK,
  output [6:0] ADRES_OUT,
  output FINISH
);

  wire comparator_1_eq, comparator_2_eq, counter_4_q;
  wire [1:0] counter_1_q;
  wire [6:0] adder_1_out, adder_2_out, counter_2_q, multiplexer_1_out, multiplexer_2_out, subtractor_1_out,
       subtractor_2_out, subtractor_3_out, T1;

  Adder #(.width(7)) adder_1 (.a(ADRES_ROOT), .b(7'b0011100), .out(adder_1_out));  // open: cin, cout
  Subtractor #(.width(7)) subtractor_1 (.a(adder_1_out), .b(7'b0001000), .out(subtractor_1_out));  // open: bin, bout
  Subtractor #(.width(7)) subtractor_2 (
    .a(subtractor_1_out), .b(7'b0001000), .out(subtractor_2_out));  // open: bin, bout
  Subtractor #(.width(7)) subtractor_3 (
    .a(subtractor_2_out), .b(7'b0001000), .out(subtractor_3_out));  // open: bin, bout
  Counter #(.width(2), .max('h3)) counter_1 (
    .Q(counter_1_q), .clk(comparator_1_eq));  // open: load, D, count, carry, clr
  Comparator #(.width(7), .mode("unsigned")) comparator_1 (
    .a(counter_2_q), .b(7'b0010000), .eq(comparator_1_eq));  // open: gt, lt
  Counter #(.width(7), .max('h3f)) counter_2 (.Q(counter_2_q), .clk(CLK));  // open: load, D, count, carry, clr
  Multiplexer #(.select(2), .width(7)) multiplexer_1 (
    .in0(adder_1_out), .in1(subtractor_1_out), .in2(subtractor_2_out), .in3(subtractor_3_out),
    .out(multiplexer_1_out), .sel(counter_1_q));  // open: en
  Comparator #(.width(7), .mode("unsigned")) comparator_2 (
    .a(counter_2_q), .b(7'b0000101), .eq(comparator_2_eq));  // open: gt, lt
  Counter #(.width(7), .max('h4)) counter_3 (.Q(T1), .clk(CLK));  // open: load, D, count, carry, clr
  Multiplexer #(.width(7)) multiplexer_2 (
    .in0(multiplexer_1_out), .in1(adder_2_out), .out(multiplexer_2_out), .sel(counter_4_q));  // open: en
  Counter #(.width(1), .max('h1)) counter_4 (
    .Q(counter_4_q), .clk(comparator_2_eq));  // open: load, D, count, carry, clr
  Subtractor #(.width(7)) subtractor_4 (.a(multiplexer_2_out), .b(T1), .out(ADRES_OUT));  // open: bin, bout
  Adder #(.width(7)) adder_2 (.a(multiplexer_1_out), .b(7'b0001000), .out(adder_2_out));  // open: cin, cout
  Comparator #(.width(7), .mode("unsigned")) comparator_3 (
    .a(counter_2_q), .b(7'b0111111), .eq(FINISH));  // open: gt, lt
  RAM #(.addrWidth(7), .dataWidth(2)) ram_1 (.addr(ADRES_OUT));  // open: data, sel, clk, ld, clr

  // Notes on the sheet:
  //   PRAWY DOLNY OD ROOT
  //   1 wiersz
  //   2 wiersz
  //   3 wiersz
  //   4 wiersz
endmodule
