// Logisim project adreso-latacz.circ as structural Verilog: 1 circuit, main circuit adreso-latacz
module adreso_latacz (
  input  [6:0] ADRES_ROOT,
  input  CLK,
  output [6:0] ADRES_OUT,
  output FINISH
);

  wire comparator_1_eq, comparator_2_eq, comparator_3_eq, counter_3_q, counter_4_q;
  wire [1:0] counter_2_q;
  wire [5:0] counter_5_q;
  wire [6:0] adder_1_out, adder_2_out, multiplexer_1_out, multiplexer_2_out, subtractor_1_out,
       subtractor_2_out, subtractor_3_out, T1;

  Counter #(.width(7), .max('h3)) counter_1 (.Q(T1), .clk(CLK));  // open: load, D, count, carry, clr
  Adder #(.width(7)) adder_1 (.a(ADRES_ROOT), .b(7'b0011011), .out(adder_1_out));  // open: cin, cout
  Subtractor #(.width(7)) subtractor_1 (.a(adder_1_out), .b(7'b0001000), .out(subtractor_1_out));  // open: bin, bout
  Subtractor #(.width(7)) subtractor_2 (
    .a(subtractor_1_out), .b(7'b0001000), .out(subtractor_2_out));  // open: bin, bout
  Subtractor #(.width(7)) subtractor_3 (
    .a(subtractor_2_out), .b(7'b0001000), .out(subtractor_3_out));  // open: bin, bout
  Comparator #(.width(7), .mode("unsigned")) comparator_1 (
    .a(T1), .b({7{1'b0}}), .eq(comparator_1_eq));  // open: gt, lt
  Counter #(.width(2), .max('h3)) counter_2 (
    .Q(counter_2_q), .clk(comparator_2_eq));  // open: load, D, count, carry, clr
  Comparator #(.width(1), .mode("unsigned")) comparator_2 (
    .a(counter_4_q), .b(1'b0), .eq(comparator_2_eq));  // open: gt, lt
  Multiplexer #(.select(2), .width(7)) multiplexer_1 (
    .in0(adder_1_out), .in1(subtractor_1_out), .in2(subtractor_2_out), .in3(subtractor_3_out),
    .out(multiplexer_1_out), .sel(counter_2_q));  // open: en
  Counter #(.width(1), .max('h1)) counter_3 (
    .Q(counter_3_q), .clk(comparator_1_eq));  // open: load, D, count, carry, clr
  Multiplexer #(.width(7)) multiplexer_2 (
    .in0(multiplexer_1_out), .in1(adder_2_out), .out(multiplexer_2_out), .sel(counter_3_q));  // open: en
  Comparator #(.width(1), .mode("unsigned")) comparator_3 (
    .a(counter_3_q), .b(1'b0), .eq(comparator_3_eq));  // open: gt, lt
  Counter #(.width(1), .max('h1)) counter_4 (
    .Q(counter_4_q), .clk(comparator_3_eq));  // open: load, D, count, carry, clr
  Subtractor #(.width(7)) subtractor_4 (.a(multiplexer_2_out), .b(T1), .out(ADRES_OUT));  // open: bin, bout
  Adder #(.width(7)) adder_2 (.a(multiplexer_1_out), .b(7'b0001000), .out(adder_2_out));  // open: cin, cout
  Counter #(.width(6), .max('h3f)) counter_5 (.Q(counter_5_q), .clk(CLK));  // open: load, D, count, carry, clr
  Comparator #(.width(6), .mode("unsigned")) comparator_4 (
    .a(counter_5_q), .b({6{1'b1}}), .eq(FINISH));  // open: gt, lt
  RAM #(.addrWidth(7), .dataWidth(2)) ram_1 (.addr(ADRES_OUT));  // open: data, sel, clk, ld, clr

  // Other names for the same wires on the sheet: T2 = CLK

  // Notes on the sheet:
  //   PRAWY DOLNY OD ROOT
  //   1 wiersz
  //   2 wiersz
  //   3 wiersz
  //   4 wiersz
endmodule
