// Logisim project obnizanie_do_bloczku3.circ as structural Verilog: 1 circuit, main circuit obnizanie
module obnizanie (
  input  [1:0] DATA_IN,
  input  [6:0] A1,
  input  CLK,
  input  ENABLE,
  output [1:0] DATA_OUT,
  output [6:0] A,
  output \ZAMROŹ ,
  output [3:0] out_8,
  output [3:0] out_9,
  output RAM_CLK,
  output FINISH
);

  wire a_t, and_1_out, comparator_1_eq, comparator_2_eq, comparator_3_eq, comparator_4_eq, comparator_5_eq,
       comparator_6_eq, demultiplexer_1_out0, demultiplexer_1_out1, demultiplexer_1_out2,
       demultiplexer_1_out3, demultiplexer_1_out4, demultiplexer_1_out5, demultiplexer_1_out6,
       demultiplexer_1_out7, demultiplexer_1_out8, demultiplexer_1_out9, demultiplexer_1_out10, or_2_out,
       undriven_3;
  wire [1:0] main_2_out, multiplexer_4_out, multiplexer_4_out_2, multiplexer_5_out, multiplexer_5_out_2,
       multiplexer_6_out, multiplexer_6_out_2, register_2_q, register_3_q, register_4_q;
  wire [2:0] counter_2_q, undriven;
  wire [3:0] counter_1_q, undriven_2;
  wire [6:0] adder_1_out, adder_2_out, counter_3_q, multiplexer_2_out, subtractor_1_out, subtractor_2_out,
       subtractor_3_out, subtractor_4_out;

  Adder #(.width(7)) adder_1 (.a(A1), .b(7'b0100100), .out(adder_1_out));  // open: cin, cout
  Counter #(.width(4), .max('hf)) counter_1 (.Q(counter_1_q), .clk(and_1_out));  // open: load, D, count, carry, clr
  or or_1 (RAM_CLK, demultiplexer_1_out6, demultiplexer_1_out8, demultiplexer_1_out10);
  Counter #(.width(3), .max('h7)) counter_2 (.Q(counter_2_q), .clk(and_1_out));  // open: load, D, count, carry, clr
  Demultiplexer #(.select(4), .disabled(0)) demultiplexer_1 (
    .out0(demultiplexer_1_out0), .out1(demultiplexer_1_out1), .out2(demultiplexer_1_out2),
    .out3(demultiplexer_1_out3), .out4(demultiplexer_1_out4), .out5(demultiplexer_1_out5),
    .out6(demultiplexer_1_out6), .out7(demultiplexer_1_out7), .out8(demultiplexer_1_out8),
    .out9(demultiplexer_1_out9), .out10(demultiplexer_1_out10), .out11(a_t), .in(1'b1), .sel(counter_1_q));  // open: out12, out13, out14, out15, en
  Counter #(.width(7), .max('hf)) counter_3 (
    .Q(counter_3_q), .clk(demultiplexer_1_out0));  // open: load, D, count, carry, clr
  switch8bit_main main_1 (.INPUT(counter_2_q));  // open: _0, _0_2, _0_3, _0_4, _0_5, _0_6, _0_7, _0_8
  and and_1 (and_1_out, CLK, ENABLE);
  Multiplexer #(.width(7)) multiplexer_1 (
    .in0(multiplexer_2_out), .in1(adder_2_out), .out(A), .en(or_2_out));  // open: sel
  Adder #(.width(7)) adder_2 (.a(multiplexer_2_out), .b(7'b0001000), .out(adder_2_out));  // open: cin, cout
  smart_selector_main main_2 (
    .OUT(main_2_out), ._0_0(demultiplexer_1_out2), ._0_1(demultiplexer_1_out5), ._1_0(demultiplexer_1_out3),
    ._1_1(demultiplexer_1_out6), ._2_0(demultiplexer_1_out4));  // open: _2_1
  Subtractor #(.width(7)) subtractor_1 (.a(adder_1_out), .b(counter_3_q), .out(subtractor_1_out));  // open: bin, bout
  or or_2 (or_2_out, demultiplexer_1_out5, demultiplexer_1_out6, demultiplexer_1_out8, demultiplexer_1_out10);
  Comparator #(.width(3), .mode("unsigned")) comparator_1 (
    .a(undriven), .b(3'b111), .eq(comparator_1_eq));  // open: gt, lt
  Comparator #(.width(7), .mode("unsigned")) comparator_2 (
    .a(counter_3_q), .b(7'b0011111), .eq(comparator_2_eq));  // open: gt, lt
  Multiplexer #(.select(2), .width(7)) multiplexer_2 (
    .in0(subtractor_1_out), .in1(subtractor_2_out), .in2(subtractor_3_out), .in3(subtractor_4_out),
    .out(multiplexer_2_out), .sel(main_2_out));  // open: en
  Subtractor #(.width(7)) subtractor_2 (
    .a(subtractor_1_out), .b(7'b0000001), .out(subtractor_2_out));  // open: bin, bout
  Subtractor #(.width(7)) subtractor_3 (
    .a(subtractor_2_out), .b(7'b0000001), .out(subtractor_3_out));  // open: bin, bout
  Subtractor #(.width(7)) subtractor_4 (
    .a(subtractor_3_out), .b(7'b0000001), .out(subtractor_4_out));  // open: bin, bout
  BitSelector bitselector_1 ();  // open: in, out, sel
  and and_2 (FINISH, comparator_1_eq, comparator_2_eq);
  Register #(.width(2)) register_1 (.D(DATA_IN), .Q(out_8[3:2]), .clk(demultiplexer_1_out1));  // open: en, clr
  Register #(.width(2)) register_2 (.D(DATA_IN), .Q(register_2_q), .clk(demultiplexer_1_out2));  // open: en, clr
  Register #(.width(2)) register_3 (.D(DATA_IN), .Q(register_3_q), .clk(demultiplexer_1_out3));  // open: en, clr
  Register #(.width(2)) register_4 (.D(DATA_IN), .Q(register_4_q), .clk(demultiplexer_1_out4));  // open: en, clr
  Comparator #(.width(2), .mode("unsigned")) comparator_3 (
    .a(out_8[3:2]), .b(2'b00), .eq(comparator_3_eq));  // open: gt, lt
  // NOT_Gate not_1 has open pins: in=comparator_3_eq, out=open
  Comparator #(.width(2), .mode("unsigned")) comparator_4 (
    .a(register_2_q), .b(2'b00), .eq(comparator_4_eq));  // open: gt, lt
  // NOT_Gate not_2 has open pins: in=comparator_4_eq, out=open
  Comparator #(.width(2), .mode("unsigned")) comparator_5 (
    .a(register_3_q), .b(2'b00), .eq(comparator_5_eq));  // open: gt, lt
  // NOT_Gate not_3 has open pins: in=comparator_5_eq, out=open
  Comparator #(.width(2), .mode("unsigned")) comparator_6 (
    .a(register_4_q), .b(2'b00), .eq(comparator_6_eq));  // open: gt, lt
  // NOT_Gate not_4 has open pins: in=comparator_6_eq, out=open
  Multiplexer #(.select(4), .width(4)) multiplexer_3 (
    .in8(4'b0010), .out(out_9), .sel({out_8[3:2], DATA_IN}));  // open: in0, in1, in2, in3, in4, in5, in6, in7, in9, in10, in11, in12, in13, in14, in15, en
  Multiplexer #(.select(4), .width(4)) multiplexer_4 (
    .out({multiplexer_4_out_2, multiplexer_4_out}), .sel({register_2_q, DATA_IN}));  // open: in0, in1, in2, in3, in4, in5, in6, in7, in8, in9, in10, in11, in12, in13, in14, in15, en
  Multiplexer #(.select(4), .width(4)) multiplexer_5 (
    .out({multiplexer_5_out_2, multiplexer_5_out}), .sel({register_3_q, DATA_IN}));  // open: in0, in1, in2, in3, in4, in5, in6, in7, in8, in9, in10, in11, in12, in13, in14, in15, en
  Multiplexer #(.select(4), .width(4)) multiplexer_6 (
    .out({multiplexer_6_out_2, multiplexer_6_out}), .sel({register_4_q, DATA_IN}));  // open: in0, in1, in2, in3, in4, in5, in6, in7, in8, in9, in10, in11, in12, in13, in14, in15, en
  Register #(.width(2)) register_5 (.D(out_9[3:2]), .clk(demultiplexer_1_out5));  // open: en, Q, clr
  Register #(.width(2)) register_6 (.D(multiplexer_4_out_2), .clk(demultiplexer_1_out7));  // open: en, Q, clr
  Register #(.width(2)) register_7 (.D(multiplexer_5_out_2), .clk(demultiplexer_1_out9));  // open: en, Q, clr
  Register #(.width(2)) register_8 (.D(multiplexer_6_out_2), .clk(undriven_3));  // open: en, Q, clr
  Comparator #(.width(4), .mode("unsigned")) comparator_7 (.a(undriven_2), .b(4'b0110), .eq(\ZAMROŹ ));  // open: gt, lt
  Multiplexer #(.select(3), .width(2), .disabled(0)) multiplexer_7 (
    .in0(out_9[1:0]), .out(DATA_OUT));  // open: in1, in2, in3, in4, in5, in6, in7, sel, en

  assign out_8[1:0] = DATA_IN;

  // Notes on the sheet:
  //   do zmiany na -8
  //   zmodyfikowac ze dostaje prawy dolny
  //   aktualny adres weryfikowany
  //   W
  //   N
endmodule
