// Logisim project wiersz_koniec_piatek.circ as structural Verilog: 1 circuit, main circuit wiersz
module wiersz (
  input  [1:0] DATA_IN,
  input  CLK,
  output [1:0] DATA_OUT,
  output RAM_CLK
);

  wire _0, and_1_out, czy_zderzenie_1_p3, czy_zderzenie_2_p3, czy_zderzenie_3_p3, czy_zderzenie_4_p3,
       demultiplexer_1_out0, demultiplexer_1_out1, demultiplexer_1_out2, demultiplexer_1_out3,
       demultiplexer_1_out4, demultiplexer_1_out5, demultiplexer_1_out6, demultiplexer_1_out7,
       demultiplexer_1_out8, demultiplexer_1_out9, demultiplexer_1_out10, demultiplexer_1_out11,
       demultiplexer_1_out12, demultiplexer_1_out13, demultiplexer_1_out14, or_2_out, T3, ZD;
  wire [1:0] _1, _2, _3, _4, A, B, C, counter_3_q, czy_zderzenie_1_p4, D, multiplexer_3_out,
       multiplexer_4_out, T1, zamieniacz_1_n_2, zamieniacz_1_w_2, zamieniacz_2_n_2, zamieniacz_2_w_2,
       zamieniacz_3_n_2, zamieniacz_3_w_2, zamieniacz_4_n_2, zamieniacz_4_w_2;
  wire [3:0] counter_1_q, subtractor_1_out;

  or or_1 (RAM_CLK, demultiplexer_1_out7, demultiplexer_1_out8, demultiplexer_1_out9, demultiplexer_1_out10, demultiplexer_1_out11, demultiplexer_1_out12, demultiplexer_1_out13, demultiplexer_1_out14);
  and and_1 (and_1_out, 1'b1, CLK);
  Demultiplexer #(.select(4)) demultiplexer_1 (
    .out0(demultiplexer_1_out0), .out1(demultiplexer_1_out1), .out2(demultiplexer_1_out2),
    .out3(demultiplexer_1_out3), .out4(demultiplexer_1_out4), .out5(demultiplexer_1_out5),
    .out6(demultiplexer_1_out6), .out7(demultiplexer_1_out7), .out8(demultiplexer_1_out8),
    .out9(demultiplexer_1_out9), .out10(demultiplexer_1_out10), .out11(demultiplexer_1_out11),
    .out12(demultiplexer_1_out12), .out13(demultiplexer_1_out13), .out14(demultiplexer_1_out14), .out15(_0),
    .in(and_1_out), .sel(subtractor_1_out));  // open: en
  Counter #(.width(4), .max('hf)) counter_1 (.Q(counter_1_q), .clk(CLK));  // open: load, D, count, carry, clr
  Subtractor #(.width(4)) subtractor_1 (.a(counter_1_q), .b(4'b0001), .out(subtractor_1_out));  // open: bin, bout
  Register #(.width(2)) register_1 (.D(DATA_IN), .Q(A), .clk(_0));  // open: en, clr
  Register #(.width(2)) register_2 (.D(DATA_IN), .Q(B), .clk(demultiplexer_1_out0));  // open: en, clr
  Register #(.width(2)) register_3 (.D(DATA_IN), .Q(C), .clk(demultiplexer_1_out1));  // open: en, clr
  Register #(.width(2)) register_4 (.D(DATA_IN), .Q(D), .clk(demultiplexer_1_out2));  // open: en, clr
  Register #(.width(2)) register_5 (.D(DATA_IN), .Q(_1), .clk(demultiplexer_1_out3));  // open: en, clr
  Register #(.width(2)) register_6 (.D(DATA_IN), .Q(_2), .clk(demultiplexer_1_out4));  // open: en, clr
  Register #(.width(2)) register_7 (.D(DATA_IN), .Q(_3), .clk(demultiplexer_1_out5));  // open: en, clr
  Register #(.width(2)) register_8 (.D(DATA_IN), .Q(_4), .clk(demultiplexer_1_out6));  // open: en, clr
  or or_2 (or_2_out, demultiplexer_1_out8, demultiplexer_1_out9, demultiplexer_1_out10, demultiplexer_1_out11, demultiplexer_1_out12, demultiplexer_1_out13, demultiplexer_1_out14);
  // czy_zderzenie czy_zderzenie_1: pin names not known; wires that end beside it: A, _1, czy_zderzenie_1_p3, czy_zderzenie_1_p4
  // czy_zderzenie czy_zderzenie_2: pin names not known; wires that end beside it: B, _2, czy_zderzenie_2_p3
  // czy_zderzenie czy_zderzenie_3: pin names not known; wires that end beside it: C, _3, czy_zderzenie_3_p3
  // czy_zderzenie czy_zderzenie_4: pin names not known; wires that end beside it: D, _4, czy_zderzenie_4_p3
  Counter #(.width(2), .max('h3)) counter_2 (.Q(T1), .clk(or_2_out), .clr(_0));  // open: load, D, count, carry
  Multiplexer #(.select(2), .width(2)) multiplexer_1 (
    .in0(2'b11), .in1(2'b10), .in2(2'b10), .in3(2'b01), .out(czy_zderzenie_1_p4), .sel(T1));  // open: en
  or or_3 (ZD, czy_zderzenie_1_p3, czy_zderzenie_2_p3, czy_zderzenie_3_p3, czy_zderzenie_4_p3);
  zamieniacz zamieniacz_1 (
    .W(A), .N(_1), .W_2(zamieniacz_1_w_2), .N_2(zamieniacz_1_n_2), .WYSTAPILO_ZDERZENIE(ZD));  // open: out_4
  zamieniacz zamieniacz_2 (
    .W(B), .N(_2), .W_2(zamieniacz_2_w_2), .N_2(zamieniacz_2_n_2), .WYSTAPILO_ZDERZENIE(ZD));  // open: out_4
  zamieniacz zamieniacz_3 (
    .W(C), .N(_3), .W_2(zamieniacz_3_w_2), .N_2(zamieniacz_3_n_2), .WYSTAPILO_ZDERZENIE(ZD));  // open: out_4
  zamieniacz zamieniacz_4 (
    .W(D), .N(_4), .W_2(zamieniacz_4_w_2), .N_2(zamieniacz_4_n_2), .WYSTAPILO_ZDERZENIE(ZD));  // open: out_4
  Multiplexer #(.width(2)) multiplexer_2 (
    .in0(multiplexer_3_out), .in1(multiplexer_4_out), .out(DATA_OUT), .sel(T3));  // open: en
  Multiplexer #(.select(2), .width(2)) multiplexer_3 (
    .in0(zamieniacz_1_w_2), .in1(zamieniacz_2_w_2), .in2(zamieniacz_3_w_2), .in3(zamieniacz_4_w_2),
    .out(multiplexer_3_out), .sel(T1));  // open: en
  Counter #(.width(2), .max('h3)) counter_3 (
    .Q(counter_3_q), .clk(demultiplexer_1_out11), .clr(_0));  // open: load, D, count, carry
  Multiplexer #(.select(2), .width(2)) multiplexer_4 (
    .in0(zamieniacz_1_n_2), .in1(zamieniacz_2_n_2), .in2(zamieniacz_3_n_2), .in3(zamieniacz_4_n_2),
    .out(multiplexer_4_out), .sel(T1));  // open: en
  Comparator #(.width(2), .mode("unsigned")) comparator_1 (.a(counter_3_q), .b(2'b00), .gt(T3));  // open: eq, lt

  // Other names for the same wires on the sheet: T4 = _0

  // Notes on the sheet:
  //   MUX TESTOWY
  //   ZDERZENIE
endmodule
