// Logisim project komparator 4-bitowy.circ as structural Verilog: 1 circuit, main circuit main
module main (
  input  [3:0] A,
  input  [3:0] B,
  input  in_3,
  output A_B,
  output A_B_2,
  output A_B_3
);

  wire main_1_a_b, main_1_a_b_2, main_1_a_b_3, main_2_a_b, main_2_a_b_2, main_2_a_b_3, main_3_a_b,
       main_3_a_b_2, main_3_a_b_3, main_4_a_b, main_4_a_b_3;

  komparator_main main_1 (
    .poprzedni(in_3), .A_B(main_1_a_b), .A_B_2(main_1_a_b_2), .A_B_3(main_1_a_b_3), .A(A[3]), .B(B[3]));
  komparator_main main_2 (
    .poprzedni(main_1_a_b_2), .A_B(main_2_a_b), .A_B_2(main_2_a_b_2), .A_B_3(main_2_a_b_3), .A(A[2]), .B(B[2]));
  komparator_main main_3 (
    .poprzedni(main_2_a_b_2), .A_B(main_3_a_b), .A_B_2(main_3_a_b_2), .A_B_3(main_3_a_b_3), .A(A[1]), .B(B[1]));
  komparator_main main_4 (
    .poprzedni(main_3_a_b_2), .A_B(main_4_a_b), .A_B_2(A_B_2), .A_B_3(main_4_a_b_3), .A(A[0]), .B(B[0]));
  nand nand_1 (A_B, ~main_1_a_b, ~main_2_a_b, ~main_3_a_b, ~main_4_a_b);  // NAND_Gate
  nand nand_2 (A_B_3, ~main_4_a_b_3, ~main_3_a_b_3, ~main_2_a_b_3, ~main_1_a_b_3);  // NAND_Gate
endmodule
