// Logisim project testowy.circ as structural Verilog: 1 circuit, main circuit main
module main (
  input  [6:0] in_1
);

  wire [6:0] adder_1_out, adder_2_out, adder_3_out, subtractor_1_out, subtractor_2_out;

  Adder #(.width(7)) adder_1 (.a(in_1), .b(7'b0100111), .out(adder_1_out));  // open: cin, cout
  Adder #(.width(7)) adder_2 (.a(in_1), .b(7'b0000001), .out(adder_2_out));  // open: cin, cout
  Adder #(.width(7)) adder_3 (.a(in_1), .b(7'b0001000), .out(adder_3_out));  // open: cin, cout
  Subtractor #(.width(7)) subtractor_1 (.a(in_1), .b(7'b0000001), .out(subtractor_1_out));  // open: bin, bout
  Subtractor #(.width(7)) subtractor_2 (.a(in_1), .b(7'b0001000), .out(subtractor_2_out));  // open: bin, bout
  RAM #(.addrWidth(7), .dataWidth(2), .bus("separate")) ram_1 (.addr(in_1));  // open: din, data, str, sel, clk, ld, clr
  RAM #(.addrWidth(7), .dataWidth(2), .bus("separate")) ram_2 (.addr(adder_1_out));  // open: din, data, str, sel, clk, ld, clr
  RAM #(.addrWidth(7), .dataWidth(2), .bus("separate")) ram_3 (.addr(adder_2_out));  // open: din, data, str, sel, clk, ld, clr
  RAM #(.addrWidth(7), .dataWidth(2), .bus("separate")) ram_4 (.addr(adder_3_out));  // open: din, data, str, sel, clk, ld, clr
  RAM #(.addrWidth(7), .dataWidth(2), .bus("separate")) ram_5 (.addr(subtractor_1_out));  // open: din, data, str, sel, clk, ld, clr
  RAM #(.addrWidth(7), .dataWidth(2), .bus("separate")) ram_6 (.addr(subtractor_2_out));  // open: din, data, str, sel, clk, ld, clr

  // Notes on the sheet:
  //   +1 to jedno w prawo
  //   -1 to jedno w lewo
  //   -8 to 1 do gory
  //   +8 to jedno w dol
endmodule
