// Logisim project obnizanie.circ as structural Verilog: 1 circuit, main circuit main
module main (
  input  [6:0] A1,
  input  [1:0] DATA_IN,
  input  CLK,
  input  ENABLE,
  output [1:0] DATA_OUT,
  output [6:0] A,
  output RAM_CLK,
  output FINISH
);

  wire adreso_latacz_1_finish, and_1_out, demultiplexer_3_out0, main_1_ram_clk, TRYB;
  wire [1:0] demultiplexer_2_out0, main_1_data_out;
  wire [6:0] adreso_latacz_1_adres_out, demultiplexer_1_out0;

  and and_1 (and_1_out, CLK, ENABLE);
  Comparator #(.width(7), .mode("unsigned")) comparator_1 (.a(A1), .b(7'b1011111), .gt(TRYB));  // open: eq, lt
  Demultiplexer #(.width(7)) demultiplexer_1 (.out0(demultiplexer_1_out0), .in(A1), .sel(TRYB));  // open: out1, en
  Demultiplexer #(.width(2)) demultiplexer_2 (.out0(demultiplexer_2_out0), .in(DATA_IN), .sel(TRYB));  // open: out1, en
  Demultiplexer demultiplexer_3 (.out0(demultiplexer_3_out0), .in(and_1_out), .sel(TRYB));  // open: out1, en
  adreso_latacz adreso_latacz_1 (
    .CLK(demultiplexer_3_out0), .ADRES_OUT(adreso_latacz_1_adres_out), .FINISH(adreso_latacz_1_finish),
    .ADRES_ROOT(demultiplexer_1_out0));
  wiersz_normal_main main_1 (
    .CLK(demultiplexer_3_out0), .DATA_OUT(main_1_data_out), .DATA_IN(demultiplexer_2_out0),
    .RAM_CLK(main_1_ram_clk));
  Multiplexer #(.width(2)) multiplexer_1 (.in0(main_1_data_out), .out(DATA_OUT), .sel(TRYB));  // open: in1, en
  Multiplexer #(.width(7)) multiplexer_2 (.in0(adreso_latacz_1_adres_out), .out(A), .sel(TRYB));  // open: in1, en
  Multiplexer multiplexer_3 (.in0(main_1_ram_clk), .out(RAM_CLK), .sel(TRYB));  // open: in1, en
  Multiplexer multiplexer_4 (.in0(adreso_latacz_1_finish), .out(FINISH), .sel(TRYB));  // open: in1, en

  // Notes on the sheet:
  //   jeżeli większe niż 95 to tryb podłoga
  //   0 to normal
  //   1 to podloga
  //   NORMAL
  //   PODŁOGA
endmodule
