// Logisim project 2bit comparator.circ as structural Verilog: 1 circuit, main circuit main
module main (
  input  [1:0] in_1,
  input  [1:0] in_2,
  output A_B,
  output A_B_2,
  output A_B_3
);

  wire main_1_out_4, main_1_out_5, main_1_out_6, main_2_out_4, main_2_out_6;

  _1bitcomp_main main_1 (
    .in_3(1'b1), .B(in_2[1]), .A(in_1[1]), .out_4(main_1_out_4), .out_5(main_1_out_5), .out_6(main_1_out_6));
  _1bitcomp_main main_2 (
    .in_3(main_1_out_5), .B(in_2[0]), .A(in_1[0]), .out_4(main_2_out_4), .out_5(A_B_2), .out_6(main_2_out_6));
  nand nand_1 (A_B, ~main_1_out_4, ~main_2_out_4);  // NAND_Gate
  nand nand_2 (A_B_3, ~main_2_out_6, ~main_1_out_6);  // NAND_Gate
endmodule
