// Logisim project Block randomizer.circ as structural Verilog: 1 circuit, main circuit BLC RAND
module BLC_RAND (
  input  CLK,
  input  START,
  input  [6:0] GAME_BLC_ADRESS,
  input  [1:0] GAME_BLC_STATE,
  output OUT_B,
  output [6:0] OUT_A,
  output [1:0] OUT_D,
  output GAME_OVER
);

  wire and_1_out, controlled_buffer_1_out, main_1_a_b_2, main_2_a_b_2, main_3_a_b_2, main_4_a_b_2,
       main_8_a_b_2, main_9_a_b_2, main_10_a_b_2, n7bit_comparator_1_out_4, or_1_out;
  wire [1:0] main_5_out_4, main_6_out_4, main_7_out_4, n2x2_block_1_out_4, rand_1_out;
  wire [6:0] main_5_out_3, main_6_out_3, main_7_out_3, n2x2_block_1_out_3;

  Counter #(.width(4), .max('hf), .trigger("falling")) counter_1 (
    .carry(OUT_B), .clk(controlled_buffer_1_out));  // open: load, D, count, Q, clr
  assign controlled_buffer_1_out = START ? CLK : 1'bz;  // Controlled_Buffer controlled_buffer_1
  Pull_Resistor pull_resistor_1 (.node(controlled_buffer_1_out));
  RAND rand_1 (.CLK(OUT_B), .OUT(rand_1_out));
  _2bit_comparator_main main_1 (.in_1(2'b00), .in_2(rand_1_out), .A_B_2(main_1_a_b_2));  // open: A_B, A_B_3
  _2bit_comparator_main main_2 (.in_1(2'b01), .in_2(rand_1_out), .A_B_2(main_2_a_b_2));  // open: A_B, A_B_3
  _2bit_comparator_main main_3 (.in_1(2'b10), .in_2(rand_1_out), .A_B_2(main_3_a_b_2));  // open: A_B, A_B_3
  _2bit_comparator_main main_4 (.in_1(2'b11), .in_2(rand_1_out), .A_B_2(main_4_a_b_2));  // open: A_B, A_B_3
  _1x4_Block_main main_5 (
    .START_GEN(main_1_a_b_2), .CLK(controlled_buffer_1_out), .out_3(main_5_out_3), .out_4(main_5_out_4));  // open: out_5
  _2x2_Block u_2x2_block_1 (
    .in_1(controlled_buffer_1_out), .in_2(main_2_a_b_2), .out_3(n2x2_block_1_out_3),
    .out_4(n2x2_block_1_out_4));  // open: out_5
  T_Block_main main_6 (
    .START_GEN(main_3_a_b_2), .CLK(controlled_buffer_1_out), .out_3(main_6_out_3), .out_4(main_6_out_4));  // open: out_5
  L_Block_main main_7 (
    .START_GEN(main_4_a_b_2), .CLK(controlled_buffer_1_out), .out_3(main_7_out_3), .out_4(main_7_out_4));  // open: out_5
  assign OUT_A = main_1_a_b_2 ? main_5_out_3 : 7'bz;  // Controlled_Buffer controlled_buffer_2
  assign OUT_A = main_2_a_b_2 ? n2x2_block_1_out_3 : 7'bz;  // Controlled_Buffer controlled_buffer_3
  assign OUT_D = main_2_a_b_2 ? n2x2_block_1_out_4 : 2'bz;  // Controlled_Buffer controlled_buffer_4
  assign OUT_A = main_3_a_b_2 ? main_6_out_3 : 7'bz;  // Controlled_Buffer controlled_buffer_5
  assign OUT_A = main_4_a_b_2 ? main_7_out_3 : 7'bz;  // Controlled_Buffer controlled_buffer_6
  assign OUT_D = main_1_a_b_2 ? main_5_out_4 : 2'bz;  // Controlled_Buffer controlled_buffer_7
  assign OUT_D = main_3_a_b_2 ? main_6_out_4 : 2'bz;  // Controlled_Buffer controlled_buffer_8
  assign OUT_D = main_4_a_b_2 ? main_7_out_4 : 2'bz;  // Controlled_Buffer controlled_buffer_9
  _2bit_comparator_main main_8 (.in_1(GAME_BLC_STATE), .in_2(2'b10), .A_B_2(main_8_a_b_2));  // open: A_B, A_B_3
  _2bit_comparator_main main_9 (.in_1(GAME_BLC_STATE), .in_2(2'b01), .A_B_2(main_9_a_b_2));  // open: A_B, A_B_3
  _7bit_comparator u_7bit_comparator_1 (
    .gen_adress(OUT_A), .game_adress(GAME_BLC_ADRESS), .out_4(n7bit_comparator_1_out_4));  // open: out_3, out_5
  or or_1 (or_1_out, main_8_a_b_2, main_9_a_b_2);
  _2bit_comparator_main main_10 (.in_1(OUT_D), .in_2(2'b10), .A_B_2(main_10_a_b_2));  // open: A_B, A_B_3
  and and_1 (and_1_out, main_10_a_b_2, or_1_out);
  assign GAME_OVER = n7bit_comparator_1_out_4 ? and_1_out : 1'bz;  // Controlled_Buffer controlled_buffer_10
  Pull_Resistor pull_resistor_2 (.node(GAME_OVER));

  // Notes on the sheet:
  //   OUT_B - is the system working
  //   OUT_D - is current block solid/air
  //   OUT_A - code for coordinates of current block
endmodule
