// Logisim project logiczno-ustawiacz_p4_backup.circ as structural Verilog: 1 circuit, main circuit logiczno-ustawiacz_norm
module logiczno_ustawiacz_norm (
  input  [1:0] REG_0,
  input  [1:0] REG_1,
  input  [1:0] REG_2,
  input  [1:0] REG_3,
  input  [1:0] REG_0_2,
  input  [1:0] REG_1_2,
  input  [1:0] REG_2_2,
  input  [1:0] REG_3_2,
  input  [1:0] REG_0_3,
  input  [1:0] REG_1_3,
  input  [1:0] REG_2_3,
  input  [1:0] REG_3_3,
  input  [1:0] REG_0_4,
  input  [1:0] REG_1_4,
  input  [1:0] REG_2_4,
  input  [1:0] REG_3_4,
  input  [1:0] REG_0_5,
  input  [1:0] REG_1_5,
  input  [1:0] REG_2_5,
  input  [1:0] REG_3_5,
  output [1:0] OUT_0,
  output [1:0] OUT_1,
  output [1:0] OUT_2,
  output [1:0] OUT_3,
  output [1:0] OUT_0_2,
  output [1:0] OUT_1_2,
  output [1:0] OUT_2_2,
  output [1:0] OUT_3_2,
  output [1:0] OUT_0_3,
  output [1:0] OUT_1_3,
  output [1:0] OUT_2_3,
  output [1:0] OUT_3_3,
  output [1:0] OUT_0_4,
  output [1:0] OUT_1_4,
  output [1:0] OUT_2_4,
  output [1:0] OUT_3_4,
  output [1:0] OUT_0_5,
  output [1:0] OUT_1_5,
  output [1:0] OUT_2_5,
  output [1:0] OUT_3_5,
  output ZD_OUT
);

  wire czy_zderzenie_1_out, czy_zderzenie_2_out, czy_zderzenie_3_out, czy_zderzenie_4_out,
       czy_zderzenie_5_out, czy_zderzenie_6_out, czy_zderzenie_7_out, czy_zderzenie_8_out,
       czy_zderzenie_9_out, czy_zderzenie_10_out, czy_zderzenie_11_out, czy_zderzenie_12_out,
       czy_zderzenie_13_out, czy_zderzenie_14_out, czy_zderzenie_15_out, czy_zderzenie_16_out, or_1_out,
       or_2_out, or_3_out, or_4_out;
  wire [1:0] zamieniacz_1_w_2, zamieniacz_2_w_2, zamieniacz_3_w_2, zamieniacz_4_w_2, zamieniacz_5_w_2,
       zamieniacz_6_w_2, zamieniacz_7_w_2, zamieniacz_8_w_2, zamieniacz_9_w_2, zamieniacz_10_w_2,
       zamieniacz_11_w_2, zamieniacz_12_w_2;

  czy_zderzenie czy_zderzenie_1 (.W(REG_0_2), .N(REG_0), .OUT(czy_zderzenie_1_out));
  czy_zderzenie czy_zderzenie_2 (.W(REG_1_2), .N(REG_1), .OUT(czy_zderzenie_2_out));
  czy_zderzenie czy_zderzenie_3 (.W(REG_2_2), .N(REG_2), .OUT(czy_zderzenie_3_out));
  czy_zderzenie czy_zderzenie_4 (.W(REG_3_2), .N(REG_3), .OUT(czy_zderzenie_4_out));
  or or_1 (or_1_out, czy_zderzenie_1_out, czy_zderzenie_2_out, czy_zderzenie_3_out, czy_zderzenie_4_out);
  czy_zderzenie czy_zderzenie_5 (.W(REG_0_3), .N(REG_0_2), .OUT(czy_zderzenie_5_out));
  czy_zderzenie czy_zderzenie_6 (.W(REG_1_3), .N(REG_1_2), .OUT(czy_zderzenie_6_out));
  czy_zderzenie czy_zderzenie_7 (.W(REG_2_3), .N(REG_2_2), .OUT(czy_zderzenie_7_out));
  czy_zderzenie czy_zderzenie_8 (.W(REG_3_3), .N(REG_3_2), .OUT(czy_zderzenie_8_out));
  zamieniacz zamieniacz_1 (
    .W(REG_3_2), .N(REG_3), .W_2(zamieniacz_1_w_2), .N_2(OUT_3), .WYSTAPILO_ZDERZENIE(ZD_OUT));  // open: out_4
  zamieniacz zamieniacz_2 (
    .W(REG_2_2), .N(REG_2), .W_2(zamieniacz_2_w_2), .N_2(OUT_2), .WYSTAPILO_ZDERZENIE(ZD_OUT));  // open: out_4
  zamieniacz zamieniacz_3 (
    .W(REG_1_2), .N(REG_1), .W_2(zamieniacz_3_w_2), .N_2(OUT_1), .WYSTAPILO_ZDERZENIE(ZD_OUT));  // open: out_4
  zamieniacz zamieniacz_4 (
    .W(REG_0_2), .N(REG_0), .W_2(zamieniacz_4_w_2), .N_2(OUT_0), .WYSTAPILO_ZDERZENIE(ZD_OUT));  // open: out_4
  or or_2 (or_2_out, czy_zderzenie_5_out, czy_zderzenie_6_out, czy_zderzenie_7_out, czy_zderzenie_8_out);
  zamieniacz zamieniacz_5 (
    .W(REG_3_3), .N(zamieniacz_1_w_2), .W_2(zamieniacz_5_w_2), .N_2(OUT_3_2), .WYSTAPILO_ZDERZENIE(ZD_OUT));  // open: out_4
  zamieniacz zamieniacz_6 (
    .W(REG_2_3), .N(zamieniacz_2_w_2), .W_2(zamieniacz_6_w_2), .N_2(OUT_2_2), .WYSTAPILO_ZDERZENIE(ZD_OUT));  // open: out_4
  zamieniacz zamieniacz_7 (
    .W(REG_1_3), .N(zamieniacz_3_w_2), .W_2(zamieniacz_7_w_2), .N_2(OUT_1_2), .WYSTAPILO_ZDERZENIE(ZD_OUT));  // open: out_4
  zamieniacz zamieniacz_8 (
    .W(REG_0_3), .N(zamieniacz_4_w_2), .W_2(zamieniacz_8_w_2), .N_2(OUT_0_2), .WYSTAPILO_ZDERZENIE(ZD_OUT));  // open: out_4
  czy_zderzenie czy_zderzenie_9 (.W(REG_0_4), .N(REG_0_3), .OUT(czy_zderzenie_9_out));
  czy_zderzenie czy_zderzenie_10 (.W(REG_1_4), .N(REG_1_3), .OUT(czy_zderzenie_10_out));
  czy_zderzenie czy_zderzenie_11 (.W(REG_2_4), .N(REG_2_3), .OUT(czy_zderzenie_11_out));
  czy_zderzenie czy_zderzenie_12 (.W(REG_3_4), .N(REG_1_3), .OUT(czy_zderzenie_12_out));
  or or_3 (or_3_out, czy_zderzenie_9_out, czy_zderzenie_10_out, czy_zderzenie_11_out, czy_zderzenie_12_out);
  zamieniacz zamieniacz_9 (
    .W(REG_3_4), .N(zamieniacz_5_w_2), .W_2(zamieniacz_9_w_2), .N_2(OUT_3_3), .WYSTAPILO_ZDERZENIE(ZD_OUT));  // open: out_4
  zamieniacz zamieniacz_10 (
    .W(REG_2_4), .N(zamieniacz_6_w_2), .W_2(zamieniacz_10_w_2), .N_2(OUT_2_3), .WYSTAPILO_ZDERZENIE(ZD_OUT));  // open: out_4
  zamieniacz zamieniacz_11 (
    .W(REG_1_4), .N(zamieniacz_7_w_2), .W_2(zamieniacz_11_w_2), .N_2(OUT_1_3), .WYSTAPILO_ZDERZENIE(ZD_OUT));  // open: out_4
  zamieniacz zamieniacz_12 (
    .W(REG_0_4), .N(zamieniacz_8_w_2), .W_2(zamieniacz_12_w_2), .N_2(OUT_0_3), .WYSTAPILO_ZDERZENIE(ZD_OUT));  // open: out_4
  czy_zderzenie czy_zderzenie_13 (.W(REG_0_5), .N(REG_0_4), .OUT(czy_zderzenie_13_out));
  czy_zderzenie czy_zderzenie_14 (.W(REG_1_5), .N(REG_1_4), .OUT(czy_zderzenie_14_out));
  czy_zderzenie czy_zderzenie_15 (.W(REG_2_5), .N(REG_2_4), .OUT(czy_zderzenie_15_out));
  czy_zderzenie czy_zderzenie_16 (.W(REG_3_5), .N(REG_1_4), .OUT(czy_zderzenie_16_out));
  or or_4 (or_4_out, czy_zderzenie_13_out, czy_zderzenie_14_out, czy_zderzenie_15_out, czy_zderzenie_16_out);
  zamieniacz zamieniacz_13 (
    .W(REG_3_5), .N(zamieniacz_9_w_2), .W_2(OUT_3_5), .N_2(OUT_3_4), .WYSTAPILO_ZDERZENIE(ZD_OUT));  // open: out_4
  zamieniacz zamieniacz_14 (
    .W(REG_2_5), .N(zamieniacz_10_w_2), .W_2(OUT_2_5), .N_2(OUT_2_4), .WYSTAPILO_ZDERZENIE(ZD_OUT));  // open: out_4
  zamieniacz zamieniacz_15 (
    .W(REG_1_5), .N(zamieniacz_11_w_2), .W_2(OUT_1_5), .N_2(OUT_1_4), .WYSTAPILO_ZDERZENIE(ZD_OUT));  // open: out_4
  zamieniacz zamieniacz_16 (
    .W(REG_0_5), .N(zamieniacz_12_w_2), .W_2(OUT_0_5), .N_2(OUT_0_4), .WYSTAPILO_ZDERZENIE(ZD_OUT));  // open: out_4
  or or_5 (ZD_OUT, or_4_out, or_3_out, or_2_out, or_1_out);

  // Other names for the same wires on the sheet: _0[1:0] = REG_0; _1[1:0] = REG_1; _2[1:0] = REG_2; _3[1:0] = REG_3;
  //   _4[1:0] = REG_0_2; _5[1:0] = REG_1_2; _6[1:0] = REG_2_2; _7[1:0] = REG_3_2; _8[1:0] = REG_0_3;
  //   _9[1:0] = REG_1_3; _10[1:0] = REG_2_3; _11[1:0] = REG_3_3; _12[1:0] = REG_0_4; _13[1:0] = REG_1_4;
  //   _14[1:0] = REG_2_4; _15[1:0] = REG_3_4; _16[1:0] = REG_0_5; _17[1:0] = REG_1_5; _18[1:0] = REG_2_5;
  //   _19[1:0] = REG_3_5; OUT_4[1:0] = OUT_0_2; OUT_5[1:0] = OUT_1_2; OUT_6[1:0] = OUT_2_2; OUT_7[1:0] = OUT_3_2;
  //   OUT_8[1:0] = OUT_0_3; OUT_9[1:0] = OUT_1_3; OUT_10[1:0] = OUT_2_3; OUT_11[1:0] = OUT_3_3; OUT_12[1:0] = OUT_0_4;
  //   OUT_13[1:0] = OUT_1_4; OUT_14[1:0] = OUT_2_4; OUT_15[1:0] = OUT_3_4; OUT_16[1:0] = OUT_0_5;
  //   OUT_17[1:0] = OUT_1_5; OUT_18[1:0] = OUT_2_5; OUT_19[1:0] = OUT_3_5; ZD = ZD_OUT

  // Notes on the sheet:
  //   wiersz 1
  //   wiersz 2
  //   wiersz 3
  //   wiersz 4
  //   wiersz 5
  //   ZDERZENIE
endmodule
