// Logisim project zamieniacz.circ as structural Verilog: 1 circuit, main circuit zamieniacz
module zamieniacz (
  input  WYSTAPILO_ZDERZENIE,
  input  [1:0] W,
  input  [1:0] N,
  output [4:0] out_4,
  output [1:0] W_2,
  output [1:0] N_2
);

  wire [4:0] adder_1_out;

  Adder #(.width(5)) adder_1 (.a({1'b0, N, W}), .b(5'b10000), .out(adder_1_out));  // open: cin, cout
  Multiplexer #(.width(5)) multiplexer_1 (
    .in0({1'b0, N, W}), .in1(adder_1_out), .out(out_4), .sel(WYSTAPILO_ZDERZENIE));  // open: en
  Multiplexer #(.select(5), .width(4)) multiplexer_2 (
    .in0(4'b0000), .in1(4'b0001), .in2(4'b1000), .in4(4'b0100), .in5(4'b0101), .in8(4'b1000), .in16(4'b0000),
    .in17(4'b0001), .in18(4'b0001), .in20(4'b0100), .in21(4'b0101), .in22(4'b0101), .in24(4'b0100),
    .in25(4'b0101), .in26(4'b0101), .out({N_2, W_2}), .sel(out_4));  // open: in3, in6, in7, in9, in10, in11, in12, in13, in14, in15, in19, in23, in27, in28, in29, in30, in31, en
endmodule
