// Logisim project MEGA_register_p4.circ as structural Verilog: 1 circuit, main circuit main
module main (
  input  [1:0] DATA_IN,
  input  CLK,
  output [1:0] DATA_OUT_0,
  output [1:0] DATA_OUT_1,
  output [1:0] DATA_OUT_2,
  output [1:0] DATA_OUT_3,
  output [1:0] DATA_OUT_4,
  output [1:0] DATA_OUT_5,
  output [1:0] DATA_OUT_6,
  output [1:0] DATA_OUT_7,
  output [1:0] DATA_OUT_8,
  output [1:0] DATA_OUT_9,
  output [1:0] DATA_OUT_10,
  output [1:0] DATA_OUT_11,
  output [1:0] DATA_OUT_12,
  output [1:0] DATA_OUT_13,
  output [1:0] DATA_OUT_14,
  output [1:0] DATA_OUT_15,
  output [1:0] DATA_OUT_16,
  output [1:0] DATA_OUT_17,
  output [1:0] DATA_OUT_18,
  output [1:0] DATA_OUT_19
);

  wire demultiplexer_1_out0, demultiplexer_1_out1, demultiplexer_1_out2, demultiplexer_1_out3,
       demultiplexer_1_out4, demultiplexer_1_out5, demultiplexer_1_out6, demultiplexer_1_out7,
       demultiplexer_1_out8, demultiplexer_1_out9, demultiplexer_1_out10, demultiplexer_1_out11,
       demultiplexer_1_out12, demultiplexer_1_out13, demultiplexer_1_out14, demultiplexer_1_out15,
       demultiplexer_1_out16, demultiplexer_1_out17, demultiplexer_1_out18, demultiplexer_1_out19,
       undriven_3, undriven_4, undriven_5, undriven_6;
  wire [1:0] _17, _18, _19, _20, undriven_2;
  wire [4:0] adder_1_out, counter_1_q, undriven;

  Demultiplexer #(.select(5)) demultiplexer_1 (
    .out0(demultiplexer_1_out0), .out1(demultiplexer_1_out1), .out2(demultiplexer_1_out2),
    .out3(demultiplexer_1_out3), .out4(demultiplexer_1_out4), .out5(demultiplexer_1_out5),
    .out6(demultiplexer_1_out6), .out7(demultiplexer_1_out7), .out8(demultiplexer_1_out8),
    .out9(demultiplexer_1_out9), .out10(demultiplexer_1_out10), .out11(demultiplexer_1_out11),
    .out12(demultiplexer_1_out12), .out13(demultiplexer_1_out13), .out14(demultiplexer_1_out14),
    .out15(demultiplexer_1_out15), .out16(demultiplexer_1_out16), .out17(demultiplexer_1_out17),
    .out18(demultiplexer_1_out18), .out19(demultiplexer_1_out19), .in(CLK), .sel(counter_1_q));  // open: out20, out21, out22, out23, out24, out25, out26, out27, out28, out29, out30, out31, en
  Counter #(.width(5), .max('h11)) counter_1 (.Q(counter_1_q), .clk(CLK));  // open: load, D, count, carry, clr
  Adder #(.width(5)) adder_1 (.a(undriven), .b(5'b00100), .out(adder_1_out));  // open: cin, cout
  Register #(.width(2)) register_1 (.D(DATA_IN), .Q(DATA_OUT_4), .clk(demultiplexer_1_out0));  // open: en, clr
  Register #(.width(2)) register_2 (.D(DATA_IN), .Q(DATA_OUT_5), .clk(demultiplexer_1_out1));  // open: en, clr
  Register #(.width(2)) register_3 (.D(DATA_IN), .Q(DATA_OUT_6), .clk(demultiplexer_1_out2));  // open: en, clr
  Register #(.width(2)) register_4 (.D(DATA_IN), .Q(DATA_OUT_7), .clk(demultiplexer_1_out3));  // open: en, clr
  Register #(.width(2)) register_5 (.D(DATA_IN), .Q(DATA_OUT_8), .clk(demultiplexer_1_out4));  // open: en, clr
  Register #(.width(2)) register_6 (.D(DATA_IN), .Q(DATA_OUT_16), .clk(demultiplexer_1_out12));  // open: en, clr
  Register #(.width(2)) register_7 (.D(DATA_IN), .Q(DATA_OUT_17), .clk(demultiplexer_1_out13));  // open: en, clr
  Register #(.width(2)) register_8 (.D(DATA_IN), .Q(DATA_OUT_9), .clk(demultiplexer_1_out5));  // open: en, clr
  Register #(.width(2)) register_9 (.D(DATA_IN), .Q(DATA_OUT_18), .clk(demultiplexer_1_out14));  // open: en, clr
  Register #(.width(2)) register_10 (.D(DATA_IN), .Q(DATA_OUT_10), .clk(demultiplexer_1_out6));  // open: en, clr
  Register #(.width(2)) register_11 (.D(DATA_IN), .Q(DATA_OUT_11), .clk(demultiplexer_1_out7));  // open: en, clr
  Register #(.width(2)) register_12 (.D(DATA_IN), .Q(DATA_OUT_19), .clk(demultiplexer_1_out15));  // open: en, clr
  Register #(.width(2)) register_13 (.D(DATA_IN), .Q(DATA_OUT_12), .clk(demultiplexer_1_out8));  // open: en, clr
  Register #(.width(2)) register_14 (.D(undriven_2), .Q(_18), .clk(undriven_4));  // open: en, clr
  Register #(.width(2)) register_15 (.D(undriven_2), .Q(_17), .clk(undriven_3));  // open: en, clr
  Register #(.width(2)) register_16 (.D(DATA_IN), .Q(DATA_OUT_13), .clk(demultiplexer_1_out9));  // open: en, clr
  Register #(.width(2)) register_17 (.D(undriven_2), .Q(_19), .clk(undriven_5));  // open: en, clr
  Register #(.width(2)) register_18 (.D(DATA_IN), .Q(DATA_OUT_15), .clk(demultiplexer_1_out11));  // open: en, clr
  Register #(.width(2)) register_19 (.D(DATA_IN), .Q(DATA_OUT_14), .clk(demultiplexer_1_out10));  // open: en, clr
  Register #(.width(2)) register_20 (.D(undriven_2), .Q(_20), .clk(undriven_6));  // open: en, clr

  assign DATA_OUT_0 = 2'b01;
  assign DATA_OUT_1 = 2'b01;
  assign DATA_OUT_2 = 2'b01;
  assign DATA_OUT_3 = 2'b01;

  // Other names for the same wires on the sheet: _1[1:0] = DATA_OUT_4; _2[1:0] = DATA_OUT_5; _3[1:0] = DATA_OUT_6;
  //   _4[1:0] = DATA_OUT_7; _5[1:0] = DATA_OUT_8; _6[1:0] = DATA_OUT_9; _7[1:0] = DATA_OUT_10; _8[1:0] = DATA_OUT_11;
  //   _9[1:0] = DATA_OUT_12; _10[1:0] = DATA_OUT_13; _11[1:0] = DATA_OUT_14; _12[1:0] = DATA_OUT_15;
  //   _13[1:0] = DATA_OUT_16; _14[1:0] = DATA_OUT_17; _15[1:0] = DATA_OUT_18; _16[1:0] = DATA_OUT_19;
  //   TP1[1:0] = DATA_IN

  // Notes on the sheet:
  //   11
endmodule
