// Logisim project main.circ as structural Verilog: 1 circuit, main circuit main
module main (
  output [6:0] out_1,
  output [6:0] out_2
);

  wire blc_rand_1_p3, CLK, comparator_1_eq, comparator_2_eq, comparator_3_eq, controlled_buffer_1_out,
       gpu_manager_1_out_5, gpu_manager_1_out_6, gpu_manager_1_out_7, gpu_manager_1_out_8, main_1_finish,
       main_1_ram_clk, main_1_zderzenie, RAM_CLK;
  wire [1:0] blc_rand_1_p5, Data_In, Data_Out, demultiplexer_1_out1, Gpu_Data, main_1_data_out;
  wire [2:0] State_Select;
  wire [6:0] Adress, blc_rand_1_p4, GPU_Adress, gpu_manager_1_out_4, main_1_a, multiplier_1_out;
  wire [7:0] gpu_1_p5, gpu_1_p6, gpu_1_p7, gpu_1_p8, gpu_1_p9, gpu_1_p10, gpu_1_p11, gpu_1_p12, gpu_1_p13,
       gpu_1_p14, gpu_1_p15, gpu_1_p16, gpu_1_p17, gpu_1_p18, gpu_1_p19, gpu_1_p20;

  Demultiplexer #(.select(3), .width(2)) demultiplexer_1 (
    .out1(demultiplexer_1_out1), .out2(Gpu_Data), .in(Data_Out), .sel(State_Select));  // open: out0, out3, out4, out5, out6, out7, en
  Counter #(.width(4), .max('hf)) counter_1 (.Q(out_2[3:0]), .clk(main_1_finish));  // open: load, D, count, carry, clr
  Adder #(.width(7)) adder_1 (.a(7'b0000010), .b(multiplier_1_out), .out(out_1));  // open: cin, cout
  Multiplier #(.width(7)) multiplier_1 (
    .a(7'b0001000), .b({3'b000, out_2[3:0]}), .out(multiplier_1_out));  // open: cin, cout
  Comparator #(.width(3)) comparator_1 (.a(State_Select), .b(3'b000), .eq(comparator_1_eq));  // open: gt, lt
  Comparator #(.width(3)) comparator_2 (.a(State_Select), .b(3'b001), .eq(comparator_2_eq));  // open: gt, lt
  opadanie_main main_1 (
    .A1(out_1), .DATA_IN(demultiplexer_1_out1), .CLK(CLK), .ENABLE(comparator_2_eq),
    .DATA_OUT(main_1_data_out), .A(main_1_a), .RAM_CLK(main_1_ram_clk), .FINISH(main_1_finish),
    .ZDERZENIE(main_1_zderzenie));
  // BLC_RAND blc_rand_1: pin names not known; wires that end beside it: comparator_1_eq, CLK, blc_rand_1_p3, blc_rand_1_p4, blc_rand_1_p5
  Multiplexer #(.select(3), .width(7)) multiplexer_1 (
    .in0(blc_rand_1_p4), .in1(main_1_a), .in2(GPU_Adress), .out(Adress), .sel(State_Select));  // open: in3, in4, in5, in6, in7, en
  Multiplexer #(.select(3), .width(2)) multiplexer_2 (
    .in0(blc_rand_1_p5), .in1(main_1_data_out), .out(Data_In), .sel(State_Select));  // open: in2, in3, in4, in5, in6, in7, en
  Multiplexer #(.select(3)) multiplexer_3 (
    .in0(CLK), .in1(main_1_ram_clk), .in2(1'b0), .out(RAM_CLK), .sel(State_Select));  // open: in3, in4, in5, in6, in7, en
  Clock clock_1 (.out(CLK));
  RAM #(.addrWidth(7), .dataWidth(2), .bus("separate")) ram_1 (
    .addr(Adress), .din(Data_In), .data(Data_Out), .clk(RAM_CLK));  // open: str, sel, ld, clr
  assign controlled_buffer_1_out = comparator_3_eq ? CLK : 1'bz;  // Controlled_Buffer controlled_buffer_1
  Comparator #(.width(3)) comparator_3 (.a(State_Select), .b(3'b010), .eq(comparator_3_eq));  // open: gt, lt
  GPU_manager gpu_manager_1 (
    .in_1(Gpu_Data), .in_2(controlled_buffer_1_out), .out_3(GPU_Adress), .out_4(gpu_manager_1_out_4),
    .out_5(gpu_manager_1_out_5), .out_6(gpu_manager_1_out_6), .out_7(gpu_manager_1_out_7),
    .out_8(gpu_manager_1_out_8));
  Pull_Resistor pull_resistor_1 (.node(controlled_buffer_1_out));
  // GPU gpu_1: pin names not known; wires that end beside it: gpu_manager_1_out_4, gpu_manager_1_out_5, gpu_manager_1_out_6, gpu_manager_1_out_7, gpu_1_p5, gpu_1_p6, gpu_1_p7, gpu_1_p8, gpu_1_p9, gpu_1_p10, gpu_1_p11, gpu_1_p12, gpu_1_p13, gpu_1_p14, gpu_1_p15, gpu_1_p16, gpu_1_p17, gpu_1_p18, gpu_1_p19, gpu_1_p20
  DotMatrix #(.inputtype("row"), .matrixcols(8), .matrixrows(16), .dotshape("circle")) dotmatrix_1 (
    .row0(gpu_1_p5), .row1(gpu_1_p6), .row2(gpu_1_p7), .row3(gpu_1_p8), .row4(gpu_1_p9), .row5(gpu_1_p10),
    .row6(gpu_1_p11), .row7(gpu_1_p12), .row8(gpu_1_p13), .row9(gpu_1_p14), .row10(gpu_1_p15),
    .row11(gpu_1_p16), .row12(gpu_1_p17), .row13(gpu_1_p18), .row14(gpu_1_p19), .row15(gpu_1_p20));

  assign out_2[6:4] = 3'b000;
endmodule
